// Logisim project schematic.circ as structural Verilog
module main (
  input  [3:0] a,
  input  sub_notadd,
  input  [3:0] b,
  output [3:0] s,
  output cout
);

  wire adder_1_cout, subtractor_1_bout;
  wire [3:0] adder_1_out, subtractor_1_out;

  Adder #(.width(4)) adder_1 (.a(a), .b(b), .out(adder_1_out), .cout(adder_1_cout));  // open: cin
  Subtractor #(.width(4)) subtractor_1 (.a(a), .b(b), .out(subtractor_1_out), .bout(subtractor_1_bout));  // open: bin
  Multiplexer #(.width(4)) multiplexer_1 (.in0(adder_1_out), .in1(subtractor_1_out), .out(s), .sel(sub_notadd));
  Multiplexer multiplexer_2 (.in0(adder_1_cout), .in1(subtractor_1_bout), .out(cout), .sel(sub_notadd));
endmodule

module four_bit_adder (
  input  cin,
  input  a0,
  input  a1,
  input  a2,
  input  a3,
  input  b0,
  input  b1,
  input  b2,
  input  b3,
  output s0,
  output s1,
  output s2,
  output s3,
  output cout
);

  wire full_adder_1_cout, full_adder_2_cout, full_adder_3_cout;

  full_adder full_adder_1 (.a(a0), .b(b0), .cin(cin), .s(s0), .cout(full_adder_1_cout));
  full_adder full_adder_2 (.a(a1), .b(b1), .cin(full_adder_1_cout), .s(s1), .cout(full_adder_2_cout));
  full_adder full_adder_3 (.a(a2), .b(b2), .cin(full_adder_2_cout), .s(s2), .cout(full_adder_3_cout));
  full_adder full_adder_4 (.a(a3), .b(b3), .cin(full_adder_3_cout), .s(s3), .cout(cout));
endmodule

module full_adder (
  input  a,
  input  b,
  input  cin,
  output s,
  output cout
);

  wire and_1_out, and_2_out, xor_1_out;

  xor xor_1 (xor_1_out, a, b);
  xor xor_2 (s, xor_1_out, cin);
  and and_1 (and_1_out, xor_1_out, cin);
  and and_2 (and_2_out, a, b);
  or or_1 (cout, and_1_out, and_2_out);
endmodule
