// Logisim project schematic.circ as structural Verilog: 1 circuit, main circuit main
module main (
  input  [31:0] in1,
  input  clk,
  input  load,
  output [31:0] out1
);

  wire [31:0] and_1_out, negator_1_out, negator_2_out, register_1_q, register_2_q;

  Negator #(.width(32)) negator_1 (.in(in1), .out(negator_1_out));
  Register #(.width(32)) register_1 (.D(negator_1_out), .clk(clk), .Q(register_1_q));  // open: en, clr
  Register #(.width(32)) register_2 (.D(and_1_out), .clk(clk), .Q(register_2_q));  // open: en, clr
  assign and_1_out = register_1_q & in1;  // AND_Gate and_1, 32 bits wide
  Negator #(.width(32)) negator_2 (.in(register_2_q), .out(negator_2_out));
  Adder #(.width(32)) adder_1 (.a(negator_2_out), .b(in1), .out(out1));  // open: cin, cout
endmodule
