// Logisim project schematic.circ as structural Verilog: 1 circuit, main circuit main
module main (
  input  [31:0] in1,
  input  load,
  input  clk,
  output [31:0] out1
);

  wire [1:0] adder_1_out, register_1_q;
  wire [31:0] adder_2_out, and_1_out, multiplexer_1_out, negator_1_out, negator_2_out, R1_q;

  Register #(.width(2)) register_1 (.D(adder_1_out), .clk(clk), .Q(register_1_q), .clr(load));  // open: en
  Register #(.width(32)) R1 (.D(in1), .en(load), .clk(clk), .Q(R1_q));  // open: clr
  Adder #(.width(2)) adder_1 (.a(register_1_q), .b(2'b01), .out(adder_1_out));  // open: cin, cout
  Negator #(.width(32)) negator_1 (.in(R1_q), .out(negator_1_out));
  assign and_1_out = R1_q & out1;  // AND_Gate and_1, 32 bits wide
  Negator #(.width(32)) negator_2 (.in(out1), .out(negator_2_out));
  Adder #(.width(32)) adder_2 (.a(R1_q), .b(out1), .out(adder_2_out));  // open: cin, cout
  Multiplexer #(.select(2), .width(32)) multiplexer_1 (
    .in0(negator_1_out), .in1(and_1_out), .in2(negator_2_out), .in3(adder_2_out), .out(multiplexer_1_out),
    .sel(register_1_q));
  Register #(.width(32)) R2 (.D(multiplexer_1_out), .clk(clk), .Q(out1), .clr(load));  // open: en
endmodule
