// Logisim project schematic.circ as structural Verilog: 1 circuit, main circuit main
module main (
  input  [31:0] divisor,
  input  [31:0] dividend,
  input  start,
  input  clk,
  output [31:0] remainder,
  output [31:0] quotient,
  output done
);

  wire and_1_out, comparator_1_eq, comparator_2_lt, comparator_3_eq, not_1_out, not_2_out, or_1_out, or_2_out;
  wire [7:0] counter_1_q;
  wire [31:0] adder_1_out, multiplexer_1_out, multiplexer_2_out, multiplexer_3_out, multiplexer_4_out,
       multiplexer_5_out, multiplexer_6_out, subtractor_1_out;

  Comparator comparator_1 (.a({8{1'b0}}), .b(counter_1_q), .eq(comparator_1_eq));  // open: gt, lt
  Subtractor #(.width(32)) subtractor_1 (.a(remainder), .b(divisor), .out(subtractor_1_out));  // open: bin, bout
  Comparator #(.width(32)) comparator_2 (.a(remainder), .b(divisor), .lt(comparator_2_lt));  // open: gt, eq
  Adder #(.width(32)) adder_1 (.a(quotient), .b(32'h1), .out(adder_1_out));  // open: cin, cout
  Counter counter_1 (
    .clr(start), .load(comparator_1_eq), .up(1'b0), .clk(clk), .D(8'h40), .Q(counter_1_q));  // open: count, carry
  Multiplexer #(.width(32)) multiplexer_1 (
    .in0(remainder), .in1(subtractor_1_out), .out(multiplexer_1_out), .sel(not_1_out));
  not not_1 (not_1_out, comparator_2_lt);
  Multiplexer #(.width(32)) multiplexer_2 (.in0(quotient), .in1(adder_1_out), .out(multiplexer_2_out), .sel(not_1_out));
  Multiplexer #(.width(32)) multiplexer_3 (
    .in0(multiplexer_2_out), .in1(dividend), .out(multiplexer_3_out), .sel(comparator_1_eq));
  or or_1 (or_1_out, comparator_1_eq, counter_1_q[0]);
  Multiplexer #(.width(32)) multiplexer_4 (
    .in0(multiplexer_1_out), .in1({32{1'b0}}), .out(multiplexer_4_out), .sel(comparator_1_eq));
  Register #(.width(32)) a (.D(multiplexer_5_out), .clk(and_1_out), .Q(remainder));  // open: en, clr
  Multiplexer #(.width(32)) multiplexer_5 (
    .in0({remainder[30:0], quotient[31]}), .in1(multiplexer_4_out), .out(multiplexer_5_out), .sel(or_1_out));
  Register #(.width(32)) q (.D(multiplexer_6_out), .clk(and_1_out), .Q(quotient));  // open: en, clr
  Multiplexer #(.width(32)) multiplexer_6 (
    .in0({quotient[30:0], 1'b0}), .in1(multiplexer_3_out), .out(multiplexer_6_out), .sel(or_1_out));
  and and_1 (and_1_out, clk, not_2_out);
  not not_2 (not_2_out, done);
  Comparator comparator_3 (.a(counter_1_q), .b(8'h1), .eq(comparator_3_eq));  // open: gt, lt
  Register #(.width(1)) register_1 (.D(or_2_out), .clk(clk), .Q(done), .clr(start));  // open: en
  or or_2 (or_2_out, done, comparator_3_eq);
endmodule
