// Logisim project T_Q3.circ as structural Verilog: 1 circuit, main circuit main
module main (
);

  wire A, and_1_out, and_2_out, and_3_out, and_4_out, B, C, CLK_out, comparator_1_eq, comparator_2_eq,
       comparator_3_eq, comparator_4_eq, or_1_out, or_2_out, or_3_out, or_4_out;
  wire [7:0] adder_1_out, adder_2_out, multiplexer_1_out, R0, R1, R2, subtractor_1_out, xor_1_out;

  Comparator comparator_1 (.a(R1), .b({8{1'b0}}), .eq(comparator_1_eq));  // open: gt, lt
  Comparator comparator_2 (.a(R2), .b({8{1'b0}}), .eq(comparator_2_eq));  // open: gt, lt
  Comparator comparator_3 (.a(R0), .b(8'h8), .eq(comparator_3_eq));  // open: gt, lt
  Comparator comparator_4 (.a(R0), .b(R2), .eq(comparator_4_eq));  // open: gt, lt
  or or_1 (or_1_out, comparator_1_eq, comparator_2_eq);
  and and_1 (and_1_out, comparator_3_eq, A);
  and and_2 (and_2_out, comparator_4_eq, B);
  and and_3 (and_3_out, or_1_out, C);
  and and_4 (and_4_out, or_2_out, CLK_out);
  or or_2 (or_2_out, and_1_out, and_2_out, and_3_out);
  Clock CLK (.out(CLK_out));
  D_Flip_Flop u_A (.D(and_3_out), .clk(and_4_out), .Q(A));  // open: Qn, preset, reset
  D_Flip_Flop u_B (.D(and_1_out), .clk(and_4_out), .Q(B));  // open: Qn, preset, reset
  D_Flip_Flop u_C (.D(and_2_out), .clk(and_4_out), .Q(C));  // open: Qn, preset, reset
  or or_3 (or_3_out, B, C);
  or or_4 (or_4_out, A, B);
  assign xor_1_out = R0 ^ R2;  // XOR_Gate xor_1, 8 bits wide
  Adder adder_1 (.a(subtractor_1_out), .b(R2), .out(adder_1_out));  // open: cin, cout
  Register u_R0 (.D(adder_2_out), .en(or_4_out), .clk(CLK_out), .Q(R0));  // open: clr
  Adder adder_2 (.a(R0), .b(8'h1), .out(adder_2_out));  // open: cin, cout
  Subtractor subtractor_1 (.a(R1), .b(8'h1), .out(subtractor_1_out));  // open: bin, bout
  Register u_R1 (.D(subtractor_1_out), .en(C), .clk(CLK_out), .Q(R1));  // open: clr
  Multiplexer #(.width(8)) multiplexer_1 (.in0(xor_1_out), .in1(adder_1_out), .out(multiplexer_1_out), .sel(C));
  Register u_R2 (.D(multiplexer_1_out), .en(or_3_out), .clk(CLK_out), .Q(R2));  // open: clr
endmodule
