// Logisim project T_Q6.circ as structural Verilog: 1 circuit, main circuit main
module main (
);

  wire and_1_out, and_2_out, and_3_out, and_4_out, clock_1_out, comparator_1_lt, E_q, F0_q, F1_q, F2_q, F3_q,
       not_1_out, or_1_out, or_2_out, or_3_out, or_4_out, or_5_out, S_q;
  wire [7:0] adder_1_out, adder_2_out, adder_3_out, adder_4_out, multiplexer_1_out, multiplexer_2_out,
       multiplexer_3_out, multiplexer_4_out, not_2_out, R0_q, R1_q, R2_q, R3_q;

  and and_1 (and_1_out, F3_q, comparator_1_lt);
  and and_2 (and_2_out, F3_q, not_1_out);
  Clock clock_1 (.out(clock_1_out));
  D_Flip_Flop E (.D(or_1_out), .clk(clock_1_out), .Q(E_q), .reset(S_q));  // open: Qn, preset
  or or_1 (or_1_out, E_q, and_1_out);
  D_Flip_Flop S (.D(1'b0), .clk(clock_1_out), .Q(S_q));  // open: Qn, preset, reset
  D_Flip_Flop F0 (.D(S_q), .clk(clock_1_out), .Q(F0_q));  // open: Qn, preset, reset
  D_Flip_Flop F1 (.D(F0_q), .clk(clock_1_out), .Q(F1_q), .reset(S_q));  // open: Qn, preset
  D_Flip_Flop F2 (.D(or_2_out), .clk(clock_1_out), .Q(F2_q), .reset(S_q));  // open: Qn, preset
  or or_2 (or_2_out, F1_q, and_2_out);
  D_Flip_Flop F3 (.D(F2_q), .clk(clock_1_out), .Q(F3_q), .reset(S_q));  // open: Qn, preset
  not not_1 (not_1_out, comparator_1_lt);
  Comparator comparator_1 (.a(R2_q), .b({8{1'b0}}), .lt(comparator_1_lt));  // open: gt, eq
  Adder adder_1 (.a(R1_q), .b(8'h1), .out(adder_1_out));  // open: cin, cout
  assign not_2_out = ~R1_q;  // NOT_Gate not_2, 8 bits wide
  and and_3 (and_3_out, comparator_1_lt, F3_q);
  and and_4 (and_4_out, not_1_out, F3_q);
  Multiplexer #(.width(8)) multiplexer_1 (.in0(adder_1_out), .in1(not_2_out), .out(multiplexer_1_out), .sel(F0_q));
  Multiplexer #(.width(8)) multiplexer_2 (.in0(multiplexer_1_out), .in1(R0_q), .out(multiplexer_2_out), .sel(S_q));
  or or_3 (or_3_out, S_q, F0_q, F1_q);
  Adder adder_2 (.a(R0_q), .b(R2_q), .out(adder_2_out));  // open: cin, cout
  Multiplexer #(.width(8)) multiplexer_3 (.in0(adder_2_out), .in1(adder_3_out), .out(multiplexer_3_out), .sel(F2_q));
  Adder adder_3 (.a(R2_q), .b(R1_q), .out(adder_3_out));  // open: cin, cout
  or or_4 (or_4_out, and_3_out, F2_q);
  Adder adder_4 (.a(R3_q), .b(8'h1), .out(adder_4_out));  // open: cin, cout
  Multiplexer #(.width(8)) multiplexer_4 (.in0(adder_4_out), .in1({8{1'b0}}), .out(multiplexer_4_out), .sel(S_q));
  or or_5 (or_5_out, S_q, and_4_out);
  Register R0 (.en(1'b0), .clk(clock_1_out), .Q(R0_q));  // open: D, clr
  Register R1 (.D(multiplexer_2_out), .en(or_3_out), .clk(clock_1_out), .Q(R1_q));  // open: clr
  Register R2 (.D(multiplexer_3_out), .en(or_4_out), .clk(clock_1_out), .Q(R2_q));  // open: clr
  Register R3 (.D(multiplexer_4_out), .en(or_5_out), .clk(clock_1_out), .Q(R3_q));  // open: clr
endmodule
