// Logisim project T_Q7.circ as structural Verilog: 1 circuit, main circuit main
// A
module main (
  input  t,
  input  s,
  input  r,
  input  q,
  input  p
);

  wire A_q, adder_1_out, and_1_out, and_2_out, and_3_out, and_4_out, and_5_out, and_6_out, clock_1_out,
       controlled_buffer_1_out, M_q, or_1_out, RR_q, X_q, xor_1_out, Y_q;

  Adder #(.width(1)) adder_1 (.a(A_q), .b(Y_q), .out(adder_1_out));  // open: cin, cout
  Clock clock_1 (.out(clock_1_out));
  assign controlled_buffer_1_out = t ? adder_1_out : 1'bz;  // Controlled_Buffer controlled_buffer_1
  or or_1 (or_1_out, p, t);
  xor xor_1 (xor_1_out, RR_q, Y_q);
  assign controlled_buffer_1_out = s ? xor_1_out : 1'bz;  // Controlled_Buffer controlled_buffer_2
  D_Flip_Flop A (.D(controlled_buffer_1_out), .clk(and_1_out), .Q(A_q));  // open: Qn, preset, reset
  and and_1 (and_1_out, clock_1_out, s);
  D_Flip_Flop B (.D(controlled_buffer_1_out), .clk(and_2_out));  // open: Q, Qn, preset, reset
  and and_2 (and_2_out, clock_1_out, or_1_out);
  D_Flip_Flop X (.D(controlled_buffer_1_out), .clk(and_3_out), .Q(X_q));  // open: Qn, preset, reset
  and and_3 (and_3_out, clock_1_out, p);
  D_Flip_Flop M (.D(controlled_buffer_1_out), .clk(and_4_out), .Q(M_q));  // open: Qn, preset, reset
  and and_4 (and_4_out, clock_1_out, q);
  D_Flip_Flop RR (.D(controlled_buffer_1_out), .clk(and_5_out), .Q(RR_q));  // open: Qn, preset, reset
  and and_5 (and_5_out, clock_1_out, r);
  D_Flip_Flop Y (.D(controlled_buffer_1_out), .clk(and_6_out), .Q(Y_q));  // open: Qn, preset, reset
  and and_6 (and_6_out, clock_1_out, r);
  assign controlled_buffer_1_out = p ? A_q : 1'bz;  // Controlled_Buffer controlled_buffer_3
  assign controlled_buffer_1_out = q ? X_q : 1'bz;  // Controlled_Buffer controlled_buffer_4
  assign controlled_buffer_1_out = r ? M_q : 1'bz;  // Controlled_Buffer controlled_buffer_5

  // Notes on the sheet:
  //   BUS
endmodule
