// Logisim project schematic3.circ as structural Verilog: 15 circuits, main circuit main
module main (
  input  [3:0] aluop,
  input  [31:0] b,
  input  [31:0] a,
  input  clk,
  input  rst,
  input  output_inverted,
  input  output_inc,
  output [31:0] res_high,
  output [31:0] res_low,
  output done
);

  wire comparator_1_eq;
  wire [31:0] addd_1_res_high, addd_1_res_low, andd_1_res_high, andd_1_res_low, cloo_1_res_high,
       cloo_1_res_low, cloo_2_res_high, cloo_2_res_low, divv_1_quotient, divv_1_remainder, mull_1_res_high,
       mull_1_res_low, multiplexer_1_out, multiplexer_2_out, not_1_out, orr_1_res_high, orr_1_res_low,
       rotrr_1_res_high, rotrr_1_res_low, slll_1_res_high, slll_1_res_low, sraa_1_res_high, sraa_1_res_low,
       srll_1_res_high, srll_1_res_low, xorr_1_res_high, xorr_1_res_low;
  wire [63:0] adder_1_out, multiplexer_3_out, not_2_out, register_1_q;

  assign not_1_out = ~a;  // NOT_Gate not_1, 32 bits wide
  Comparator #(.mode("unsigned"), .width(4)) comparator_1 (
    .a(aluop), .b(4'b0001), .eq(comparator_1_eq));  // open: gt, lt
  ADDD addd_1 (.S(comparator_1_eq), .b(b), .a(a), .res_low(addd_1_res_low), .res_high(addd_1_res_high));  // open: out_5
  DIVV divv_1 (
    .divisor(b), .dividend(a), .clk(clk), .remainder(divv_1_remainder), .quotient(divv_1_quotient));  // open: done
  ANDD andd_1 (.a(a), .b(b), .res_high(andd_1_res_high), .res_low(andd_1_res_low));
  ORR orr_1 (.a(a), .b(b), .res_high(orr_1_res_high), .res_low(orr_1_res_low));
  XORR xorr_1 (.a(a), .b(b), .res_high(xorr_1_res_high), .res_low(xorr_1_res_low));
  CLOO cloo_1 (.a(a), .res_high(cloo_1_res_high), .res_low(cloo_1_res_low));
  CLOO cloo_2 (.a(not_1_out), .res_high(cloo_2_res_high), .res_low(cloo_2_res_low));
  SLLL slll_1 (.a(a), .b(b), .res_low(slll_1_res_low), .res_high(slll_1_res_high));
  SRLL srll_1 (.a(a), .b(b), .res_high(srll_1_res_high), .res_low(srll_1_res_low));
  SRAA sraa_1 (.a(a), .b(b), .res_high(sraa_1_res_high), .res_low(sraa_1_res_low));
  ROTRR rotrr_1 (.a(a), .b(b), .res_high(rotrr_1_res_high), .res_low(rotrr_1_res_low));
  MULL mull_1 (.b(b), .clk(clk), .a(a), .res_low(mull_1_res_low), .res_high(mull_1_res_high));  // open: Done
  Multiplexer #(.select(4), .width(32)) multiplexer_1 (
    .in0(addd_1_res_high), .in1(addd_1_res_high), .in2(mull_1_res_high), .in3(divv_1_remainder),
    .in4(andd_1_res_high), .in5(orr_1_res_high), .in6(xorr_1_res_high), .in7(cloo_1_res_high),
    .in8(cloo_2_res_high), .in9(slll_1_res_high), .in10(srll_1_res_high), .in11(sraa_1_res_high),
    .in12(rotrr_1_res_high), .out(multiplexer_1_out), .sel(aluop));  // open: in13, in14, in15
  Multiplexer #(.select(4), .width(32)) multiplexer_2 (
    .in0(addd_1_res_low), .in1(addd_1_res_low), .in2(mull_1_res_low), .in3(divv_1_quotient),
    .in4(andd_1_res_low), .in5(orr_1_res_low), .in6(xorr_1_res_low), .in7(cloo_1_res_low),
    .in8(cloo_2_res_low), .in9(slll_1_res_low), .in10(srll_1_res_low), .in11(sraa_1_res_low),
    .in12(rotrr_1_res_low), .out(multiplexer_2_out), .sel(aluop));  // open: in13, in14, in15
  Register #(.width(64)) register_1 (
    .D({multiplexer_1_out, multiplexer_2_out}), .clk(clk), .Q(register_1_q), .clr(rst));  // open: en
  assign not_2_out = ~register_1_q;  // NOT_Gate not_2, 64 bits wide
  Multiplexer #(.width(64)) multiplexer_3 (
    .in0(register_1_q), .in1(not_2_out), .out(multiplexer_3_out), .sel(output_inverted));
  Adder #(.width(64)) adder_1 (.a(multiplexer_3_out), .b(64'h1), .out(adder_1_out));  // open: cin, cout
  Multiplexer #(.width(64)) multiplexer_4 (
    .in0(multiplexer_3_out), .in1(adder_1_out), .out({res_high, res_low}), .sel(output_inc));

  assign done = 1'b1;
endmodule

module ALUU (
  input  clk,
  input  rst,
  input  [31:0] a,
  input  [31:0] b,
  input  output_inc,
  input  output_inverted,
  input  [3:0] aluop
);

  wire [63:0] multiplexer_1_out, multiplexer_2_out, not_1_out;

  Multiplexer #(.select(4), .width(64)) multiplexer_1 (
    .out(multiplexer_1_out), .sel(aluop));  // open: in0, in1, in2, in3, in4, in5, in6, in7, in8, in9, in10, in11, in12, in13, in14, in15
  assign not_1_out = ~multiplexer_1_out;  // NOT_Gate not_1, 64 bits wide
  Multiplexer #(.width(64)) multiplexer_2 (
    .in0(multiplexer_1_out), .in1(not_1_out), .out(multiplexer_2_out), .sel(output_inverted));
  Adder #(.width(64)) adder_1 (.a({64{1'b0}}), .b(multiplexer_2_out), .cin(output_inc));  // open: out, cout
endmodule

module ADDD (
  input  S,
  input  [31:0] b,
  input  [31:0] a,
  output [31:0] res_low,
  output [63:0] out_5,
  output [31:0] res_high
);

  wire adder_1_cout, adder_2_cout, adder_3_cout, adder_4_cout, adder_5_cout, adder_6_cout, adder_7_cout,
       adder_8_cout, adder_9_cout, adder_10_cout, adder_11_cout, adder_12_cout, adder_13_cout, adder_14_cout,
       adder_15_cout, comparator_1_gt, multiplexer_3_out, multiplexer_5_out, multiplexer_7_out,
       multiplexer_9_out, multiplexer_11_out, multiplexer_13_out, multiplexer_15_out;
  wire [3:0] adder_2_out, adder_3_out, adder_4_out, adder_5_out, adder_6_out, adder_7_out, adder_8_out,
       adder_9_out, adder_10_out, adder_11_out, adder_12_out, adder_13_out, adder_14_out, adder_15_out;
  wire [31:0] multiplexer_1_out, multiplexer_16_out, multiplexer_17_out, not_1_out;

  assign not_1_out = ~b;  // NOT_Gate not_1, 32 bits wide
  Multiplexer #(.width(32)) multiplexer_1 (.in0(b), .in1(not_1_out), .out(multiplexer_1_out), .sel(S));
  Comparator #(.mode("unsigned"), .width(32)) comparator_1 (.a(a), .b(b), .gt(comparator_1_gt));  // open: eq, lt
  Adder #(.width(4)) adder_1 (.a(a[3:0]), .b(multiplexer_1_out[3:0]), .out(out_5[3:0]), .cin(S), .cout(adder_1_cout));
  Adder #(.width(4)) adder_2 (
    .a(a[7:4]), .b(multiplexer_1_out[7:4]), .out(adder_2_out), .cout(adder_2_cout));  // open: cin
  Adder #(.width(4)) adder_3 (
    .a(a[7:4]), .b(multiplexer_1_out[7:4]), .out(adder_3_out), .cin(1'b1), .cout(adder_3_cout));
  Adder #(.width(4)) adder_4 (
    .a(a[11:8]), .b(multiplexer_1_out[11:8]), .out(adder_4_out), .cout(adder_4_cout));  // open: cin
  Adder #(.width(4)) adder_5 (
    .a(a[11:8]), .b(multiplexer_1_out[11:8]), .out(adder_5_out), .cin(1'b1), .cout(adder_5_cout));
  Adder #(.width(4)) adder_6 (
    .a(a[15:12]), .b(multiplexer_1_out[15:12]), .out(adder_6_out), .cout(adder_6_cout));  // open: cin
  Adder #(.width(4)) adder_7 (
    .a(a[15:12]), .b(multiplexer_1_out[15:12]), .out(adder_7_out), .cin(1'b1), .cout(adder_7_cout));
  Adder #(.width(4)) adder_8 (
    .a(a[19:16]), .b(multiplexer_1_out[19:16]), .out(adder_8_out), .cout(adder_8_cout));  // open: cin
  Adder #(.width(4)) adder_9 (
    .a(a[19:16]), .b(multiplexer_1_out[19:16]), .out(adder_9_out), .cin(1'b1), .cout(adder_9_cout));
  Adder #(.width(4)) adder_10 (
    .a(a[23:20]), .b(multiplexer_1_out[23:20]), .out(adder_10_out), .cout(adder_10_cout));  // open: cin
  Adder #(.width(4)) adder_11 (
    .a(a[23:20]), .b(multiplexer_1_out[23:20]), .out(adder_11_out), .cin(1'b1), .cout(adder_11_cout));
  Adder #(.width(4)) adder_12 (
    .a(a[27:24]), .b(multiplexer_1_out[27:24]), .out(adder_12_out), .cout(adder_12_cout));  // open: cin
  Adder #(.width(4)) adder_13 (
    .a(a[27:24]), .b(multiplexer_1_out[27:24]), .out(adder_13_out), .cin(1'b1), .cout(adder_13_cout));
  Adder #(.width(4)) adder_14 (
    .a(a[31:28]), .b(multiplexer_1_out[31:28]), .out(adder_14_out), .cout(adder_14_cout));  // open: cin
  Adder #(.width(4)) adder_15 (
    .a(a[31:28]), .b(multiplexer_1_out[31:28]), .out(adder_15_out), .cin(1'b1), .cout(adder_15_cout));
  Multiplexer #(.width(4)) multiplexer_2 (.in0(adder_2_out), .in1(adder_3_out), .out(out_5[7:4]), .sel(adder_1_cout));
  Multiplexer multiplexer_3 (.in0(adder_2_cout), .in1(adder_3_cout), .out(multiplexer_3_out), .sel(adder_1_cout));
  Multiplexer #(.width(4)) multiplexer_4 (
    .in0(adder_4_out), .in1(adder_5_out), .out(out_5[11:8]), .sel(multiplexer_3_out));
  Multiplexer multiplexer_5 (.in0(adder_4_cout), .in1(adder_5_cout), .out(multiplexer_5_out), .sel(multiplexer_3_out));
  Multiplexer #(.width(4)) multiplexer_6 (
    .in0(adder_6_out), .in1(adder_7_out), .out(out_5[15:12]), .sel(multiplexer_5_out));
  Multiplexer multiplexer_7 (.in0(adder_6_cout), .in1(adder_7_cout), .out(multiplexer_7_out), .sel(multiplexer_5_out));
  Multiplexer #(.width(4)) multiplexer_8 (
    .in0(adder_8_out), .in1(adder_9_out), .out(out_5[19:16]), .sel(multiplexer_7_out));
  Multiplexer multiplexer_9 (.in0(adder_8_cout), .in1(adder_9_cout), .out(multiplexer_9_out), .sel(multiplexer_7_out));
  Multiplexer #(.width(4)) multiplexer_10 (
    .in0(adder_10_out), .in1(adder_11_out), .out(out_5[23:20]), .sel(multiplexer_9_out));
  Multiplexer multiplexer_11 (
    .in0(adder_10_cout), .in1(adder_11_cout), .out(multiplexer_11_out), .sel(multiplexer_9_out));
  Multiplexer #(.width(4)) multiplexer_12 (
    .in0(adder_12_out), .in1(adder_13_out), .out(out_5[27:24]), .sel(multiplexer_11_out));
  Multiplexer multiplexer_13 (
    .in0(adder_12_cout), .in1(adder_13_cout), .out(multiplexer_13_out), .sel(multiplexer_11_out));
  Multiplexer #(.width(4)) multiplexer_14 (
    .in0(adder_14_out), .in1(adder_15_out), .out(out_5[31:28]), .sel(multiplexer_13_out));
  Multiplexer multiplexer_15 (
    .in0(adder_14_cout), .in1(adder_15_cout), .out(multiplexer_15_out), .sel(multiplexer_13_out));
  Multiplexer #(.width(32)) multiplexer_16 (
    .in0({32{1'b0}}), .in1(32'h1), .out(multiplexer_16_out), .sel(multiplexer_15_out));
  Multiplexer #(.width(32)) multiplexer_17 (
    .in0({32{1'b1}}), .in1({32{1'b0}}), .out(multiplexer_17_out), .sel(comparator_1_gt));
  Multiplexer #(.width(32)) multiplexer_18 (
    .in0(multiplexer_16_out), .in1(multiplexer_17_out), .out(out_5[63:32]), .sel(S));

  assign res_high = out_5[63:32];
  assign res_low = out_5[31:0];
endmodule

module MULL (
  input  [31:0] b,
  input  clk,
  input  [31:0] a,
  output [31:0] res_low,
  output [31:0] res_high,
  output Done
);

  wire comparator_1_eq, comparator_2_eq, comparator_3_lt, d_ff_1_qn, nand_1_out, not_1_out, or_1_out;
  wire [7:0] counter_1_q;
  wire [31:0] bb_q, multiplexer_1_out, register_1_q, register_2_q, srll_1_res_low;
  wire [63:0] aa1_q, aa_q, adder_1_out, bit_extender_1_out, faa_1_cout, faa_1_s, multiplexer_2_out,
       multiplexer_3_out, multiplexer_4_out, shifter_1_out, shifter_2_out, shifter_3_out;

  Register #(.width(32)) register_1 (.D(b), .clk(clk), .Q(register_1_q));  // open: en, clr
  Register #(.width(32)) register_2 (.D(a), .clk(clk), .Q(register_2_q));  // open: en, clr
  Comparator #(.width(32)) comparator_1 (.a(register_1_q), .b(b), .eq(comparator_1_eq));  // open: gt, lt
  Comparator #(.width(32)) comparator_2 (.a(register_2_q), .b(a), .eq(comparator_2_eq));  // open: gt, lt
  Multiplexer #(.width(32)) multiplexer_1 (.in0(srll_1_res_low), .in1(b), .out(multiplexer_1_out), .sel(nand_1_out));
  nand nand_1 (nand_1_out, comparator_1_eq, comparator_2_eq);
  Counter counter_1 (.load(nand_1_out), .clk(clk), .D(8'h10), .Q(counter_1_q));  // open: clr, up, count, carry
  Register #(.width(32)) bb (.D(multiplexer_1_out), .en(d_ff_1_qn), .clk(clk), .Q(bb_q));  // open: clr
  SRLL srll_1 (.a(bb_q), .b(32'h2), .res_low(srll_1_res_low));  // open: res_high
  Comparator comparator_3 (.a(8'h1), .b(counter_1_q), .lt(comparator_3_lt));  // open: gt, eq
  Multiplexer #(.width(64)) multiplexer_2 (
    .in0(shifter_2_out), .in1(bit_extender_1_out), .out(multiplexer_2_out), .sel(nand_1_out));
  assign bit_extender_1_out = {{32{1'b0}}, a};  // Bit_Extender bit_extender_1
  not not_1 (not_1_out, comparator_3_lt);
  Register #(.width(64)) aa (.D(multiplexer_2_out), .en(d_ff_1_qn), .clk(clk), .Q(aa_q));  // open: clr
  Shifter #(.width(64)) shifter_1 (.in(multiplexer_2_out), .\dist (6'b000001), .out(shifter_1_out));
  D_Flip_Flop d_ff_1 (.D(or_1_out), .clk(clk), .Q(Done), .Qn(d_ff_1_qn), .reset(nand_1_out));  // open: preset
  or or_1 (or_1_out, Done, not_1_out);
  Register #(.width(64)) aa1 (.D(shifter_1_out), .en(d_ff_1_qn), .clk(clk), .Q(aa1_q));  // open: clr
  Shifter #(.width(64)) shifter_2 (.in(aa1_q), .\dist (6'b000001), .out(shifter_2_out));
  Register #(.width(64)) P (.D(adder_1_out), .en(d_ff_1_qn), .clk(clk), .Q({res_high, res_low}), .clr(nand_1_out));
  Multiplexer #(.width(64)) multiplexer_3 (.in0({64{1'b0}}), .in1(aa_q), .out(multiplexer_3_out), .sel(bb_q[0]));
  Multiplexer #(.width(64)) multiplexer_4 (.in0({64{1'b0}}), .in1(aa1_q), .out(multiplexer_4_out), .sel(bb_q[1]));
  FAA faa_1 (.a(multiplexer_3_out), .b(multiplexer_4_out), .c({res_high, res_low}), .s(faa_1_s), .cout(faa_1_cout));
  Shifter #(.width(64)) shifter_3 (.in(faa_1_cout), .\dist (6'b000001), .out(shifter_3_out));
  Adder #(.width(64)) adder_1 (.a(faa_1_s), .b(shifter_3_out), .out(adder_1_out));  // open: cin, cout
endmodule

module CLOO (
  input  [31:0] a,
  output [31:0] res_high,
  output [31:0] res_low
);

  wire comparator_1_eq, comparator_2_eq, comparator_3_eq, comparator_4_eq, comparator_5_eq, multiplexer_9_out;
  wire [1:0] multiplexer_7_out;
  wire [3:0] multiplexer_5_out;
  wire [5:0] adder_1_out, adder_2_out, adder_3_out, adder_4_out, adder_5_out, adder_6_out, multiplexer_2_out,
       multiplexer_4_out, multiplexer_6_out, multiplexer_8_out, multiplexer_10_out;
  wire [7:0] multiplexer_3_out;
  wire [15:0] multiplexer_1_out;

  Adder #(.width(6)) adder_1 (.a({6{1'b0}}), .b(6'b000001), .out(adder_1_out));  // open: cin, cout
  Multiplexer #(.width(16)) multiplexer_1 (
    .in0(a[31:16]), .in1(a[15:0]), .out(multiplexer_1_out), .sel(comparator_1_eq));
  Comparator #(.mode("unsigned"), .width(16)) comparator_1 (
    .a(a[31:16]), .b({16{1'b1}}), .eq(comparator_1_eq));  // open: gt, lt
  Multiplexer #(.width(6)) multiplexer_2 (
    .in0({6{1'b0}}), .in1(adder_1_out), .out(multiplexer_2_out), .sel(comparator_1_eq));
  Comparator #(.mode("unsigned")) comparator_2 (
    .a(multiplexer_1_out[15:8]), .b({8{1'b1}}), .eq(comparator_2_eq));  // open: gt, lt
  Adder #(.width(6)) adder_2 (.a(multiplexer_2_out), .b(6'b001000), .out(adder_2_out));  // open: cin, cout
  Multiplexer #(.width(8)) multiplexer_3 (
    .in0(multiplexer_1_out[15:8]), .in1(multiplexer_1_out[7:0]), .out(multiplexer_3_out),
    .sel(comparator_2_eq));
  Multiplexer #(.width(6)) multiplexer_4 (
    .in0(multiplexer_2_out), .in1(adder_2_out), .out(multiplexer_4_out), .sel(comparator_2_eq));
  Comparator #(.mode("unsigned"), .width(4)) comparator_3 (
    .a(multiplexer_3_out[7:4]), .b(4'b1111), .eq(comparator_3_eq));  // open: gt, lt
  Adder #(.width(6)) adder_3 (.a(multiplexer_4_out), .b(6'b000100), .out(adder_3_out));  // open: cin, cout
  Multiplexer #(.width(4)) multiplexer_5 (
    .in0(multiplexer_3_out[7:4]), .in1(multiplexer_3_out[3:0]), .out(multiplexer_5_out), .sel(comparator_3_eq));
  Multiplexer #(.width(6)) multiplexer_6 (
    .in0(multiplexer_4_out), .in1(adder_3_out), .out(multiplexer_6_out), .sel(comparator_3_eq));
  Comparator #(.mode("unsigned"), .width(2)) comparator_4 (
    .a(multiplexer_5_out[3:2]), .b(2'b11), .eq(comparator_4_eq));  // open: gt, lt
  Adder #(.width(6)) adder_4 (.a(multiplexer_6_out), .b(6'b000010), .out(adder_4_out));  // open: cin, cout
  Multiplexer #(.width(2)) multiplexer_7 (
    .in0(multiplexer_5_out[3:2]), .in1(multiplexer_5_out[1:0]), .out(multiplexer_7_out), .sel(comparator_4_eq));
  Multiplexer #(.width(6)) multiplexer_8 (
    .in0(multiplexer_6_out), .in1(adder_4_out), .out(multiplexer_8_out), .sel(comparator_4_eq));
  Comparator #(.mode("unsigned"), .width(1)) comparator_5 (
    .a(multiplexer_7_out[1]), .b(1'b1), .eq(comparator_5_eq));  // open: gt, lt
  Adder #(.width(6)) adder_5 (.a(multiplexer_8_out), .b(6'b000001), .out(adder_5_out));  // open: cin, cout
  Multiplexer multiplexer_9 (
    .in0(multiplexer_7_out[1]), .in1(multiplexer_7_out[0]), .out(multiplexer_9_out), .sel(comparator_5_eq));
  Multiplexer #(.width(6)) multiplexer_10 (
    .in0(multiplexer_8_out), .in1(adder_5_out), .out(multiplexer_10_out), .sel(comparator_5_eq));
  Adder #(.width(6)) adder_6 (
    .a({6{1'b0}}), .b(multiplexer_10_out), .out(adder_6_out), .cin(multiplexer_9_out));  // open: cout
  assign res_low = {{26{1'b0}}, adder_6_out};  // Bit_Extender bit_extender_1

  assign res_high = {32{1'b0}};
endmodule

module ROTRR (
  input  [31:0] a,
  input  [31:0] b,
  output [31:0] res_high,
  output [31:0] res_low
);

  wire [63:0] srl64_1_res_low;

  SRL64 srl64_1 (.a({a, {32{1'b0}}}), .b(b), .res_low(srl64_1_res_low));  // open: res_high
  assign res_low = srl64_1_res_low[31:0] | srl64_1_res_low[63:32];  // OR_Gate or_1, 32 bits wide

  assign res_high = {32{1'b0}};
endmodule

module SRLL (
  input  [31:0] a,
  input  [31:0] b,
  output [31:0] res_high,
  output [31:0] res_low
);

  wire or_1_out;
  wire [31:0] multiplexer_1_out, shifter_1_out, shifter_2_out, shifter_3_out, subtractor_1_out;

  Subtractor #(.width(32)) subtractor_1 (.a(b), .b(32'h1), .out(subtractor_1_out));  // open: bin, bout
  Shifter #(.shift("lr"), .width(32)) shifter_1 (.in(a), .\dist (b[4:0]), .out(shifter_1_out));
  Shifter #(.shift("lr"), .width(32)) shifter_2 (.in(a), .\dist (subtractor_1_out[4:0]), .out(shifter_2_out));
  Shifter #(.shift("lr"), .width(32)) shifter_3 (.in(shifter_2_out), .\dist (5'b00001), .out(shifter_3_out));
  Multiplexer #(.width(32)) multiplexer_1 (
    .in0(shifter_3_out), .in1(shifter_1_out), .out(multiplexer_1_out), .sel(b[0]));
  or or_1 (or_1_out, b[0], b[1], b[2], b[3], b[4]);
  Multiplexer #(.width(32)) multiplexer_2 (.in0(a), .in1(multiplexer_1_out), .out(res_low), .sel(or_1_out));

  assign res_high = {32{1'b0}};
endmodule

module SLLL (
  input  [31:0] a,
  input  [31:0] b,
  output [31:0] res_low,
  output [31:0] res_high
);

  wire [31:0] subtractor_1_out;
  wire [63:0] bit_extender_1_out, shifter_1_out, shifter_2_out, shifter_3_out;

  assign bit_extender_1_out = {{32{1'b0}}, a};  // Bit_Extender bit_extender_1
  Subtractor #(.width(32)) subtractor_1 (.a(b), .b(32'h1), .out(subtractor_1_out));  // open: bin, bout
  Shifter #(.width(64)) shifter_1 (.in(bit_extender_1_out), .\dist ({1'b0, b[4:0]}), .out(shifter_1_out));
  Shifter #(.width(64)) shifter_2 (
    .in(bit_extender_1_out), .\dist ({1'b0, subtractor_1_out[4:0]}), .out(shifter_2_out));
  Shifter #(.width(64)) shifter_3 (.in(shifter_2_out), .\dist (6'b000001), .out(shifter_3_out));
  Multiplexer #(.width(64)) multiplexer_1 (
    .in0(shifter_3_out), .in1(shifter_1_out), .out({res_high, res_low}), .sel(b[0]));
endmodule

module FAA (
  input  [63:0] a,
  input  [63:0] b,
  input  [63:0] c,
  output [63:0] s,
  output [63:0] cout
);

  wire [63:0] and_1_out, and_2_out, xor_1_out;

  assign and_1_out = b & a;  // AND_Gate and_1, 64 bits wide
  assign xor_1_out = a ^ b;  // XOR_Gate xor_1, 64 bits wide
  assign and_2_out = xor_1_out & c;  // AND_Gate and_2, 64 bits wide
  assign s = xor_1_out ^ c;  // XOR_Gate xor_2, 64 bits wide
  assign cout = and_1_out | and_2_out;  // OR_Gate or_1, 64 bits wide
endmodule

module ANDD (
  input  [31:0] a,
  input  [31:0] b,
  output [31:0] res_high,
  output [31:0] res_low
);

  assign res_low = a & b;  // AND_Gate and_1, 32 bits wide

  assign res_high = {32{1'b0}};
endmodule

module ORR (
  input  [31:0] a,
  input  [31:0] b,
  output [31:0] res_high,
  output [31:0] res_low
);

  assign res_low = a | b;  // OR_Gate or_1, 32 bits wide

  assign res_high = {32{1'b0}};
endmodule

module XORR (
  input  [31:0] a,
  input  [31:0] b,
  output [31:0] res_high,
  output [31:0] res_low
);

  assign res_low = a ^ b;  // XOR_Gate xor_1, 32 bits wide

  assign res_high = {32{1'b0}};
endmodule

module SRAA (
  input  [31:0] a,
  input  [31:0] b,
  output [31:0] res_high,
  output [31:0] res_low
);

  wire [31:0] and_1_out, bit_extender_1_out, slll_1_res_low, srll_1_res_low, subtractor_1_out;

  assign and_1_out = b & 32'h1f;  // AND_Gate and_1, 32 bits wide
  assign bit_extender_1_out = {{31{a[31]}}, a[31]};  // Bit_Extender bit_extender_1
  Subtractor #(.width(32)) subtractor_1 (.a(32'h20), .b(and_1_out), .out(subtractor_1_out));  // open: bin, bout
  SRLL srll_1 (.a(a), .b(b), .res_low(srll_1_res_low));  // open: res_high
  SLLL slll_1 (.a(bit_extender_1_out), .b(subtractor_1_out), .res_low(slll_1_res_low));  // open: res_high
  assign res_low = srll_1_res_low | slll_1_res_low;  // OR_Gate or_1, 32 bits wide
  assign res_high = {{31{res_low[31]}}, res_low[31]};  // Bit_Extender bit_extender_2
endmodule

module SRL64 (
  input  [63:0] a,
  input  [31:0] b,
  output [31:0] res_high,
  output [63:0] res_low
);

  wire or_1_out;
  wire [31:0] subtractor_1_out;
  wire [63:0] multiplexer_1_out, shifter_1_out, shifter_2_out, shifter_3_out;

  Subtractor #(.width(32)) subtractor_1 (.a(b), .b(32'h1), .out(subtractor_1_out));  // open: bin, bout
  Shifter #(.shift("lr"), .width(64)) shifter_1 (.in(a), .\dist ({1'b0, b[4:0]}), .out(shifter_1_out));
  Shifter #(.shift("lr"), .width(64)) shifter_2 (.in(a), .\dist ({1'b0, subtractor_1_out[4:0]}), .out(shifter_2_out));
  Shifter #(.shift("lr"), .width(64)) shifter_3 (.in(shifter_2_out), .\dist (6'b000001), .out(shifter_3_out));
  Multiplexer #(.width(64)) multiplexer_1 (
    .in0(shifter_3_out), .in1(shifter_1_out), .out(multiplexer_1_out), .sel(b[0]));
  or or_1 (or_1_out, b[0], b[1], b[2], b[3], b[4]);
  Multiplexer #(.width(64)) multiplexer_2 (.in0(a), .in1(multiplexer_1_out), .out(res_low), .sel(or_1_out));

  assign res_high = {32{1'b0}};
endmodule

module DIVV (
  input  [31:0] divisor,
  input  [31:0] dividend,
  input  clk,
  output [31:0] remainder,
  output [31:0] quotient,
  output done
);

  wire and_1_out, comparator_1_eq, comparator_2_eq, comparator_3_eq, comparator_3_gt, comparator_4_eq,
       nand_1_out, not_1_out, not_2_out, or_1_out, or_3_out, or_4_out, or_5_out;
  wire [6:0] counter_1_q;
  wire [31:0] b_q, multiplexer_1_out, multiplexer_2_out, multiplexer_3_out, multiplexer_4_out,
       multiplexer_5_out, multiplexer_6_out, or_2_out, register_1_q, register_2_q, subtractor_1_out;

  Register #(.width(32)) register_1 (.D(divisor), .en(1'b1), .clk(clk), .Q(register_1_q));  // open: clr
  Register #(.width(32)) register_2 (.D(dividend), .en(1'b1), .clk(clk), .Q(register_2_q));  // open: clr
  Comparator #(.width(32)) comparator_1 (.a(register_1_q), .b(divisor), .eq(comparator_1_eq));  // open: gt, lt
  nand nand_1 (nand_1_out, comparator_2_eq, comparator_1_eq);
  Comparator #(.width(32)) comparator_2 (.a(register_2_q), .b(dividend), .eq(comparator_2_eq));  // open: gt, lt
  Register #(.width(32)) b (.D(divisor), .en(nand_1_out), .clk(clk), .Q(b_q));  // open: clr
  not not_1 (not_1_out, or_1_out);
  or or_1 (or_1_out, counter_1_q[0], counter_1_q[1], counter_1_q[2], counter_1_q[3], counter_1_q[4], counter_1_q[5], counter_1_q[6]);
  assign or_2_out = quotient | 32'h1;  // OR_Gate or_2, 32 bits wide
  Counter #(.max('h7f), .width(7)) counter_1 (
    .clr(nand_1_out), .load(not_1_out), .up(1'b0), .clk(clk), .D(7'b1000000), .Q(counter_1_q));  // open: count, carry
  Multiplexer #(.width(32)) multiplexer_1 (
    .in0(remainder), .in1(subtractor_1_out), .out(multiplexer_1_out), .sel(or_3_out));
  Subtractor #(.width(32)) subtractor_1 (.a(remainder), .b(b_q), .out(subtractor_1_out));  // open: bin, bout
  Comparator #(.mode("unsigned"), .width(32)) comparator_3 (
    .a(remainder), .b(b_q), .gt(comparator_3_gt), .eq(comparator_3_eq));  // open: lt
  or or_3 (or_3_out, comparator_3_gt, comparator_3_eq);
  Multiplexer #(.width(32)) multiplexer_2 (.in0(quotient), .in1(or_2_out), .out(multiplexer_2_out), .sel(or_3_out));
  Multiplexer #(.width(32)) multiplexer_3 (
    .in0(multiplexer_2_out), .in1(dividend), .out(multiplexer_3_out), .sel(not_1_out));
  or or_4 (or_4_out, not_1_out, counter_1_q[0]);
  Multiplexer #(.width(32)) multiplexer_4 (
    .in0({remainder[30:0], quotient[31]}), .in1(multiplexer_5_out), .out(multiplexer_4_out), .sel(or_4_out));
  Multiplexer #(.width(32)) multiplexer_5 (
    .in0(multiplexer_1_out), .in1({32{1'b0}}), .out(multiplexer_5_out), .sel(not_1_out));
  Multiplexer #(.width(32)) multiplexer_6 (
    .in0({quotient[30:0], 1'b0}), .in1(multiplexer_3_out), .out(multiplexer_6_out), .sel(or_4_out));
  and and_1 (and_1_out, clk, not_2_out);
  Register #(.width(32)) a (.D(multiplexer_4_out), .en(1'b1), .clk(and_1_out), .Q(remainder));  // open: clr
  Register #(.width(32)) q (.D(multiplexer_6_out), .en(1'b1), .clk(and_1_out), .Q(quotient));  // open: clr
  not not_2 (not_2_out, done);
  Comparator #(.width(7)) comparator_4 (.a(counter_1_q), .b(7'b0000001), .eq(comparator_4_eq));  // open: gt, lt
  D_Flip_Flop d_ff_1 (.D(or_5_out), .clk(clk), .Q(done), .reset(nand_1_out));  // open: Qn, preset
  or or_5 (or_5_out, done, comparator_4_eq);
endmodule
