// Logisim project schematic.circ as structural Verilog
// R31
module main (
  input  rst,
  input  Jen,
  input  clk,
  input  [31:0] Jin,
  output [31:0] Jout,
  output [31:0] R1,
  output [31:0] R2,
  output [31:0] R3,
  output [31:0] R4,
  output [31:0] R5,
  output [8:0] PC,
  output [31:0] R6,
  output [31:0] R7,
  output [31:0] R8,
  output InstDone,
  output [31:0] R9,
  output [31:0] R10,
  output [31:0] R11,
  output [31:0] R12,
  output [31:0] R13,
  output [31:0] R14,
  output [31:0] R15,
  output [31:0] R16,
  output [31:0] R17,
  output [31:0] R18,
  output [31:0] R19,
  output [31:0] R20,
  output [31:0] R21,
  output [31:0] R22,
  output [31:0] R23,
  output [31:0] R24,
  output [31:0] R25,
  output [31:0] R26,
  output [31:0] R27,
  output [31:0] R28,
  output [31:0] R29,
  output [31:0] R30,
  output [31:0] R31
);

  wire addi_lw, ALUsrc, and_1_out, and_2_out, branch, branchN, j, jal, jr, link, memToReg, memW, or_1_out,
       or_2_out, regDst, regWrite, shift, zero;
  wire [3:0] ALUop;
  wire [4:0] multiplexer_4_out, multiplexer_6_out, multiplexer_8_out, multiplexer_9_out, rd, register_10_q,
       register_11_q, rs, rt, x1_rd, x1_rs, x1_rt, x1_shmt;
  wire [5:0] func, opCode;
  wire [8:0] adder_1_out, adder_2_out, multiplexer_1_out, multiplexer_2_out, multiplexer_3_out, pc_t,
       pcDelayed, register_1_q, register_2_q;
  wire [15:0] x1_imm;
  wire [31:0] a, ALUres, ALUres2, b, b2, bit_extender_1_out, bit_extender_2_out, bit_extender_3_out,
       Dmem_dout, Dread, DWrite, Imem_dout, Imem_jout, imm, InstructionReg_q, multiplexer_5_out,
       multiplexer_10_out, multiplexer_11_out, multiplexer_12_out, shmt, x3_res_low, x4_dread0, x4_dread1;

  Register #(.width(9)) register_1 (.D(pc_t), .clk(clk), .Q(register_1_q), .clr(rst));  // open: en
  Adder #(.width(9)) adder_1 (.a(pc_t), .b(9'h1), .out(adder_1_out));  // open: cin, cout
  Register #(.width(9)) register_2 (.D(register_1_q), .clk(clk), .Q(register_2_q), .clr(rst));  // open: en
  Register #(.width(9)) register_3 (.D(register_2_q), .clk(clk), .Q(pcDelayed), .clr(rst));  // open: en
  Register #(.width(9)) register_4 (.D(pcDelayed), .clk(clk), .Q(PC), .clr(rst));  // open: en
  and and_1 (and_1_out, ~zero, branchN);  // AND_Gate
  or or_1 (or_1_out, and_1_out, and_2_out);
  Multiplexer #(.width(9)) multiplexer_1 (
    .in0(adder_1_out), .in1(adder_2_out), .out(multiplexer_1_out), .sel(or_1_out));
  Adder #(.width(9)) adder_2 (.a(pcDelayed), .b(imm[8:0]), .out(adder_2_out));  // open: cin, cout
  and and_2 (and_2_out, zero, branch);
  Multiplexer #(.width(9)) multiplexer_2 (
    .in0(multiplexer_1_out), .in1(imm[8:0]), .out(multiplexer_2_out), .sel(or_2_out));
  or or_2 (or_2_out, jal, j);
  Register #(.width(9)) pcc (.D(multiplexer_3_out), .clk(clk), .Q(pc_t), .clr(rst));  // open: en
  Multiplexer #(.width(9)) multiplexer_3 (.in0(multiplexer_2_out), .in1(a[8:0]), .out(multiplexer_3_out), .sel(jr));
  ControlUnit controlunit_1 (
    .opCode(opCode), .clock(clk), .rst(rst), .func(func), .ALUop(ALUop), .regDst(regDst), .j(j),
    .ALUsrc(ALUsrc), .shift(shift), .branchN(branchN), .jr(jr), .jal(jal), .beq(branch), .addi_lw(addi_lw),
    .memWrite(memW), .regWrite(regWrite), .memToReg(memToReg), .link(link));
  jtag_ram512 Dmem (
    .clk(clk), .Jen(Jen), .Din(b2), .Jin(Imem_jout), .Wen(memW), .Addr(ALUres[8:0]), .Jout(Jout),
    .Dout(Dmem_dout));
  Register #(.width(32)) MemoryDataReg (.D(Dmem_dout), .clk(clk), .Q(Dread), .clr(rst));  // open: en
  jtag_ram512 Imem (
    .clk(clk), .Jen(Jen), .Jin(Jin), .Addr(pc_t), .Jout(Imem_jout), .Dout(Imem_dout));  // open: Din, Wen
  Register #(.width(32)) InstructionReg (.D(Imem_dout), .clk(clk), .Q(InstructionReg_q), .clr(rst));  // open: en
  InstructionDecode x1 (
    .Instruction(InstructionReg_q), .opCode(opCode), .rt(x1_rt), .rs(x1_rs), .imm(x1_imm), .rd(x1_rd),
    .shmt(x1_shmt), .func(func));
  Register #(.width(5)) register_5 (.D(x1_rs), .clk(clk), .Q(rs), .clr(rst));  // open: en
  Register #(.width(5)) register_6 (.D(x1_rt), .clk(clk), .Q(rt), .clr(rst));  // open: en
  Register #(.width(5)) register_7 (.D(x1_rd), .clk(clk), .Q(rd), .clr(rst));  // open: en
  assign bit_extender_1_out = {{16{x1_imm[15]}}, x1_imm};  // Bit_Extender bit_extender_1
  assign bit_extender_2_out = {{27{1'b0}}, x1_shmt};  // Bit_Extender bit_extender_2
  Register #(.width(32)) register_8 (.D(bit_extender_1_out), .clk(clk), .Q(imm), .clr(rst));  // open: en
  Register #(.width(32)) register_9 (.D(bit_extender_2_out), .clk(clk), .Q(shmt), .clr(rst));  // open: en
  Multiplexer #(.width(5)) multiplexer_4 (.in0(rt), .in1(rd), .out(multiplexer_4_out), .sel(regDst));
  Multiplexer #(.width(32)) multiplexer_5 (.in0(ALUres2), .in1(Dread), .out(multiplexer_5_out), .sel(memToReg));
  Register #(.width(5)) register_10 (.D(multiplexer_6_out), .clk(clk), .Q(register_10_q), .clr(rst));  // open: en
  Multiplexer #(.width(5)) multiplexer_6 (.in0(multiplexer_4_out), .in1(rs), .out(multiplexer_6_out), .sel(addi_lw));
  assign bit_extender_3_out = {{23{pcDelayed[8]}}, pcDelayed};  // Bit_Extender bit_extender_3
  Register #(.width(5)) register_11 (.D(register_10_q), .clk(clk), .Q(register_11_q), .clr(rst));  // open: en
  Multiplexer #(.width(32)) multiplexer_7 (.in0(multiplexer_5_out), .in1(bit_extender_3_out), .out(DWrite), .sel(link));
  Multiplexer #(.width(5)) multiplexer_8 (
    .in0({5{1'b0}}), .in1(register_11_q), .out(multiplexer_8_out), .sel(regWrite));
  Multiplexer #(.width(5)) multiplexer_9 (
    .in0(multiplexer_8_out), .in1({5{1'b1}}), .out(multiplexer_9_out), .sel(link));
  regfile x4 (
    .clk(clk), .rst(rst), .Dwrite(DWrite), .Awrite(multiplexer_9_out), .Aread0(x1_rt), .Aread1(x1_rs),
    .Dread0(x4_dread0), .Dread1(x4_dread1), .R1(R1), .R2(R2), .R3(R3), .R4(R4), .R5(R5), .R6(R6), .R7(R7),
    .R8(R8), .R9(R9), .R10(R10), .R11(R11), .R12(R12), .R13(R13), .R14(R14), .R15(R15), .R16(R16), .R17(R17),
    .R18(R18), .R19(R19), .R20(R20), .R21(R21), .R22(R22), .R23(R23), .R24(R24), .R25(R25), .R26(R26),
    .R27(R27), .R28(R28), .R29(R29), .R30(R30), .R31(R31));
  Register #(.width(32)) u_A (.D(x4_dread0), .clk(clk), .Q(a), .clr(rst));  // open: en
  Register #(.width(32)) u_B (.D(x4_dread1), .clk(clk), .Q(b), .clr(rst));  // open: en
  Register #(.width(32)) register_12 (.D(b), .clk(clk), .Q(b2), .clr(rst));  // open: en
  Multiplexer #(.width(32)) multiplexer_10 (.in0(b), .in1(imm), .out(multiplexer_10_out), .sel(ALUsrc));
  Multiplexer #(.width(32)) multiplexer_11 (
    .in0(multiplexer_10_out), .in1(shmt), .out(multiplexer_11_out), .sel(shift));
  Multiplexer #(.width(32)) multiplexer_12 (.in0(a), .in1(b), .out(multiplexer_12_out), .sel(shift));
  ALU x3 (
    .aluop(ALUop), .b(multiplexer_11_out), .a(multiplexer_12_out), .clk(clk), .zero(zero),
    .res_low(x3_res_low), .InstDone(InstDone));  // open: res_high
  Register #(.width(32)) register_13 (.D(x3_res_low), .clk(clk), .Q(ALUres), .clr(rst));  // open: en
  Register #(.width(32)) register_14 (.D(ALUres), .clk(clk), .Q(ALUres2), .clr(rst));  // open: en
endmodule

module jtag_ram8 (
  input  clk,
  input  Jen,
  input  [31:0] Din,
  input  [31:0] Jin,
  input  Wen,
  input  [2:0] Addr,
  output [31:0] Dout,
  output [31:0] Jout
);

  wire decoder_1_out0, decoder_1_out1, decoder_1_out2, decoder_1_out3, decoder_1_out4, decoder_1_out5,
       decoder_1_out6, decoder_1_out7, or_1_out, or_2_out, or_3_out, or_4_out, or_5_out, or_6_out, or_7_out,
       or_8_out;
  wire [31:0] M0, M1, M2, M3, M4, M5, M6, multiplexer_1_out, multiplexer_2_out, multiplexer_3_out,
       multiplexer_4_out, multiplexer_5_out, multiplexer_6_out, multiplexer_7_out, multiplexer_8_out;

  Decoder #(.select(3)) decoder_1 (
    .out0(decoder_1_out0), .out1(decoder_1_out1), .out2(decoder_1_out2), .out3(decoder_1_out3),
    .out4(decoder_1_out4), .out5(decoder_1_out5), .out6(decoder_1_out6), .out7(decoder_1_out7), .sel(Addr),
    .en(Wen));
  Multiplexer #(.width(32)) multiplexer_1 (.in0(Din), .in1(Jin), .out(multiplexer_1_out), .sel(Jen));
  Multiplexer #(.width(32)) multiplexer_2 (.in0(Din), .in1(M0), .out(multiplexer_2_out), .sel(Jen));
  Multiplexer #(.width(32)) multiplexer_3 (.in0(Din), .in1(M1), .out(multiplexer_3_out), .sel(Jen));
  Multiplexer #(.width(32)) multiplexer_4 (.in0(Din), .in1(M2), .out(multiplexer_4_out), .sel(Jen));
  Multiplexer #(.width(32)) multiplexer_5 (.in0(Din), .in1(M3), .out(multiplexer_5_out), .sel(Jen));
  Multiplexer #(.width(32)) multiplexer_6 (.in0(Din), .in1(M4), .out(multiplexer_6_out), .sel(Jen));
  Multiplexer #(.width(32)) multiplexer_7 (.in0(Din), .in1(M5), .out(multiplexer_7_out), .sel(Jen));
  Multiplexer #(.width(32)) multiplexer_8 (.in0(Din), .in1(M6), .out(multiplexer_8_out), .sel(Jen));
  Register #(.width(32)) register_1 (.D(multiplexer_1_out), .en(or_1_out), .clk(clk), .Q(M0));  // open: clr
  or or_1 (or_1_out, Jen, decoder_1_out0);
  Register #(.width(32)) register_2 (.D(multiplexer_2_out), .en(or_2_out), .clk(clk), .Q(M1));  // open: clr
  or or_2 (or_2_out, Jen, decoder_1_out1);
  Register #(.width(32)) register_3 (.D(multiplexer_3_out), .en(or_3_out), .clk(clk), .Q(M2));  // open: clr
  or or_3 (or_3_out, Jen, decoder_1_out2);
  Register #(.width(32)) register_4 (.D(multiplexer_4_out), .en(or_4_out), .clk(clk), .Q(M3));  // open: clr
  or or_4 (or_4_out, Jen, decoder_1_out3);
  Register #(.width(32)) register_5 (.D(multiplexer_5_out), .en(or_5_out), .clk(clk), .Q(M4));  // open: clr
  or or_5 (or_5_out, Jen, decoder_1_out4);
  Register #(.width(32)) register_6 (.D(multiplexer_6_out), .en(or_6_out), .clk(clk), .Q(M5));  // open: clr
  or or_6 (or_6_out, Jen, decoder_1_out5);
  Register #(.width(32)) register_7 (.D(multiplexer_7_out), .en(or_7_out), .clk(clk), .Q(M6));  // open: clr
  or or_7 (or_7_out, Jen, decoder_1_out6);
  Register #(.width(32)) register_8 (.D(multiplexer_8_out), .en(or_8_out), .clk(clk), .Q(Jout));  // open: clr
  or or_8 (or_8_out, Jen, decoder_1_out7);
  Multiplexer #(.select(3), .width(32)) multiplexer_9 (
    .in0(M0), .in1(M1), .in2(M2), .in3(M3), .in4(M4), .in5(M5), .in6(M6), .in7(Jout), .out(Dout), .sel(Addr));

  // Other names for the same wires on the sheet: M7[31:0] = Jout
endmodule

module jtag_ram64 (
  input  clk,
  input  Jen,
  input  [31:0] Din,
  input  [31:0] Jin,
  input  Wen,
  input  [5:0] Addr,
  output [31:0] Dout,
  output [31:0] Jout
);

  wire decoder_1_out0, decoder_1_out1, decoder_1_out2, decoder_1_out3, decoder_1_out4, decoder_1_out5,
       decoder_1_out6, decoder_1_out7;
  wire [31:0] b0_dout, b0_jout, b1_dout, b1_jout, b2_dout, b2_jout, b3_dout, b3_jout, b4_dout, b4_jout,
       b5_dout, b5_jout, b6_dout, b6_jout, b7_dout;

  Decoder #(.select(3)) decoder_1 (
    .out0(decoder_1_out0), .out1(decoder_1_out1), .out2(decoder_1_out2), .out3(decoder_1_out3),
    .out4(decoder_1_out4), .out5(decoder_1_out5), .out6(decoder_1_out6), .out7(decoder_1_out7),
    .sel(Addr[5:3]), .en(Wen));
  jtag_ram8 b0 (
    .clk(clk), .Jen(Jen), .Din(Din), .Jin(Jin), .Wen(decoder_1_out0), .Addr(Addr[2:0]), .Dout(b0_dout),
    .Jout(b0_jout));
  jtag_ram8 b1 (
    .clk(clk), .Jen(Jen), .Din(Din), .Jin(b0_jout), .Wen(decoder_1_out1), .Addr(Addr[2:0]), .Dout(b1_dout),
    .Jout(b1_jout));
  jtag_ram8 b2 (
    .clk(clk), .Jen(Jen), .Din(Din), .Jin(b1_jout), .Wen(decoder_1_out2), .Addr(Addr[2:0]), .Dout(b2_dout),
    .Jout(b2_jout));
  jtag_ram8 b3 (
    .clk(clk), .Jen(Jen), .Din(Din), .Jin(b2_jout), .Wen(decoder_1_out3), .Addr(Addr[2:0]), .Dout(b3_dout),
    .Jout(b3_jout));
  jtag_ram8 b4 (
    .clk(clk), .Jen(Jen), .Din(Din), .Jin(b3_jout), .Wen(decoder_1_out4), .Addr(Addr[2:0]), .Dout(b4_dout),
    .Jout(b4_jout));
  jtag_ram8 b5 (
    .clk(clk), .Jen(Jen), .Din(Din), .Jin(b4_jout), .Wen(decoder_1_out5), .Addr(Addr[2:0]), .Dout(b5_dout),
    .Jout(b5_jout));
  jtag_ram8 b6 (
    .clk(clk), .Jen(Jen), .Din(Din), .Jin(b5_jout), .Wen(decoder_1_out6), .Addr(Addr[2:0]), .Dout(b6_dout),
    .Jout(b6_jout));
  jtag_ram8 b7 (
    .clk(clk), .Jen(Jen), .Din(Din), .Jin(b6_jout), .Wen(decoder_1_out7), .Addr(Addr[2:0]), .Dout(b7_dout),
    .Jout(Jout));
  Multiplexer #(.select(3), .width(32)) multiplexer_1 (
    .in0(b0_dout), .in1(b1_dout), .in2(b2_dout), .in3(b3_dout), .in4(b4_dout), .in5(b5_dout), .in6(b6_dout),
    .in7(b7_dout), .out(Dout), .sel(Addr[5:3]));
endmodule

module jtag_ram512 (
  input  clk,
  input  Jen,
  input  [31:0] Din,
  input  [31:0] Jin,
  input  Wen,
  input  [8:0] Addr,
  output [31:0] Jout,
  output [31:0] Dout
);

  wire decoder_1_out0, decoder_1_out1, decoder_1_out2, decoder_1_out3, decoder_1_out4, decoder_1_out5,
       decoder_1_out6, decoder_1_out7;
  wire [31:0] b0_dout, b0_jout, b1_dout, b1_jout, b2_dout, b2_jout, b3_dout, b3_jout, b4_dout, b4_jout,
       b5_dout, b5_jout, b6_dout, b6_jout, b7_dout;

  Decoder #(.select(3)) decoder_1 (
    .out0(decoder_1_out0), .out1(decoder_1_out1), .out2(decoder_1_out2), .out3(decoder_1_out3),
    .out4(decoder_1_out4), .out5(decoder_1_out5), .out6(decoder_1_out6), .out7(decoder_1_out7),
    .sel(Addr[8:6]), .en(Wen));
  jtag_ram64 b0 (
    .clk(clk), .Jen(Jen), .Din(Din), .Jin(Jin), .Wen(decoder_1_out0), .Addr(Addr[5:0]), .Dout(b0_dout),
    .Jout(b0_jout));
  jtag_ram64 b1 (
    .clk(clk), .Jen(Jen), .Din(Din), .Jin(b0_jout), .Wen(decoder_1_out1), .Addr(Addr[5:0]), .Dout(b1_dout),
    .Jout(b1_jout));
  jtag_ram64 b2 (
    .clk(clk), .Jen(Jen), .Din(Din), .Jin(b1_jout), .Wen(decoder_1_out2), .Addr(Addr[5:0]), .Dout(b2_dout),
    .Jout(b2_jout));
  jtag_ram64 b3 (
    .clk(clk), .Jen(Jen), .Din(Din), .Jin(b2_jout), .Wen(decoder_1_out3), .Addr(Addr[5:0]), .Dout(b3_dout),
    .Jout(b3_jout));
  jtag_ram64 b4 (
    .clk(clk), .Jen(Jen), .Din(Din), .Jin(b3_jout), .Wen(decoder_1_out4), .Addr(Addr[5:0]), .Dout(b4_dout),
    .Jout(b4_jout));
  jtag_ram64 b5 (
    .clk(clk), .Jen(Jen), .Din(Din), .Jin(b4_jout), .Wen(decoder_1_out5), .Addr(Addr[5:0]), .Dout(b5_dout),
    .Jout(b5_jout));
  jtag_ram64 b6 (
    .clk(clk), .Jen(Jen), .Din(Din), .Jin(b5_jout), .Wen(decoder_1_out6), .Addr(Addr[5:0]), .Dout(b6_dout),
    .Jout(b6_jout));
  jtag_ram64 b7 (
    .clk(clk), .Jen(Jen), .Din(Din), .Jin(b6_jout), .Wen(decoder_1_out7), .Addr(Addr[5:0]), .Dout(b7_dout),
    .Jout(Jout));
  Multiplexer #(.select(3), .width(32)) multiplexer_1 (
    .in0(b0_dout), .in1(b1_dout), .in2(b2_dout), .in3(b3_dout), .in4(b4_dout), .in5(b5_dout), .in6(b6_dout),
    .in7(b7_dout), .out(Dout), .sel(Addr[8:6]));
endmodule

module ADDD (
  input  S,
  input  [31:0] b,
  input  [31:0] a,
  output [31:0] res_low,
  output [31:0] res_high
);

  wire adder_1_cout, adder_2_cout, adder_3_cout, adder_4_cout, adder_5_cout, adder_6_cout, adder_7_cout,
       adder_8_cout, adder_9_cout, adder_10_cout, adder_11_cout, adder_12_cout, adder_13_cout, adder_14_cout,
       adder_15_cout, comparator_1_gt, multiplexer_3_out, multiplexer_5_out, multiplexer_7_out,
       multiplexer_9_out, multiplexer_11_out, multiplexer_13_out, multiplexer_15_out;
  wire [3:0] adder_2_out, adder_3_out, adder_4_out, adder_5_out, adder_6_out, adder_7_out, adder_8_out,
       adder_9_out, adder_10_out, adder_11_out, adder_12_out, adder_13_out, adder_14_out, adder_15_out;
  wire [31:0] multiplexer_1_out, multiplexer_16_out, multiplexer_17_out, not_1_out;

  assign not_1_out = ~b;  // NOT_Gate not_1, 32 bits wide
  Multiplexer #(.width(32)) multiplexer_1 (.in0(b), .in1(not_1_out), .out(multiplexer_1_out), .sel(S));
  Comparator #(.mode("unsigned"), .width(32)) comparator_1 (.a(a), .b(b), .gt(comparator_1_gt));  // open: eq, lt
  Adder #(.width(4)) adder_1 (.a(a[3:0]), .b(multiplexer_1_out[3:0]), .out(res_low[3:0]), .cin(S), .cout(adder_1_cout));
  Adder #(.width(4)) adder_2 (
    .a(a[7:4]), .b(multiplexer_1_out[7:4]), .out(adder_2_out), .cout(adder_2_cout));  // open: cin
  Adder #(.width(4)) adder_3 (
    .a(a[7:4]), .b(multiplexer_1_out[7:4]), .out(adder_3_out), .cin(1'b1), .cout(adder_3_cout));
  Adder #(.width(4)) adder_4 (
    .a(a[11:8]), .b(multiplexer_1_out[11:8]), .out(adder_4_out), .cout(adder_4_cout));  // open: cin
  Adder #(.width(4)) adder_5 (
    .a(a[11:8]), .b(multiplexer_1_out[11:8]), .out(adder_5_out), .cin(1'b1), .cout(adder_5_cout));
  Adder #(.width(4)) adder_6 (
    .a(a[15:12]), .b(multiplexer_1_out[15:12]), .out(adder_6_out), .cout(adder_6_cout));  // open: cin
  Adder #(.width(4)) adder_7 (
    .a(a[15:12]), .b(multiplexer_1_out[15:12]), .out(adder_7_out), .cin(1'b1), .cout(adder_7_cout));
  Adder #(.width(4)) adder_8 (
    .a(a[19:16]), .b(multiplexer_1_out[19:16]), .out(adder_8_out), .cout(adder_8_cout));  // open: cin
  Adder #(.width(4)) adder_9 (
    .a(a[19:16]), .b(multiplexer_1_out[19:16]), .out(adder_9_out), .cin(1'b1), .cout(adder_9_cout));
  Adder #(.width(4)) adder_10 (
    .a(a[23:20]), .b(multiplexer_1_out[23:20]), .out(adder_10_out), .cout(adder_10_cout));  // open: cin
  Adder #(.width(4)) adder_11 (
    .a(a[23:20]), .b(multiplexer_1_out[23:20]), .out(adder_11_out), .cin(1'b1), .cout(adder_11_cout));
  Adder #(.width(4)) adder_12 (
    .a(a[27:24]), .b(multiplexer_1_out[27:24]), .out(adder_12_out), .cout(adder_12_cout));  // open: cin
  Adder #(.width(4)) adder_13 (
    .a(a[27:24]), .b(multiplexer_1_out[27:24]), .out(adder_13_out), .cin(1'b1), .cout(adder_13_cout));
  Adder #(.width(4)) adder_14 (
    .a(a[31:28]), .b(multiplexer_1_out[31:28]), .out(adder_14_out), .cout(adder_14_cout));  // open: cin
  Adder #(.width(4)) adder_15 (
    .a(a[31:28]), .b(multiplexer_1_out[31:28]), .out(adder_15_out), .cin(1'b1), .cout(adder_15_cout));
  Multiplexer #(.width(4)) multiplexer_2 (.in0(adder_2_out), .in1(adder_3_out), .out(res_low[7:4]), .sel(adder_1_cout));
  Multiplexer multiplexer_3 (.in0(adder_2_cout), .in1(adder_3_cout), .out(multiplexer_3_out), .sel(adder_1_cout));
  Multiplexer #(.width(4)) multiplexer_4 (
    .in0(adder_4_out), .in1(adder_5_out), .out(res_low[11:8]), .sel(multiplexer_3_out));
  Multiplexer multiplexer_5 (.in0(adder_4_cout), .in1(adder_5_cout), .out(multiplexer_5_out), .sel(multiplexer_3_out));
  Multiplexer #(.width(4)) multiplexer_6 (
    .in0(adder_6_out), .in1(adder_7_out), .out(res_low[15:12]), .sel(multiplexer_5_out));
  Multiplexer multiplexer_7 (.in0(adder_6_cout), .in1(adder_7_cout), .out(multiplexer_7_out), .sel(multiplexer_5_out));
  Multiplexer #(.width(4)) multiplexer_8 (
    .in0(adder_8_out), .in1(adder_9_out), .out(res_low[19:16]), .sel(multiplexer_7_out));
  Multiplexer multiplexer_9 (.in0(adder_8_cout), .in1(adder_9_cout), .out(multiplexer_9_out), .sel(multiplexer_7_out));
  Multiplexer #(.width(4)) multiplexer_10 (
    .in0(adder_10_out), .in1(adder_11_out), .out(res_low[23:20]), .sel(multiplexer_9_out));
  Multiplexer multiplexer_11 (
    .in0(adder_10_cout), .in1(adder_11_cout), .out(multiplexer_11_out), .sel(multiplexer_9_out));
  Multiplexer #(.width(4)) multiplexer_12 (
    .in0(adder_12_out), .in1(adder_13_out), .out(res_low[27:24]), .sel(multiplexer_11_out));
  Multiplexer multiplexer_13 (
    .in0(adder_12_cout), .in1(adder_13_cout), .out(multiplexer_13_out), .sel(multiplexer_11_out));
  Multiplexer #(.width(4)) multiplexer_14 (
    .in0(adder_14_out), .in1(adder_15_out), .out(res_low[31:28]), .sel(multiplexer_13_out));
  Multiplexer multiplexer_15 (
    .in0(adder_14_cout), .in1(adder_15_cout), .out(multiplexer_15_out), .sel(multiplexer_13_out));
  Multiplexer #(.width(32)) multiplexer_16 (
    .in0({32{1'b0}}), .in1(32'h1), .out(multiplexer_16_out), .sel(multiplexer_15_out));
  Multiplexer #(.width(32)) multiplexer_17 (
    .in0({32{1'b1}}), .in1({32{1'b0}}), .out(multiplexer_17_out), .sel(comparator_1_gt));
  Multiplexer #(.width(32)) multiplexer_18 (
    .in0(multiplexer_16_out), .in1(multiplexer_17_out), .out(res_high), .sel(S));
endmodule

module SRLL (
  input  [31:0] a,
  input  [31:0] b,
  output [31:0] res_high,
  output [31:0] res_low
);

  wire or_1_out;
  wire [31:0] multiplexer_1_out, shifter_1_out, shifter_2_out, shifter_3_out, subtractor_1_out;

  Subtractor #(.width(32)) subtractor_1 (.a(b), .b(32'h1), .out(subtractor_1_out));  // open: bin, bout
  Shifter #(.shift("lr"), .width(32)) shifter_1 (.in(a), .\dist (b[4:0]), .out(shifter_1_out));
  Shifter #(.shift("lr"), .width(32)) shifter_2 (.in(a), .\dist (subtractor_1_out[4:0]), .out(shifter_2_out));
  Shifter #(.shift("lr"), .width(32)) shifter_3 (.in(shifter_2_out), .\dist (5'b00001), .out(shifter_3_out));
  Multiplexer #(.width(32)) multiplexer_1 (
    .in0(shifter_3_out), .in1(shifter_1_out), .out(multiplexer_1_out), .sel(b[0]));
  or or_1 (or_1_out, b[0], b[1], b[2], b[3], b[4]);
  Multiplexer #(.width(32)) multiplexer_2 (.in0(a), .in1(multiplexer_1_out), .out(res_low), .sel(or_1_out));

  assign res_high = {32{1'b0}};
endmodule

module SLLL (
  input  [31:0] a,
  input  [31:0] b,
  output [31:0] res_low,
  output [31:0] res_high
);

  wire [31:0] subtractor_1_out;
  wire [63:0] bit_extender_1_out, shifter_1_out, shifter_2_out, shifter_3_out;

  assign bit_extender_1_out = {{32{1'b0}}, a};  // Bit_Extender bit_extender_1
  Subtractor #(.width(32)) subtractor_1 (.a(b), .b(32'h1), .out(subtractor_1_out));  // open: bin, bout
  Shifter #(.width(64)) shifter_1 (.in(bit_extender_1_out), .\dist ({1'b0, b[4:0]}), .out(shifter_1_out));
  Shifter #(.width(64)) shifter_2 (
    .in(bit_extender_1_out), .\dist ({1'b0, subtractor_1_out[4:0]}), .out(shifter_2_out));
  Shifter #(.width(64)) shifter_3 (.in(shifter_2_out), .\dist (6'b000001), .out(shifter_3_out));
  Multiplexer #(.width(64)) multiplexer_1 (
    .in0(shifter_3_out), .in1(shifter_1_out), .out({res_high, res_low}), .sel(b[0]));
endmodule

module ANDD (
  input  [31:0] a,
  input  [31:0] b,
  output [31:0] res_high,
  output [31:0] res_low
);

  assign res_low = a & b;  // AND_Gate and_1, 32 bits wide

  assign res_high = {32{1'b0}};
endmodule

module ORR (
  input  [31:0] a,
  input  [31:0] b,
  output [31:0] res_high,
  output [31:0] res_low
);

  assign res_low = a | b;  // OR_Gate or_1, 32 bits wide

  assign res_high = {32{1'b0}};
endmodule

module XORR (
  input  [31:0] a,
  input  [31:0] b,
  output [31:0] res_high,
  output [31:0] res_low
);

  assign res_low = a ^ b;  // XOR_Gate xor_1, 32 bits wide

  assign res_high = {32{1'b0}};
endmodule

module SRAA (
  input  [31:0] a,
  input  [31:0] b,
  output [31:0] res_high,
  output [31:0] res_low
);

  wire [31:0] and_1_out, bit_extender_1_out, sth1_res_low, sth2_res_low, subtractor_1_out;

  assign and_1_out = b & 32'h1f;  // AND_Gate and_1, 32 bits wide
  assign bit_extender_1_out = {{31{a[31]}}, a[31]};  // Bit_Extender bit_extender_1
  Subtractor #(.width(32)) subtractor_1 (.a(32'h20), .b(and_1_out), .out(subtractor_1_out));  // open: bin, bout
  SRLL sth1 (.a(a), .b(b), .res_low(sth1_res_low));  // open: res_high
  SLLL sth2 (.a(bit_extender_1_out), .b(subtractor_1_out), .res_low(sth2_res_low));  // open: res_high
  assign res_low = sth1_res_low | sth2_res_low;  // OR_Gate or_1, 32 bits wide
  assign res_high = {{31{res_low[31]}}, res_low[31]};  // Bit_Extender bit_extender_2
endmodule

module SRL64 (
  input  [63:0] a,
  input  [31:0] b,
  output [31:0] res_high,
  output [63:0] res_low
);

  wire or_1_out;
  wire [31:0] subtractor_1_out;
  wire [63:0] multiplexer_1_out, shifter_1_out, shifter_2_out, shifter_3_out;

  Subtractor #(.width(32)) subtractor_1 (.a(b), .b(32'h1), .out(subtractor_1_out));  // open: bin, bout
  Shifter #(.shift("lr"), .width(64)) shifter_1 (.in(a), .\dist ({1'b0, b[4:0]}), .out(shifter_1_out));
  Shifter #(.shift("lr"), .width(64)) shifter_2 (.in(a), .\dist ({1'b0, subtractor_1_out[4:0]}), .out(shifter_2_out));
  Shifter #(.shift("lr"), .width(64)) shifter_3 (.in(shifter_2_out), .\dist (6'b000001), .out(shifter_3_out));
  Multiplexer #(.width(64)) multiplexer_1 (
    .in0(shifter_3_out), .in1(shifter_1_out), .out(multiplexer_1_out), .sel(b[0]));
  or or_1 (or_1_out, b[0], b[1], b[2], b[3], b[4]);
  Multiplexer #(.width(64)) multiplexer_2 (.in0(a), .in1(multiplexer_1_out), .out(res_low), .sel(or_1_out));

  assign res_high = {32{1'b0}};
endmodule

module ALU (
  input  [3:0] aluop,
  input  [31:0] b,
  input  [31:0] a,
  input  clk,
  output [31:0] res_high,
  output zero,
  output [31:0] res_low,
  output InstDone
);

  wire comparator_1_eq, comparator_2_eq, x8_done;
  wire [31:0] adder_1_out, multiplier_1_out, slti_1_res_low, x1_res_high, x1_res_low, x2_res_high,
       x2_res_low, x3_res_high, x3_res_low, x4_res_high, x4_res_low, x5_res_high, x5_res_low, x6_res_high,
       x6_res_low, x7_res_high, x7_res_low, x8_quotient, x8_remainder;

  Multiplier #(.mode("twosComplement"), .width(32)) multiplier_1 (
    .a(a), .b(b), .out(multiplier_1_out));  // open: cin, cout
  Comparator #(.mode("unsigned"), .width(4)) comparator_1 (
    .a(aluop), .b(4'b0001), .eq(comparator_1_eq));  // open: gt, lt
  ADDD x1 (.S(comparator_1_eq), .b(b), .a(a), .res_low(x1_res_low), .res_high(x1_res_high));
  SLTI slti_1 (.a(a), .b(b), .res_low(slti_1_res_low));
  ANDD x2 (.a(a), .b(b), .res_high(x2_res_high), .res_low(x2_res_low));
  ORR x3 (.a(a), .b(b), .res_high(x3_res_high), .res_low(x3_res_low));
  XORR x4 (.a(a), .b(b), .res_high(x4_res_high), .res_low(x4_res_low));
  SLLL x5 (.a(a), .b(b), .res_low(x5_res_low), .res_high(x5_res_high));
  SRLL x6 (.a(a), .b(b), .res_high(x6_res_high), .res_low(x6_res_low));
  SRAA x7 (.a(a), .b(b), .res_high(x7_res_high), .res_low(x7_res_low));
  Adder #(.width(32)) adder_1 (.a(a), .b(b), .out(adder_1_out));  // open: cin, cout
  DIV x8 (.divisor(b), .dividend(a), .clk(clk), .remainder(x8_remainder), .quotient(x8_quotient), .done(x8_done));
  Multiplexer #(.select(4), .width(32)) multiplexer_1 (
    .in0(x1_res_high), .in1(x1_res_high), .in3(x8_remainder), .in4(x2_res_high), .in5(x3_res_high),
    .in6(x4_res_high), .in9(x5_res_high), .in10(x6_res_high), .in11(x7_res_high), .out(res_high), .sel(aluop));  // open: in2, in7, in8, in12, in13, in14, in15
  Multiplexer #(.select(4), .width(32)) multiplexer_2 (
    .in0(x1_res_low), .in1(x1_res_low), .in2(slti_1_res_low), .in3(x8_quotient), .in4(x2_res_low),
    .in5(x3_res_low), .in6(x4_res_low), .in7(a), .in8(multiplier_1_out), .in9(x5_res_low), .in10(x6_res_low),
    .in11(x7_res_low), .in12(adder_1_out), .out(res_low), .sel(aluop));  // open: in13, in14, in15
  Comparator #(.mode("unsigned"), .width(4)) comparator_2 (
    .a(aluop), .b(4'b0011), .eq(comparator_2_eq));  // open: gt, lt
  Multiplexer multiplexer_3 (.in0(1'b1), .in1(x8_done), .out(InstDone), .sel(comparator_2_eq));
  Comparator #(.width(32)) comparator_3 (.a({32{1'b0}}), .b(res_low), .eq(zero));  // open: gt, lt
endmodule

module regfile (
  input  clk,
  input  rst,
  input  [31:0] Dwrite,
  input  [4:0] Awrite,
  input  [4:0] Aread0,
  input  [4:0] Aread1,
  output [31:0] Dread0,
  output [31:0] Dread1,
  output [31:0] R1,
  output [31:0] R2,
  output [31:0] R3,
  output [31:0] R4,
  output [31:0] R5,
  output [31:0] R6,
  output [31:0] R7,
  output [31:0] R8,
  output [31:0] R9,
  output [31:0] R10,
  output [31:0] R11,
  output [31:0] R12,
  output [31:0] R13,
  output [31:0] R14,
  output [31:0] R15,
  output [31:0] R16,
  output [31:0] R17,
  output [31:0] R18,
  output [31:0] R19,
  output [31:0] R20,
  output [31:0] R21,
  output [31:0] R22,
  output [31:0] R23,
  output [31:0] R24,
  output [31:0] R25,
  output [31:0] R26,
  output [31:0] R27,
  output [31:0] R28,
  output [31:0] R29,
  output [31:0] R30,
  output [31:0] R31
);

  wire and_1_out, and_2_out, and_3_out, and_4_out, and_5_out, and_6_out, and_7_out, and_8_out, and_9_out,
       and_10_out, and_11_out, and_12_out, and_13_out, and_14_out, and_15_out, and_16_out, and_17_out,
       and_18_out, and_19_out, and_20_out, and_21_out, and_22_out, and_23_out, and_24_out, and_25_out,
       and_26_out, and_27_out, and_28_out, and_29_out, and_30_out, and_31_out, and_32_out, decoder_1_out0,
       decoder_1_out1, decoder_1_out2, decoder_1_out3, decoder_1_out4, decoder_1_out5, decoder_1_out6,
       decoder_1_out7, decoder_2_out0, decoder_2_out1, decoder_2_out2, decoder_2_out3, or_1_out, or_2_out,
       or_3_out, or_4_out, or_5_out, or_6_out, or_7_out, or_8_out, or_9_out, or_10_out, or_11_out, or_12_out,
       or_13_out, or_14_out, or_15_out, or_16_out, or_17_out, or_18_out, or_19_out, or_20_out, or_21_out,
       or_22_out, or_23_out, or_24_out, or_25_out, or_26_out, or_27_out, or_28_out, or_29_out, or_30_out,
       or_31_out, or_32_out, undriven_2, undriven_3, undriven_4, undriven_5;
  wire [31:0] multiplexer_1_out, multiplexer_2_out, multiplexer_3_out, multiplexer_4_out, multiplexer_5_out,
       multiplexer_6_out, multiplexer_7_out, multiplexer_8_out, multiplexer_9_out, undriven;

  Register #(.width(32)) register_1 (.D(undriven), .en(or_1_out), .clk(undriven_2));  // open: Q, clr
  or or_1 (or_1_out, undriven_5, and_1_out);
  and and_1 (and_1_out, undriven_4, undriven_3);
  Decoder #(.select(3)) decoder_1 (
    .out0(decoder_1_out0), .out1(decoder_1_out1), .out2(decoder_1_out2), .out3(decoder_1_out3),
    .out4(decoder_1_out4), .out5(decoder_1_out5), .out6(decoder_1_out6), .out7(decoder_1_out7),
    .sel(Awrite[4:2]));  // open: en
  Decoder #(.select(2)) decoder_2 (
    .out0(decoder_2_out0), .out1(decoder_2_out1), .out2(decoder_2_out2), .out3(decoder_2_out3),
    .sel(Awrite[1:0]));  // open: en
  Multiplexer #(.width(32)) multiplexer_1 (.in0(Dwrite), .in1({32{1'b0}}), .out(multiplexer_1_out), .sel(rst));
  and and_2 (and_2_out, decoder_2_out0, decoder_1_out1);
  and and_3 (and_3_out, decoder_2_out0, decoder_1_out2);
  and and_4 (and_4_out, decoder_2_out0, decoder_1_out3);
  and and_5 (and_5_out, decoder_2_out0, decoder_1_out4);
  and and_6 (and_6_out, decoder_2_out0, decoder_1_out5);
  and and_7 (and_7_out, decoder_2_out0, decoder_1_out6);
  and and_8 (and_8_out, decoder_2_out0, decoder_1_out7);
  Register #(.width(32)) register_2 (.D(multiplexer_1_out), .en(or_2_out), .clk(clk), .Q(R4));  // open: clr
  or or_2 (or_2_out, rst, and_2_out);
  Register #(.width(32)) register_3 (.D(multiplexer_1_out), .en(or_3_out), .clk(clk), .Q(R8));  // open: clr
  or or_3 (or_3_out, rst, and_3_out);
  Register #(.width(32)) register_4 (.D(multiplexer_1_out), .en(or_4_out), .clk(clk), .Q(R12));  // open: clr
  or or_4 (or_4_out, rst, and_4_out);
  Register #(.width(32)) register_5 (.D(multiplexer_1_out), .en(or_5_out), .clk(clk), .Q(R16));  // open: clr
  or or_5 (or_5_out, rst, and_5_out);
  Register #(.width(32)) register_6 (.D(multiplexer_1_out), .en(or_6_out), .clk(clk), .Q(R20));  // open: clr
  or or_6 (or_6_out, rst, and_6_out);
  Register #(.width(32)) register_7 (.D(multiplexer_1_out), .en(or_7_out), .clk(clk), .Q(R24));  // open: clr
  or or_7 (or_7_out, rst, and_7_out);
  Register #(.width(32)) register_8 (.D(multiplexer_1_out), .en(or_8_out), .clk(clk), .Q(R28));  // open: clr
  or or_8 (or_8_out, rst, and_8_out);
  Multiplexer #(.select(3), .width(32)) multiplexer_2 (
    .in0({32{1'b0}}), .in1(R4), .in2(R8), .in3(R12), .in4(R16), .in5(R20), .in6(R24), .in7(R28),
    .out(multiplexer_2_out), .sel(Aread0[4:2]));
  Multiplexer #(.select(3), .width(32)) multiplexer_3 (
    .in0({32{1'b0}}), .in1(R4), .in2(R8), .in3(R12), .in4(R16), .in5(R20), .in6(R24), .in7(R28),
    .out(multiplexer_3_out), .sel(Aread1[4:2]));
  and and_9 (and_9_out, decoder_2_out1, decoder_1_out0);
  and and_10 (and_10_out, decoder_2_out1, decoder_1_out1);
  and and_11 (and_11_out, decoder_2_out1, decoder_1_out2);
  and and_12 (and_12_out, decoder_2_out1, decoder_1_out3);
  and and_13 (and_13_out, decoder_2_out1, decoder_1_out4);
  and and_14 (and_14_out, decoder_2_out1, decoder_1_out5);
  and and_15 (and_15_out, decoder_2_out1, decoder_1_out6);
  and and_16 (and_16_out, decoder_2_out1, decoder_1_out7);
  Register #(.width(32)) register_9 (.D(multiplexer_1_out), .en(or_9_out), .clk(clk), .Q(R1));  // open: clr
  or or_9 (or_9_out, rst, and_9_out);
  Register #(.width(32)) register_10 (.D(multiplexer_1_out), .en(or_10_out), .clk(clk), .Q(R5));  // open: clr
  or or_10 (or_10_out, rst, and_10_out);
  Register #(.width(32)) register_11 (.D(multiplexer_1_out), .en(or_11_out), .clk(clk), .Q(R9));  // open: clr
  or or_11 (or_11_out, rst, and_11_out);
  Register #(.width(32)) register_12 (.D(multiplexer_1_out), .en(or_12_out), .clk(clk), .Q(R13));  // open: clr
  or or_12 (or_12_out, rst, and_12_out);
  Register #(.width(32)) register_13 (.D(multiplexer_1_out), .en(or_13_out), .clk(clk), .Q(R17));  // open: clr
  or or_13 (or_13_out, rst, and_13_out);
  Register #(.width(32)) register_14 (.D(multiplexer_1_out), .en(or_14_out), .clk(clk), .Q(R21));  // open: clr
  or or_14 (or_14_out, rst, and_14_out);
  Register #(.width(32)) register_15 (.D(multiplexer_1_out), .en(or_15_out), .clk(clk), .Q(R25));  // open: clr
  or or_15 (or_15_out, rst, and_15_out);
  Register #(.width(32)) register_16 (.D(multiplexer_1_out), .en(or_16_out), .clk(clk), .Q(R29));  // open: clr
  or or_16 (or_16_out, rst, and_16_out);
  Multiplexer #(.select(3), .width(32)) multiplexer_4 (
    .in0(R1), .in1(R5), .in2(R9), .in3(R13), .in4(R17), .in5(R21), .in6(R25), .in7(R29),
    .out(multiplexer_4_out), .sel(Aread0[4:2]));
  Multiplexer #(.select(3), .width(32)) multiplexer_5 (
    .in0(R1), .in1(R5), .in2(R9), .in3(R13), .in4(R17), .in5(R21), .in6(R25), .in7(R29),
    .out(multiplexer_5_out), .sel(Aread1[4:2]));
  Register #(.width(32)) register_17 (.D(multiplexer_1_out), .en(or_17_out), .clk(clk), .Q(R2));  // open: clr
  or or_17 (or_17_out, rst, and_17_out);
  and and_17 (and_17_out, decoder_2_out2, decoder_1_out0);
  Register #(.width(32)) register_18 (.D(multiplexer_1_out), .en(or_18_out), .clk(clk), .Q(R6));  // open: clr
  or or_18 (or_18_out, rst, and_18_out);
  and and_18 (and_18_out, decoder_2_out2, decoder_1_out1);
  Register #(.width(32)) register_19 (.D(multiplexer_1_out), .en(or_19_out), .clk(clk), .Q(R10));  // open: clr
  or or_19 (or_19_out, rst, and_19_out);
  and and_19 (and_19_out, decoder_2_out2, decoder_1_out2);
  Register #(.width(32)) register_20 (.D(multiplexer_1_out), .en(or_20_out), .clk(clk), .Q(R14));  // open: clr
  or or_20 (or_20_out, rst, and_20_out);
  and and_20 (and_20_out, decoder_2_out2, decoder_1_out3);
  Register #(.width(32)) register_21 (.D(multiplexer_1_out), .en(or_21_out), .clk(clk), .Q(R18));  // open: clr
  or or_21 (or_21_out, rst, and_21_out);
  and and_21 (and_21_out, decoder_2_out2, decoder_1_out4);
  Register #(.width(32)) register_22 (.D(multiplexer_1_out), .en(or_22_out), .clk(clk), .Q(R22));  // open: clr
  or or_22 (or_22_out, rst, and_22_out);
  and and_22 (and_22_out, decoder_2_out2, decoder_1_out5);
  Register #(.width(32)) register_23 (.D(multiplexer_1_out), .en(or_23_out), .clk(clk), .Q(R26));  // open: clr
  or or_23 (or_23_out, rst, and_23_out);
  and and_23 (and_23_out, decoder_2_out2, decoder_1_out6);
  Register #(.width(32)) register_24 (.D(multiplexer_1_out), .en(or_24_out), .clk(clk), .Q(R30));  // open: clr
  or or_24 (or_24_out, rst, and_24_out);
  and and_24 (and_24_out, decoder_2_out2, decoder_1_out7);
  Multiplexer #(.select(3), .width(32)) multiplexer_6 (
    .in0(R2), .in1(R6), .in2(R10), .in3(R14), .in4(R18), .in5(R22), .in6(R26), .in7(R30),
    .out(multiplexer_6_out), .sel(Aread0[4:2]));
  Multiplexer #(.select(3), .width(32)) multiplexer_7 (
    .in0(R2), .in1(R6), .in2(R10), .in3(R14), .in4(R18), .in5(R22), .in6(R26), .in7(R30),
    .out(multiplexer_7_out), .sel(Aread1[4:2]));
  Register #(.width(32)) register_25 (.D(multiplexer_1_out), .en(or_25_out), .clk(clk), .Q(R3));  // open: clr
  or or_25 (or_25_out, rst, and_25_out);
  and and_25 (and_25_out, decoder_2_out3, decoder_1_out0);
  Register #(.width(32)) register_26 (.D(multiplexer_1_out), .en(or_26_out), .clk(clk), .Q(R7));  // open: clr
  or or_26 (or_26_out, rst, and_26_out);
  and and_26 (and_26_out, decoder_2_out3, decoder_1_out1);
  Register #(.width(32)) register_27 (.D(multiplexer_1_out), .en(or_27_out), .clk(clk), .Q(R11));  // open: clr
  or or_27 (or_27_out, rst, and_27_out);
  and and_27 (and_27_out, decoder_2_out3, decoder_1_out2);
  Register #(.width(32)) register_28 (.D(multiplexer_1_out), .en(or_28_out), .clk(clk), .Q(R15));  // open: clr
  or or_28 (or_28_out, rst, and_28_out);
  and and_28 (and_28_out, decoder_2_out3, decoder_1_out3);
  Register #(.width(32)) register_29 (.D(multiplexer_1_out), .en(or_29_out), .clk(clk), .Q(R19));  // open: clr
  or or_29 (or_29_out, rst, and_29_out);
  and and_29 (and_29_out, decoder_2_out3, decoder_1_out4);
  Register #(.width(32)) register_30 (.D(multiplexer_1_out), .en(or_30_out), .clk(clk), .Q(R23));  // open: clr
  or or_30 (or_30_out, rst, and_30_out);
  and and_30 (and_30_out, decoder_2_out3, decoder_1_out5);
  Register #(.width(32)) register_31 (.D(multiplexer_1_out), .en(or_31_out), .clk(clk), .Q(R27));  // open: clr
  or or_31 (or_31_out, rst, and_31_out);
  and and_31 (and_31_out, decoder_2_out3, decoder_1_out6);
  Register #(.width(32)) register_32 (.D(multiplexer_1_out), .en(or_32_out), .clk(clk), .Q(R31));  // open: clr
  or or_32 (or_32_out, rst, and_32_out);
  and and_32 (and_32_out, decoder_2_out3, decoder_1_out7);
  Multiplexer #(.select(3), .width(32)) multiplexer_8 (
    .in0(R3), .in1(R7), .in2(R11), .in3(R15), .in4(R19), .in5(R23), .in6(R27), .in7(R31),
    .out(multiplexer_8_out), .sel(Aread0[4:2]));
  Multiplexer #(.select(3), .width(32)) multiplexer_9 (
    .in0(R3), .in1(R7), .in2(R11), .in3(R15), .in4(R19), .in5(R23), .in6(R27), .in7(R31),
    .out(multiplexer_9_out), .sel(Aread1[4:2]));
  Multiplexer #(.select(2), .width(32)) multiplexer_10 (
    .in0(multiplexer_2_out), .in1(multiplexer_4_out), .in2(multiplexer_6_out), .in3(multiplexer_8_out),
    .out(Dread0), .sel(Aread0[1:0]));
  Multiplexer #(.select(2), .width(32)) multiplexer_11 (
    .in0(multiplexer_3_out), .in1(multiplexer_5_out), .in2(multiplexer_7_out), .in3(multiplexer_9_out),
    .out(Dread1), .sel(Aread1[1:0]));

  // Notes on the sheet:
  //   Field Template
endmodule

module InstructionDecode (
  input  [31:0] Instruction,
  output [5:0] opCode,
  output [4:0] rt,
  output [4:0] rs,
  output [15:0] imm,
  output [4:0] rd,
  output [4:0] shmt,
  output [5:0] func
);


  assign func = Instruction[5:0];
  assign imm = Instruction[15:0];
  assign opCode = Instruction[31:26];
  assign rd = Instruction[15:11];
  assign rs = Instruction[20:16];
  assign rt = Instruction[25:21];
  assign shmt = Instruction[10:6];
endmodule

module ControlUnit (
  input  [5:0] opCode,
  input  clock,
  input  rst,
  input  [5:0] func,
  output [3:0] ALUop,
  output regDst,
  output j,
  output ALUsrc,
  output shift,
  output branchN,
  output jr,
  output jal,
  output beq,
  output addi_lw,
  output memWrite,
  output regWrite,
  output memToReg,
  output link
);

  wire [5:0] register_1_q, register_2_q, register_3_q, register_4_q, register_5_q, register_6_q;

  Register #(.width(6)) register_1 (.D(opCode), .clk(clock), .Q(register_1_q), .clr(rst));  // open: en
  Register #(.width(6)) register_2 (.D(func), .clk(clock), .Q(register_2_q), .clr(rst));  // open: en
  Register #(.width(6)) register_3 (.D(register_1_q), .clk(clock), .Q(register_3_q), .clr(rst));  // open: en
  Register #(.width(6)) register_4 (.D(register_2_q), .clk(clock), .Q(register_4_q), .clr(rst));  // open: en
  CU3 cu3_1 (
    .func(register_2_q), .opCode(register_1_q), .ALUop(ALUop), .regDst(regDst), .j(j), .ALUsrc(ALUsrc),
    .shift(shift), .branchN(branchN), .jr(jr), .jal(jal), .beq(beq), .addi_lw(addi_lw));
  CU4 cu4_1 (.opCode(register_3_q), .memWrite(memWrite));
  Register #(.width(6)) register_5 (.D(register_3_q), .clk(clock), .Q(register_5_q), .clr(rst));  // open: en
  Register #(.width(6)) register_6 (.D(register_4_q), .clk(clock), .Q(register_6_q), .clr(rst));  // open: en
  CU5 cu5_1 (.func(register_6_q), .opCode(register_5_q), .regWrite(regWrite), .memToReg(memToReg), .link(link));
endmodule

module DIV (
  input  [31:0] divisor,
  input  [31:0] dividend,
  input  clk,
  output [31:0] remainder,
  output [31:0] quotient,
  output done
);

  wire and_1_out, comparator_1_eq, comparator_2_eq, comparator_3_eq, comparator_3_gt, comparator_4_eq,
       nand_1_out, not_1_out, not_2_out, or_1_out, or_3_out, or_4_out, or_5_out;
  wire [6:0] counter_1_q;
  wire [31:0] b_q, multiplexer_1_out, multiplexer_2_out, multiplexer_3_out, multiplexer_4_out,
       multiplexer_5_out, multiplexer_6_out, or_2_out, register_1_q, register_2_q, subtractor_1_out;

  Register #(.width(32)) register_1 (.D(divisor), .en(1'b1), .clk(clk), .Q(register_1_q));  // open: clr
  Register #(.width(32)) register_2 (.D(dividend), .en(1'b1), .clk(clk), .Q(register_2_q));  // open: clr
  Comparator #(.width(32)) comparator_1 (.a(register_1_q), .b(divisor), .eq(comparator_1_eq));  // open: gt, lt
  nand nand_1 (nand_1_out, comparator_2_eq, comparator_1_eq);
  Comparator #(.width(32)) comparator_2 (.a(register_2_q), .b(dividend), .eq(comparator_2_eq));  // open: gt, lt
  Register #(.width(32)) b (.D(divisor), .en(nand_1_out), .clk(clk), .Q(b_q));  // open: clr
  not not_1 (not_1_out, or_1_out);
  or or_1 (or_1_out, counter_1_q[0], counter_1_q[1], counter_1_q[2], counter_1_q[3], counter_1_q[4], counter_1_q[5], counter_1_q[6]);
  assign or_2_out = quotient | 32'h1;  // OR_Gate or_2, 32 bits wide
  Counter #(.max('h7f), .width(7)) counter_1 (
    .clr(nand_1_out), .load(not_1_out), .up(1'b0), .clk(clk), .D(7'b1000000), .Q(counter_1_q));  // open: count, carry
  Multiplexer #(.width(32)) multiplexer_1 (
    .in0(remainder), .in1(subtractor_1_out), .out(multiplexer_1_out), .sel(or_3_out));
  Subtractor #(.width(32)) subtractor_1 (.a(remainder), .b(b_q), .out(subtractor_1_out));  // open: bin, bout
  Comparator #(.mode("unsigned"), .width(32)) comparator_3 (
    .a(remainder), .b(b_q), .gt(comparator_3_gt), .eq(comparator_3_eq));  // open: lt
  or or_3 (or_3_out, comparator_3_gt, comparator_3_eq);
  Multiplexer #(.width(32)) multiplexer_2 (.in0(quotient), .in1(or_2_out), .out(multiplexer_2_out), .sel(or_3_out));
  Multiplexer #(.width(32)) multiplexer_3 (
    .in0(multiplexer_2_out), .in1(dividend), .out(multiplexer_3_out), .sel(not_1_out));
  or or_4 (or_4_out, not_1_out, counter_1_q[0]);
  Multiplexer #(.width(32)) multiplexer_4 (
    .in0({remainder[30:0], quotient[31]}), .in1(multiplexer_5_out), .out(multiplexer_4_out), .sel(or_4_out));
  Multiplexer #(.width(32)) multiplexer_5 (
    .in0(multiplexer_1_out), .in1({32{1'b0}}), .out(multiplexer_5_out), .sel(not_1_out));
  Multiplexer #(.width(32)) multiplexer_6 (
    .in0({quotient[30:0], 1'b0}), .in1(multiplexer_3_out), .out(multiplexer_6_out), .sel(or_4_out));
  and and_1 (and_1_out, clk, not_2_out);
  Register #(.width(32)) a (.D(multiplexer_4_out), .en(1'b1), .clk(and_1_out), .Q(remainder));  // open: clr
  Register #(.width(32)) q (.D(multiplexer_6_out), .en(1'b1), .clk(and_1_out), .Q(quotient));  // open: clr
  not not_2 (not_2_out, done);
  Comparator #(.width(7)) comparator_4 (.a(counter_1_q), .b(7'b0000001), .eq(comparator_4_eq));  // open: gt, lt
  D_Flip_Flop d_ff_1 (.D(or_5_out), .clk(clk), .Q(done), .reset(nand_1_out));  // open: Qn, preset
  or or_5 (or_5_out, done, comparator_4_eq);
endmodule

module SLTI (
  input  [31:0] a,
  input  [31:0] b,
  output [31:0] res_low
);

  wire comparator_1_lt;

  Comparator #(.width(32)) comparator_1 (.a(a), .b(b), .lt(comparator_1_lt));  // open: gt, eq
  assign res_low = {{31{1'b0}}, comparator_1_lt};  // Bit_Extender bit_extender_1
endmodule

module CU3 (
  input  [5:0] func,
  input  [5:0] opCode,
  output [3:0] ALUop,
  output regDst,
  output j,
  output ALUsrc,
  output shift,
  output branchN,
  output jr,
  output jal,
  output beq,
  output addi_lw
);

  wire add, addi, andd, comparator_24_eq, div, lw, mfhi, mflo, mull, mull1, orr, Rtype, slll, slti, sraa,
       srll, sub, sw, xorr;
  wire [3:0] multiplexer_1_out, multiplexer_2_out, multiplexer_3_out, multiplexer_4_out, multiplexer_5_out,
       multiplexer_6_out, multiplexer_7_out, multiplexer_8_out, multiplexer_9_out, multiplexer_10_out,
       multiplexer_11_out, multiplexer_12_out, multiplexer_13_out, multiplexer_14_out, multiplexer_15_out,
       multiplexer_16_out, multiplexer_17_out, multiplexer_18_out, multiplexer_19_out;

  Comparator #(.mode("unsigned"), .width(6)) comparator_1 (.a(6'b100000), .b(func), .eq(add));  // open: gt, lt
  Comparator #(.mode("unsigned"), .width(6)) comparator_2 (.a(6'b100010), .b(func), .eq(sub));  // open: gt, lt
  Comparator #(.mode("unsigned"), .width(6)) comparator_3 (.a(6'b100100), .b(func), .eq(andd));  // open: gt, lt
  Comparator #(.mode("unsigned"), .width(6)) comparator_4 (.a(6'b100101), .b(func), .eq(orr));  // open: gt, lt
  Comparator #(.mode("unsigned"), .width(6)) comparator_5 (.a(6'b100110), .b(func), .eq(xorr));  // open: gt, lt
  Comparator #(.mode("unsigned"), .width(6)) comparator_6 (.a(6'b000100), .b(func), .eq(slll));  // open: gt, lt
  Comparator #(.mode("unsigned"), .width(6)) comparator_7 (.a(6'b000110), .b(func), .eq(srll));  // open: gt, lt
  Comparator #(.mode("unsigned"), .width(6)) comparator_8 (.a(6'b000111), .b(func), .eq(sraa));  // open: gt, lt
  Comparator #(.mode("unsigned"), .width(6)) comparator_9 (.a(6'b011010), .b(func), .eq(div));  // open: gt, lt
  Comparator #(.mode("unsigned"), .width(6)) comparator_10 (.a(6'b010000), .b(func), .eq(mfhi));  // open: gt, lt
  Comparator #(.mode("unsigned"), .width(6)) comparator_11 (.a({6{1'b0}}), .b(func), .eq(shift));  // open: gt, lt
  Comparator #(.mode("unsigned"), .width(6)) comparator_12 (.a(6'b001000), .b(func), .eq(jr));  // open: gt, lt
  Comparator #(.mode("unsigned"), .width(6)) comparator_13 (.a(6'b010010), .b(func), .eq(mflo));  // open: gt, lt
  Comparator #(.mode("unsigned"), .width(6)) comparator_14 (.a(6'b000010), .b(func), .eq(mull1));  // open: gt, lt
  Multiplexer #(.width(4)) multiplexer_1 (.in0(4'b0000), .in1(4'b0001), .out(multiplexer_1_out), .sel(sub));
  Multiplexer #(.width(4)) multiplexer_2 (.in0(multiplexer_1_out), .in1(4'b0100), .out(multiplexer_2_out), .sel(andd));
  Multiplexer #(.width(4)) multiplexer_3 (.in0(multiplexer_2_out), .in1(4'b0101), .out(multiplexer_3_out), .sel(orr));
  Multiplexer #(.width(4)) multiplexer_4 (.in0(multiplexer_3_out), .in1(4'b0110), .out(multiplexer_4_out), .sel(xorr));
  Multiplexer #(.width(4)) multiplexer_5 (.in0(multiplexer_4_out), .in1(4'b1001), .out(multiplexer_5_out), .sel(slll));
  Comparator #(.mode("unsigned"), .width(6)) comparator_15 (.a({6{1'b0}}), .b(opCode), .eq(Rtype));  // open: gt, lt
  Comparator #(.mode("unsigned"), .width(6)) comparator_16 (.a(6'b001000), .b(opCode), .eq(addi));  // open: gt, lt
  Comparator #(.mode("unsigned"), .width(6)) comparator_17 (.a(6'b101011), .b(opCode), .eq(sw));  // open: gt, lt
  Comparator #(.mode("unsigned"), .width(6)) comparator_18 (.a(6'b100011), .b(opCode), .eq(lw));  // open: gt, lt
  Comparator #(.mode("unsigned"), .width(6)) comparator_19 (.a(6'b000101), .b(opCode), .eq(branchN));  // open: gt, lt
  Comparator #(.mode("unsigned"), .width(6)) comparator_20 (.a(6'b001010), .b(opCode), .eq(slti));  // open: gt, lt
  Comparator #(.mode("unsigned"), .width(6)) comparator_21 (.a(6'b000010), .b(opCode), .eq(j));  // open: gt, lt
  Comparator #(.mode("unsigned"), .width(6)) comparator_22 (.a(6'b000011), .b(opCode), .eq(jal));  // open: gt, lt
  Comparator #(.mode("unsigned"), .width(6)) comparator_23 (.a(6'b000100), .b(opCode), .eq(beq));  // open: gt, lt
  Comparator #(.mode("unsigned"), .width(6)) comparator_24 (
    .a(6'b011100), .b(opCode), .eq(comparator_24_eq));  // open: gt, lt
  Multiplexer #(.width(4)) multiplexer_6 (.in0(multiplexer_5_out), .in1(4'b1010), .out(multiplexer_6_out), .sel(srll));
  Multiplexer #(.width(4)) multiplexer_7 (.in0(multiplexer_6_out), .in1(4'b1011), .out(multiplexer_7_out), .sel(sraa));
  Multiplexer #(.width(4)) multiplexer_8 (.in0(multiplexer_7_out), .in1(4'b0011), .out(multiplexer_8_out), .sel(div));
  and and_1 (mull, comparator_24_eq, mull1);
  or or_1 (ALUsrc, addi, sw, lw, branchN, slti);
  or or_2 (addi_lw, addi, lw);
  Multiplexer #(.width(4)) multiplexer_9 (.in0(multiplexer_8_out), .in1(4'b1111), .out(multiplexer_9_out), .sel(mfhi));
  Multiplexer #(.width(4)) multiplexer_10 (
    .in0(multiplexer_9_out), .in1(4'b1001), .out(multiplexer_10_out), .sel(shift));
  Multiplexer #(.width(4)) multiplexer_11 (.in0(multiplexer_10_out), .in1(4'b1111), .out(multiplexer_11_out), .sel(jr));
  or or_3 (regDst, mull, Rtype);
  Multiplexer #(.width(4)) multiplexer_12 (
    .in0(multiplexer_11_out), .in1(4'b1111), .out(multiplexer_12_out), .sel(mflo));
  Multiplexer #(.width(4)) multiplexer_13 (
    .in0(multiplexer_12_out), .in1(4'b1100), .out(multiplexer_13_out), .sel(addi));
  Multiplexer #(.width(4)) multiplexer_14 (.in0(multiplexer_13_out), .in1(4'b0000), .out(multiplexer_14_out), .sel(sw));
  Multiplexer #(.width(4)) multiplexer_15 (.in0(multiplexer_14_out), .in1(4'b0000), .out(multiplexer_15_out), .sel(lw));
  Multiplexer #(.width(4)) multiplexer_16 (
    .in0(multiplexer_15_out), .in1(4'b0111), .out(multiplexer_16_out), .sel(branchN));
  Multiplexer #(.width(4)) multiplexer_17 (
    .in0(multiplexer_16_out), .in1(4'b0010), .out(multiplexer_17_out), .sel(slti));
  Multiplexer #(.width(4)) multiplexer_18 (.in0(multiplexer_17_out), .in1(4'b1111), .out(multiplexer_18_out), .sel(j));
  Multiplexer #(.width(4)) multiplexer_19 (
    .in0(multiplexer_18_out), .in1(4'b0001), .out(multiplexer_19_out), .sel(beq));
  Multiplexer #(.width(4)) multiplexer_20 (.in0(multiplexer_19_out), .in1(4'b1000), .out(ALUop), .sel(mull));

  // Other names for the same wires on the sheet: bne = branchN; sll2 = shift
endmodule

module CU4 (
  input  [5:0] opCode,
  output memWrite
);

  Comparator #(.mode("unsigned"), .width(6)) comparator_1 (.a(6'b101011), .b(opCode), .eq(memWrite));  // open: gt, lt

  // Other names for the same wires on the sheet: sw = memWrite
endmodule

module CU5 (
  input  [5:0] func,
  input  [5:0] opCode,
  output regWrite,
  output memToReg,
  output link
);

  wire add, addi, and_1_out, andd, beq, bne, comparator_24_eq, div, j, jr, mfhi, mflo, mull, mull1, orr,
       Rtype, sll2, slll, slti, sraa, srll, sub, sw, xorr;
  wire [3:0] multiplexer_1_out, multiplexer_2_out, multiplexer_3_out, multiplexer_4_out, multiplexer_5_out,
       multiplexer_6_out, multiplexer_7_out, multiplexer_8_out, multiplexer_9_out, multiplexer_10_out,
       multiplexer_11_out;

  Comparator #(.mode("unsigned"), .width(6)) comparator_1 (.a(6'b100000), .b(func), .eq(add));  // open: gt, lt
  Comparator #(.mode("unsigned"), .width(6)) comparator_2 (.a(6'b100010), .b(func), .eq(sub));  // open: gt, lt
  Comparator #(.mode("unsigned"), .width(6)) comparator_3 (.a(6'b100100), .b(func), .eq(andd));  // open: gt, lt
  Comparator #(.mode("unsigned"), .width(6)) comparator_4 (.a(6'b100101), .b(func), .eq(orr));  // open: gt, lt
  Comparator #(.mode("unsigned"), .width(6)) comparator_5 (.a(6'b100110), .b(func), .eq(xorr));  // open: gt, lt
  Comparator #(.mode("unsigned"), .width(6)) comparator_6 (.a(6'b000100), .b(func), .eq(slll));  // open: gt, lt
  Comparator #(.mode("unsigned"), .width(6)) comparator_7 (.a(6'b000110), .b(func), .eq(srll));  // open: gt, lt
  Comparator #(.mode("unsigned"), .width(6)) comparator_8 (.a(6'b000111), .b(func), .eq(sraa));  // open: gt, lt
  Comparator #(.mode("unsigned"), .width(6)) comparator_9 (.a(6'b011010), .b(func), .eq(div));  // open: gt, lt
  Comparator #(.mode("unsigned"), .width(6)) comparator_10 (.a(6'b010000), .b(func), .eq(mfhi));  // open: gt, lt
  Comparator #(.mode("unsigned"), .width(6)) comparator_11 (.a({6{1'b0}}), .b(func), .eq(sll2));  // open: gt, lt
  Comparator #(.mode("unsigned"), .width(6)) comparator_12 (.a(6'b001000), .b(func), .eq(jr));  // open: gt, lt
  Comparator #(.mode("unsigned"), .width(6)) comparator_13 (.a(6'b010010), .b(func), .eq(mflo));  // open: gt, lt
  Comparator #(.mode("unsigned"), .width(6)) comparator_14 (.a(6'b000010), .b(func), .eq(mull1));  // open: gt, lt
  Multiplexer #(.width(4)) multiplexer_1 (.in0(4'b0000), .in1(4'b0001), .out(multiplexer_1_out), .sel(sub));
  Multiplexer #(.width(4)) multiplexer_2 (.in0(multiplexer_1_out), .in1(4'b0100), .out(multiplexer_2_out), .sel(andd));
  Multiplexer #(.width(4)) multiplexer_3 (.in0(multiplexer_2_out), .in1(4'b0101), .out(multiplexer_3_out), .sel(orr));
  Multiplexer #(.width(4)) multiplexer_4 (.in0(multiplexer_3_out), .in1(4'b0110), .out(multiplexer_4_out), .sel(xorr));
  Multiplexer #(.width(4)) multiplexer_5 (.in0(multiplexer_4_out), .in1(4'b1001), .out(multiplexer_5_out), .sel(slll));
  Multiplexer #(.width(4)) multiplexer_6 (.in0(multiplexer_5_out), .in1(4'b1010), .out(multiplexer_6_out), .sel(srll));
  Comparator #(.mode("unsigned"), .width(6)) comparator_15 (.a({6{1'b0}}), .b(opCode), .eq(Rtype));  // open: gt, lt
  Comparator #(.mode("unsigned"), .width(6)) comparator_16 (.a(6'b001000), .b(opCode), .eq(addi));  // open: gt, lt
  Comparator #(.mode("unsigned"), .width(6)) comparator_17 (.a(6'b101011), .b(opCode), .eq(sw));  // open: gt, lt
  Comparator #(.mode("unsigned"), .width(6)) comparator_18 (.a(6'b100011), .b(opCode), .eq(memToReg));  // open: gt, lt
  Comparator #(.mode("unsigned"), .width(6)) comparator_19 (.a(6'b000101), .b(opCode), .eq(bne));  // open: gt, lt
  Comparator #(.mode("unsigned"), .width(6)) comparator_20 (.a(6'b001010), .b(opCode), .eq(slti));  // open: gt, lt
  Comparator #(.mode("unsigned"), .width(6)) comparator_21 (.a(6'b000010), .b(opCode), .eq(j));  // open: gt, lt
  Comparator #(.mode("unsigned"), .width(6)) comparator_22 (.a(6'b000011), .b(opCode), .eq(link));  // open: gt, lt
  Comparator #(.mode("unsigned"), .width(6)) comparator_23 (.a(6'b000100), .b(opCode), .eq(beq));  // open: gt, lt
  Comparator #(.mode("unsigned"), .width(6)) comparator_24 (
    .a(6'b011100), .b(opCode), .eq(comparator_24_eq));  // open: gt, lt
  and and_1 (and_1_out, ~jr, Rtype);  // AND_Gate
  Multiplexer #(.width(4)) multiplexer_7 (.in0(multiplexer_6_out), .in1(4'b1011), .out(multiplexer_7_out), .sel(sraa));
  Multiplexer #(.width(4)) multiplexer_8 (.in0(multiplexer_7_out), .in1(4'b0011), .out(multiplexer_8_out), .sel(div));
  Multiplexer #(.width(4)) multiplexer_9 (.in0(multiplexer_8_out), .in1(4'b1111), .out(multiplexer_9_out), .sel(mfhi));
  and and_2 (mull, comparator_24_eq, mull1);
  or or_1 (regWrite, and_1_out, addi, mull, slti, memToReg);
  Multiplexer #(.width(4)) multiplexer_10 (
    .in0(multiplexer_9_out), .in1(4'b1001), .out(multiplexer_10_out), .sel(sll2));
  Multiplexer #(.width(4)) multiplexer_11 (.in0(multiplexer_10_out), .in1(4'b1111), .out(multiplexer_11_out), .sel(jr));
  Multiplexer #(.width(4)) multiplexer_12 (.in0(multiplexer_11_out), .in1(4'b1111), .sel(mflo));  // open: out

  // Other names for the same wires on the sheet: jal = link; lw = memToReg
endmodule
