// Logisim project schematic1.circ as structural Verilog: 33 circuits, main circuit main
// R31
module main (
  input  rst,
  input  Jen,
  input  clk,
  input  [31:0] Jin,
  output nop,
  output [8:0] pcOUT,
  output [31:0] Jout,
  output [31:0] R1,
  output [31:0] FR1,
  output [31:0] R2,
  output [31:0] FR2,
  output [31:0] R3,
  output [31:0] FR3,
  output [31:0] R4,
  output [31:0] FR4,
  output [31:0] R5,
  output [31:0] FR5,
  output [31:0] R6,
  output [31:0] FR6,
  output [31:0] R7,
  output [31:0] FR7,
  output [31:0] R8,
  output [31:0] FR8,
  output [31:0] R9,
  output [31:0] FR9,
  output [31:0] R10,
  output [31:0] FR10,
  output [31:0] R11,
  output [31:0] FR11,
  output [31:0] R12,
  output [31:0] FR12,
  output [31:0] R13,
  output [31:0] FR13,
  output [31:0] R14,
  output [31:0] FR14,
  output [31:0] R15,
  output [31:0] FR15,
  output [31:0] R16,
  output [31:0] FR16,
  output [31:0] R17,
  output [31:0] FR17,
  output [31:0] R18,
  output [31:0] FR18,
  output [31:0] R19,
  output [31:0] FR19,
  output [31:0] R20,
  output [31:0] FR20,
  output [31:0] R21,
  output [31:0] FR21,
  output [31:0] R22,
  output [31:0] FR22,
  output [31:0] R23,
  output [31:0] FR23,
  output [31:0] R24,
  output [31:0] FR24,
  output [31:0] R25,
  output [31:0] FR25,
  output [31:0] R26,
  output [31:0] FR26,
  output [31:0] R27,
  output [31:0] FR27,
  output [31:0] R28,
  output [31:0] FR28,
  output [31:0] R29,
  output [31:0] FR29,
  output [31:0] R30,
  output [31:0] FR30,
  output [31:0] R31,
  output [31:0] FR31,
  output InstDone
);

  wire and_1_out, and_3_out, branch, clk_t, comparator_1_eq, comparator_2_eq, comparator_3_eq,
       comparator_4_eq, comparator_5_eq, CUMain_alusrc, CUMain_fromcop, CUMain_memtoreg, CUMain_mohi,
       CUMain_regdst, CUMain_regwrite, CUMain_shmt, divv, FPD, FregWrite, inst, inst2, j, memW,
       multiplexer_14_out, PCWE, tocop, zero;
  wire [2:0] fop;
  wire [3:0] CUMain_aluop;
  wire [4:0] multiplexer_6_out, multiplexer_7_out, multiplexer_13_out, rd, rs, rt;
  wire [5:0] fuSIN, opcSIN;
  wire [8:0] adder_1_out, adder_2_out, multiplexer_4_out, multiplexer_5_out;
  wire [31:0] a, ALUMain_res_high, ALUres, b, Dread, Fa, FALUout, Fb, HI_q, IDMain_imm, IDMain_shmt,
       Imem_dout, Imem_jout, lastINSSIN, lastSIN, multiplexer_1_out, multiplexer_2_out, multiplexer_3_out,
       multiplexer_8_out, multiplexer_9_out, multiplexer_10_out, multiplexer_12_out;

  Adder #(.width(9)) adder_1 (.a(pcOUT), .b(9'h1), .out(adder_1_out));  // open: cin, cout
  Multiplexer #(.width(32)) multiplexer_1 (.in0(b), .in1(IDMain_imm), .out(multiplexer_1_out), .sel(CUMain_alusrc));
  Multiplexer #(.width(32)) multiplexer_2 (
    .in0(multiplexer_1_out), .in1(IDMain_shmt), .out(multiplexer_2_out), .sel(CUMain_shmt));
  and and_1 (and_1_out, ~zero, branch);  // AND_Gate
  Adder #(.width(9)) adder_2 (.a(adder_1_out), .b(IDMain_imm[8:0]), .out(adder_2_out));  // open: cin, cout
  Register #(.width(32)) register_1 (.D(Imem_dout), .clk(clk), .Q(lastSIN));  // open: en, clr
  Multiplexer #(.width(32)) multiplexer_3 (.in0(a), .in1(b), .out(multiplexer_3_out), .sel(CUMain_shmt));
  Multiplexer #(.width(9)) multiplexer_4 (
    .in0(adder_1_out), .in1(adder_2_out), .out(multiplexer_4_out), .sel(and_1_out));
  Multiplexer #(.width(9)) multiplexer_5 (
    .in0(multiplexer_4_out), .in1(IDMain_imm[8:0]), .out(multiplexer_5_out), .sel(j));
  Register #(.width(9)) pc (.D(multiplexer_5_out), .en(PCWE), .clk(clk_t), .Q(pcOUT), .clr(rst));
  InstructionDecode IDMain (
    .Instruction(Imem_dout), .opCode(opcSIN), .rt(rt), .rs(rs), .imm(IDMain_imm), .rd(rd),
    .shmt(IDMain_shmt), .func(fuSIN));
  ControlUnit CUMain (
    .func(fuSIN), .main_clock(clk), .inst(inst), .inst2(inst2), .opCode(opcSIN), .ALUop(CUMain_aluop),
    .nop(nop), .regDst(CUMain_regdst), .ALUsrc(CUMain_alusrc), .shmt(CUMain_shmt), .j(j),
    .regWrite(CUMain_regwrite), .memToReg(CUMain_memtoreg), .memWrite(memW), .branch(branch), .divv(divv),
    .mohi(CUMain_mohi), .FregWrite(FregWrite), .TOCOP(tocop), .FROMCOP(CUMain_fromcop), .FALUop(fop));
  ALU ALUMain (
    .aluop(CUMain_aluop), .b(multiplexer_2_out), .a(multiplexer_3_out), .clk(clk),
    .res_high(ALUMain_res_high), .zero(zero), .res_low(ALUres), .InstDone(inst));
  Register #(.width(32)) HI (.D(ALUMain_res_high), .en(divv), .clk(clk_t), .Q(HI_q));  // open: clr
  Multiplexer #(.width(5)) multiplexer_6 (.in0(rs), .in1(rd), .out(multiplexer_6_out), .sel(CUMain_regdst));
  Multiplexer #(.width(5)) multiplexer_7 (
    .in0({5{1'b0}}), .in1(multiplexer_6_out), .out(multiplexer_7_out), .sel(CUMain_regwrite));
  Multiplexer #(.width(32)) multiplexer_8 (.in0(ALUres), .in1(Dread), .out(multiplexer_8_out), .sel(CUMain_memtoreg));
  Multiplexer #(.width(32)) multiplexer_9 (
    .in0(multiplexer_8_out), .in1(HI_q), .out(multiplexer_9_out), .sel(CUMain_mohi));
  and and_2 (clk_t, clk, ~nop);  // AND_Gate
  Multiplexer #(.width(32)) multiplexer_10 (
    .in0(multiplexer_9_out), .in1(Fa), .out(multiplexer_10_out), .sel(CUMain_fromcop));
  Multiplexer multiplexer_11 (.in0(inst), .in1(FPD), .out(PCWE), .sel(FregWrite));
  jtag_ram512 Imem (
    .clk(clk), .Jen(Jen), .Jin(Jin), .Addr(pcOUT), .Jout(Imem_jout), .Dout(Imem_dout));  // open: Din, Wen
  regfile RegfileMain (
    .clk(clk_t), .rst(rst), .Dwrite(multiplexer_10_out), .Awrite(multiplexer_7_out), .Aread0(rt),
    .Aread1(rs), .Dread0(a), .Dread1(b), .R1(R1), .R2(R2), .R3(R3), .R4(R4), .R5(R5), .R6(R6), .R7(R7),
    .R8(R8), .R9(R9), .R10(R10), .R11(R11), .R12(R12), .R13(R13), .R14(R14), .R15(R15), .R16(R16), .R17(R17),
    .R18(R18), .R19(R19), .R20(R20), .R21(R21), .R22(R22), .R23(R23), .R24(R24), .R25(R25), .R26(R26),
    .R27(R27), .R28(R28), .R29(R29), .R30(R30), .R31(R31));
  Comparator #(.width(32)) comparator_1 (.a(lastSIN), .b(32'h1407818), .eq(comparator_1_eq));  // open: gt, lt
  or or_1 (InstDone, PCWE, comparator_1_eq);
  jtag_ram512 Dmem (
    .clk(clk), .Jen(Jen), .Din(b), .Jin(Imem_jout), .Wen(memW), .Addr(ALUres[10:2]), .Jout(Jout), .Dout(Dread));
  Multiplexer #(.width(32)) multiplexer_12 (.in0(FALUout), .in1(a), .out(multiplexer_12_out), .sel(tocop));
  Multiplexer #(.width(5)) multiplexer_13 (.in0({5{1'b0}}), .in1(rd), .out(multiplexer_13_out), .sel(FregWrite));
  regfile FP_RF (
    .clk(clk), .rst(rst), .Dwrite(multiplexer_12_out), .Awrite(multiplexer_13_out), .Aread0(rt), .Aread1(rs),
    .Dread0(Fa), .Dread1(Fb), .R1(FR1), .R2(FR2), .R3(FR3), .R4(FR4), .R5(FR5), .R6(FR6), .R7(FR7), .R8(FR8),
    .R9(FR9), .R10(FR10), .R11(FR11), .R12(FR12), .R13(FR13), .R14(FR14), .R15(FR15), .R16(FR16), .R17(FR17),
    .R18(FR18), .R19(FR19), .R20(FR20), .R21(FR21), .R22(FR22), .R23(FR23), .R24(FR24), .R25(FR25),
    .R26(FR26), .R27(FR27), .R28(FR28), .R29(FR29), .R30(FR30), .R31(FR31));
  FP_ALU FPALUMain (.a(Fa), .b(Fb), .aluop(fop), .clk(clk), .res(FALUout), .Done(FPD));
  Comparator #(.width(3)) comparator_2 (.a(fop), .b(3'b101), .eq(comparator_2_eq));  // open: gt, lt
  Comparator #(.width(6)) comparator_3 (.a(fuSIN), .b(6'b000001), .eq(comparator_3_eq));  // open: gt, lt
  Comparator #(.width(6)) comparator_4 (.a(opcSIN), .b({6{1'b0}}), .eq(comparator_4_eq));  // open: gt, lt
  and and_3 (and_3_out, comparator_2_eq, comparator_3_eq, comparator_4_eq);
  Multiplexer multiplexer_14 (.in0(inst), .in1(FPD), .out(multiplexer_14_out), .sel(and_3_out));
  Multiplexer multiplexer_15 (.in0(multiplexer_14_out), .in1(1'b1), .out(inst2), .sel(comparator_5_eq));
  Comparator #(.width(32)) comparator_5 (.a(lastINSSIN), .b(32'h1407818), .eq(comparator_5_eq));  // open: gt, lt

  // Other names for the same wires on the sheet: main_clock = clk
endmodule

module jtag_ram8 (
  input  clk,
  input  Jen,
  input  [31:0] Din,
  input  [31:0] Jin,
  input  Wen,
  input  [2:0] Addr,
  output [31:0] Dout,
  output [31:0] Jout
);

  wire decoder_1_out0, decoder_1_out1, decoder_1_out2, decoder_1_out3, decoder_1_out4, decoder_1_out5,
       decoder_1_out6, decoder_1_out7, or_1_out, or_2_out, or_3_out, or_4_out, or_5_out, or_6_out, or_7_out,
       or_8_out;
  wire [31:0] M0, M1, M2, M3, M4, M5, M6, multiplexer_1_out, multiplexer_2_out, multiplexer_3_out,
       multiplexer_4_out, multiplexer_5_out, multiplexer_6_out, multiplexer_7_out, multiplexer_8_out;

  Decoder #(.select(3)) decoder_1 (
    .out0(decoder_1_out0), .out1(decoder_1_out1), .out2(decoder_1_out2), .out3(decoder_1_out3),
    .out4(decoder_1_out4), .out5(decoder_1_out5), .out6(decoder_1_out6), .out7(decoder_1_out7), .sel(Addr),
    .en(Wen));
  Multiplexer #(.width(32)) multiplexer_1 (.in0(Din), .in1(Jin), .out(multiplexer_1_out), .sel(Jen));
  Multiplexer #(.width(32)) multiplexer_2 (.in0(Din), .in1(M0), .out(multiplexer_2_out), .sel(Jen));
  Multiplexer #(.width(32)) multiplexer_3 (.in0(Din), .in1(M1), .out(multiplexer_3_out), .sel(Jen));
  Multiplexer #(.width(32)) multiplexer_4 (.in0(Din), .in1(M2), .out(multiplexer_4_out), .sel(Jen));
  Multiplexer #(.width(32)) multiplexer_5 (.in0(Din), .in1(M3), .out(multiplexer_5_out), .sel(Jen));
  Multiplexer #(.width(32)) multiplexer_6 (.in0(Din), .in1(M4), .out(multiplexer_6_out), .sel(Jen));
  Multiplexer #(.width(32)) multiplexer_7 (.in0(Din), .in1(M5), .out(multiplexer_7_out), .sel(Jen));
  Multiplexer #(.width(32)) multiplexer_8 (.in0(Din), .in1(M6), .out(multiplexer_8_out), .sel(Jen));
  Register #(.width(32)) register_1 (.D(multiplexer_1_out), .en(or_1_out), .clk(clk), .Q(M0));  // open: clr
  or or_1 (or_1_out, Jen, decoder_1_out0);
  Register #(.width(32)) register_2 (.D(multiplexer_2_out), .en(or_2_out), .clk(clk), .Q(M1));  // open: clr
  or or_2 (or_2_out, Jen, decoder_1_out1);
  Register #(.width(32)) register_3 (.D(multiplexer_3_out), .en(or_3_out), .clk(clk), .Q(M2));  // open: clr
  or or_3 (or_3_out, Jen, decoder_1_out2);
  Register #(.width(32)) register_4 (.D(multiplexer_4_out), .en(or_4_out), .clk(clk), .Q(M3));  // open: clr
  or or_4 (or_4_out, Jen, decoder_1_out3);
  Register #(.width(32)) register_5 (.D(multiplexer_5_out), .en(or_5_out), .clk(clk), .Q(M4));  // open: clr
  or or_5 (or_5_out, Jen, decoder_1_out4);
  Register #(.width(32)) register_6 (.D(multiplexer_6_out), .en(or_6_out), .clk(clk), .Q(M5));  // open: clr
  or or_6 (or_6_out, Jen, decoder_1_out5);
  Register #(.width(32)) register_7 (.D(multiplexer_7_out), .en(or_7_out), .clk(clk), .Q(M6));  // open: clr
  or or_7 (or_7_out, Jen, decoder_1_out6);
  Register #(.width(32)) register_8 (.D(multiplexer_8_out), .en(or_8_out), .clk(clk), .Q(Jout));  // open: clr
  or or_8 (or_8_out, Jen, decoder_1_out7);
  Multiplexer #(.select(3), .width(32)) multiplexer_9 (
    .in0(M0), .in1(M1), .in2(M2), .in3(M3), .in4(M4), .in5(M5), .in6(M6), .in7(Jout), .out(Dout), .sel(Addr));

  // Other names for the same wires on the sheet: M7[31:0] = Jout
endmodule

module jtag_ram64 (
  input  clk,
  input  Jen,
  input  [31:0] Din,
  input  [31:0] Jin,
  input  Wen,
  input  [5:0] Addr,
  output [31:0] Dout,
  output [31:0] Jout
);

  wire decoder_1_out0, decoder_1_out1, decoder_1_out2, decoder_1_out3, decoder_1_out4, decoder_1_out5,
       decoder_1_out6, decoder_1_out7;
  wire [31:0] b0_dout, b0_jout, b1_dout, b1_jout, b2_dout, b2_jout, b3_dout, b3_jout, b4_dout, b4_jout,
       b5_dout, b5_jout, b6_dout, b6_jout, b7_dout;

  Decoder #(.select(3)) decoder_1 (
    .out0(decoder_1_out0), .out1(decoder_1_out1), .out2(decoder_1_out2), .out3(decoder_1_out3),
    .out4(decoder_1_out4), .out5(decoder_1_out5), .out6(decoder_1_out6), .out7(decoder_1_out7),
    .sel(Addr[5:3]), .en(Wen));
  jtag_ram8 b0 (
    .clk(clk), .Jen(Jen), .Din(Din), .Jin(Jin), .Wen(decoder_1_out0), .Addr(Addr[2:0]), .Dout(b0_dout),
    .Jout(b0_jout));
  jtag_ram8 b1 (
    .clk(clk), .Jen(Jen), .Din(Din), .Jin(b0_jout), .Wen(decoder_1_out1), .Addr(Addr[2:0]), .Dout(b1_dout),
    .Jout(b1_jout));
  jtag_ram8 b2 (
    .clk(clk), .Jen(Jen), .Din(Din), .Jin(b1_jout), .Wen(decoder_1_out2), .Addr(Addr[2:0]), .Dout(b2_dout),
    .Jout(b2_jout));
  jtag_ram8 b3 (
    .clk(clk), .Jen(Jen), .Din(Din), .Jin(b2_jout), .Wen(decoder_1_out3), .Addr(Addr[2:0]), .Dout(b3_dout),
    .Jout(b3_jout));
  jtag_ram8 b4 (
    .clk(clk), .Jen(Jen), .Din(Din), .Jin(b3_jout), .Wen(decoder_1_out4), .Addr(Addr[2:0]), .Dout(b4_dout),
    .Jout(b4_jout));
  jtag_ram8 b5 (
    .clk(clk), .Jen(Jen), .Din(Din), .Jin(b4_jout), .Wen(decoder_1_out5), .Addr(Addr[2:0]), .Dout(b5_dout),
    .Jout(b5_jout));
  jtag_ram8 b6 (
    .clk(clk), .Jen(Jen), .Din(Din), .Jin(b5_jout), .Wen(decoder_1_out6), .Addr(Addr[2:0]), .Dout(b6_dout),
    .Jout(b6_jout));
  jtag_ram8 b7 (
    .clk(clk), .Jen(Jen), .Din(Din), .Jin(b6_jout), .Wen(decoder_1_out7), .Addr(Addr[2:0]), .Dout(b7_dout),
    .Jout(Jout));
  Multiplexer #(.select(3), .width(32)) multiplexer_1 (
    .in0(b0_dout), .in1(b1_dout), .in2(b2_dout), .in3(b3_dout), .in4(b4_dout), .in5(b5_dout), .in6(b6_dout),
    .in7(b7_dout), .out(Dout), .sel(Addr[5:3]));
endmodule

module jtag_ram512 (
  input  clk,
  input  Jen,
  input  [31:0] Din,
  input  [31:0] Jin,
  input  Wen,
  input  [8:0] Addr,
  output [31:0] Jout,
  output [31:0] Dout
);

  wire decoder_1_out0, decoder_1_out1, decoder_1_out2, decoder_1_out3, decoder_1_out4, decoder_1_out5,
       decoder_1_out6, decoder_1_out7;
  wire [31:0] b0_dout, b0_jout, b1_dout, b1_jout, b2_dout, b2_jout, b3_dout, b3_jout, b4_dout, b4_jout,
       b5_dout, b5_jout, b6_dout, b6_jout, b7_dout;

  Decoder #(.select(3)) decoder_1 (
    .out0(decoder_1_out0), .out1(decoder_1_out1), .out2(decoder_1_out2), .out3(decoder_1_out3),
    .out4(decoder_1_out4), .out5(decoder_1_out5), .out6(decoder_1_out6), .out7(decoder_1_out7),
    .sel(Addr[8:6]), .en(Wen));
  jtag_ram64 b0 (
    .clk(clk), .Jen(Jen), .Din(Din), .Jin(Jin), .Wen(decoder_1_out0), .Addr(Addr[5:0]), .Dout(b0_dout),
    .Jout(b0_jout));
  jtag_ram64 b1 (
    .clk(clk), .Jen(Jen), .Din(Din), .Jin(b0_jout), .Wen(decoder_1_out1), .Addr(Addr[5:0]), .Dout(b1_dout),
    .Jout(b1_jout));
  jtag_ram64 b2 (
    .clk(clk), .Jen(Jen), .Din(Din), .Jin(b1_jout), .Wen(decoder_1_out2), .Addr(Addr[5:0]), .Dout(b2_dout),
    .Jout(b2_jout));
  jtag_ram64 b3 (
    .clk(clk), .Jen(Jen), .Din(Din), .Jin(b2_jout), .Wen(decoder_1_out3), .Addr(Addr[5:0]), .Dout(b3_dout),
    .Jout(b3_jout));
  jtag_ram64 b4 (
    .clk(clk), .Jen(Jen), .Din(Din), .Jin(b3_jout), .Wen(decoder_1_out4), .Addr(Addr[5:0]), .Dout(b4_dout),
    .Jout(b4_jout));
  jtag_ram64 b5 (
    .clk(clk), .Jen(Jen), .Din(Din), .Jin(b4_jout), .Wen(decoder_1_out5), .Addr(Addr[5:0]), .Dout(b5_dout),
    .Jout(b5_jout));
  jtag_ram64 b6 (
    .clk(clk), .Jen(Jen), .Din(Din), .Jin(b5_jout), .Wen(decoder_1_out6), .Addr(Addr[5:0]), .Dout(b6_dout),
    .Jout(b6_jout));
  jtag_ram64 b7 (
    .clk(clk), .Jen(Jen), .Din(Din), .Jin(b6_jout), .Wen(decoder_1_out7), .Addr(Addr[5:0]), .Dout(b7_dout),
    .Jout(Jout));
  Multiplexer #(.select(3), .width(32)) multiplexer_1 (
    .in0(b0_dout), .in1(b1_dout), .in2(b2_dout), .in3(b3_dout), .in4(b4_dout), .in5(b5_dout), .in6(b6_dout),
    .in7(b7_dout), .out(Dout), .sel(Addr[8:6]));
endmodule

module ADDD (
  input  S,
  input  [31:0] b,
  input  [31:0] a,
  output [31:0] res_low,
  output [31:0] res_high
);

  wire adder_1_cout, adder_2_cout, adder_3_cout, adder_4_cout, adder_5_cout, adder_6_cout, adder_7_cout,
       adder_8_cout, adder_9_cout, adder_10_cout, adder_11_cout, adder_12_cout, adder_13_cout, adder_14_cout,
       adder_15_cout, comparator_1_gt, multiplexer_3_out, multiplexer_5_out, multiplexer_7_out,
       multiplexer_9_out, multiplexer_11_out, multiplexer_13_out, multiplexer_15_out;
  wire [3:0] adder_2_out, adder_3_out, adder_4_out, adder_5_out, adder_6_out, adder_7_out, adder_8_out,
       adder_9_out, adder_10_out, adder_11_out, adder_12_out, adder_13_out, adder_14_out, adder_15_out;
  wire [31:0] multiplexer_1_out, multiplexer_16_out, multiplexer_17_out, not_1_out;

  assign not_1_out = ~b;  // NOT_Gate not_1, 32 bits wide
  Multiplexer #(.width(32)) multiplexer_1 (.in0(b), .in1(not_1_out), .out(multiplexer_1_out), .sel(S));
  Comparator #(.mode("unsigned"), .width(32)) comparator_1 (.a(a), .b(b), .gt(comparator_1_gt));  // open: eq, lt
  Adder #(.width(4)) adder_1 (.a(a[3:0]), .b(multiplexer_1_out[3:0]), .out(res_low[3:0]), .cin(S), .cout(adder_1_cout));
  Adder #(.width(4)) adder_2 (
    .a(a[7:4]), .b(multiplexer_1_out[7:4]), .out(adder_2_out), .cout(adder_2_cout));  // open: cin
  Adder #(.width(4)) adder_3 (
    .a(a[7:4]), .b(multiplexer_1_out[7:4]), .out(adder_3_out), .cin(1'b1), .cout(adder_3_cout));
  Adder #(.width(4)) adder_4 (
    .a(a[11:8]), .b(multiplexer_1_out[11:8]), .out(adder_4_out), .cout(adder_4_cout));  // open: cin
  Adder #(.width(4)) adder_5 (
    .a(a[11:8]), .b(multiplexer_1_out[11:8]), .out(adder_5_out), .cin(1'b1), .cout(adder_5_cout));
  Adder #(.width(4)) adder_6 (
    .a(a[15:12]), .b(multiplexer_1_out[15:12]), .out(adder_6_out), .cout(adder_6_cout));  // open: cin
  Adder #(.width(4)) adder_7 (
    .a(a[15:12]), .b(multiplexer_1_out[15:12]), .out(adder_7_out), .cin(1'b1), .cout(adder_7_cout));
  Adder #(.width(4)) adder_8 (
    .a(a[19:16]), .b(multiplexer_1_out[19:16]), .out(adder_8_out), .cout(adder_8_cout));  // open: cin
  Adder #(.width(4)) adder_9 (
    .a(a[19:16]), .b(multiplexer_1_out[19:16]), .out(adder_9_out), .cin(1'b1), .cout(adder_9_cout));
  Adder #(.width(4)) adder_10 (
    .a(a[23:20]), .b(multiplexer_1_out[23:20]), .out(adder_10_out), .cout(adder_10_cout));  // open: cin
  Adder #(.width(4)) adder_11 (
    .a(a[23:20]), .b(multiplexer_1_out[23:20]), .out(adder_11_out), .cin(1'b1), .cout(adder_11_cout));
  Adder #(.width(4)) adder_12 (
    .a(a[27:24]), .b(multiplexer_1_out[27:24]), .out(adder_12_out), .cout(adder_12_cout));  // open: cin
  Adder #(.width(4)) adder_13 (
    .a(a[27:24]), .b(multiplexer_1_out[27:24]), .out(adder_13_out), .cin(1'b1), .cout(adder_13_cout));
  Adder #(.width(4)) adder_14 (
    .a(a[31:28]), .b(multiplexer_1_out[31:28]), .out(adder_14_out), .cout(adder_14_cout));  // open: cin
  Adder #(.width(4)) adder_15 (
    .a(a[31:28]), .b(multiplexer_1_out[31:28]), .out(adder_15_out), .cin(1'b1), .cout(adder_15_cout));
  Multiplexer #(.width(4)) multiplexer_2 (.in0(adder_2_out), .in1(adder_3_out), .out(res_low[7:4]), .sel(adder_1_cout));
  Multiplexer multiplexer_3 (.in0(adder_2_cout), .in1(adder_3_cout), .out(multiplexer_3_out), .sel(adder_1_cout));
  Multiplexer #(.width(4)) multiplexer_4 (
    .in0(adder_4_out), .in1(adder_5_out), .out(res_low[11:8]), .sel(multiplexer_3_out));
  Multiplexer multiplexer_5 (.in0(adder_4_cout), .in1(adder_5_cout), .out(multiplexer_5_out), .sel(multiplexer_3_out));
  Multiplexer #(.width(4)) multiplexer_6 (
    .in0(adder_6_out), .in1(adder_7_out), .out(res_low[15:12]), .sel(multiplexer_5_out));
  Multiplexer multiplexer_7 (.in0(adder_6_cout), .in1(adder_7_cout), .out(multiplexer_7_out), .sel(multiplexer_5_out));
  Multiplexer #(.width(4)) multiplexer_8 (
    .in0(adder_8_out), .in1(adder_9_out), .out(res_low[19:16]), .sel(multiplexer_7_out));
  Multiplexer multiplexer_9 (.in0(adder_8_cout), .in1(adder_9_cout), .out(multiplexer_9_out), .sel(multiplexer_7_out));
  Multiplexer #(.width(4)) multiplexer_10 (
    .in0(adder_10_out), .in1(adder_11_out), .out(res_low[23:20]), .sel(multiplexer_9_out));
  Multiplexer multiplexer_11 (
    .in0(adder_10_cout), .in1(adder_11_cout), .out(multiplexer_11_out), .sel(multiplexer_9_out));
  Multiplexer #(.width(4)) multiplexer_12 (
    .in0(adder_12_out), .in1(adder_13_out), .out(res_low[27:24]), .sel(multiplexer_11_out));
  Multiplexer multiplexer_13 (
    .in0(adder_12_cout), .in1(adder_13_cout), .out(multiplexer_13_out), .sel(multiplexer_11_out));
  Multiplexer #(.width(4)) multiplexer_14 (
    .in0(adder_14_out), .in1(adder_15_out), .out(res_low[31:28]), .sel(multiplexer_13_out));
  Multiplexer multiplexer_15 (
    .in0(adder_14_cout), .in1(adder_15_cout), .out(multiplexer_15_out), .sel(multiplexer_13_out));
  Multiplexer #(.width(32)) multiplexer_16 (
    .in0({32{1'b0}}), .in1(32'h1), .out(multiplexer_16_out), .sel(multiplexer_15_out));
  Multiplexer #(.width(32)) multiplexer_17 (
    .in0({32{1'b1}}), .in1({32{1'b0}}), .out(multiplexer_17_out), .sel(comparator_1_gt));
  Multiplexer #(.width(32)) multiplexer_18 (
    .in0(multiplexer_16_out), .in1(multiplexer_17_out), .out(res_high), .sel(S));
endmodule

module SRLL (
  input  [31:0] a,
  input  [31:0] b,
  output [31:0] res_high,
  output [31:0] res_low
);

  wire or_1_out;
  wire [31:0] multiplexer_1_out, shifter_1_out, shifter_2_out, shifter_3_out, subtractor_1_out;

  Subtractor #(.width(32)) subtractor_1 (.a(b), .b(32'h1), .out(subtractor_1_out));  // open: bin, bout
  Shifter #(.shift("lr"), .width(32)) shifter_1 (.in(a), .\dist (b[4:0]), .out(shifter_1_out));
  Shifter #(.shift("lr"), .width(32)) shifter_2 (.in(a), .\dist (subtractor_1_out[4:0]), .out(shifter_2_out));
  Shifter #(.shift("lr"), .width(32)) shifter_3 (.in(shifter_2_out), .\dist (5'b00001), .out(shifter_3_out));
  Multiplexer #(.width(32)) multiplexer_1 (
    .in0(shifter_3_out), .in1(shifter_1_out), .out(multiplexer_1_out), .sel(b[0]));
  or or_1 (or_1_out, b[0], b[1], b[2], b[3], b[4]);
  Multiplexer #(.width(32)) multiplexer_2 (.in0(a), .in1(multiplexer_1_out), .out(res_low), .sel(or_1_out));

  assign res_high = {32{1'b0}};
endmodule

module SLLL (
  input  [31:0] a,
  input  [31:0] b,
  output [31:0] res_low,
  output [31:0] res_high
);

  wire [31:0] subtractor_1_out;
  wire [63:0] bit_extender_1_out, shifter_1_out, shifter_2_out, shifter_3_out;

  assign bit_extender_1_out = {{32{1'b0}}, a};  // Bit_Extender bit_extender_1
  Subtractor #(.width(32)) subtractor_1 (.a(b), .b(32'h1), .out(subtractor_1_out));  // open: bin, bout
  Shifter #(.width(64)) shifter_1 (.in(bit_extender_1_out), .\dist ({1'b0, b[4:0]}), .out(shifter_1_out));
  Shifter #(.width(64)) shifter_2 (
    .in(bit_extender_1_out), .\dist ({1'b0, subtractor_1_out[4:0]}), .out(shifter_2_out));
  Shifter #(.width(64)) shifter_3 (.in(shifter_2_out), .\dist (6'b000001), .out(shifter_3_out));
  Multiplexer #(.width(64)) multiplexer_1 (
    .in0(shifter_3_out), .in1(shifter_1_out), .out({res_high, res_low}), .sel(b[0]));
endmodule

module ANDD (
  input  [31:0] a,
  input  [31:0] b,
  output [31:0] res_high,
  output [31:0] res_low
);

  assign res_low = a & b;  // AND_Gate and_1, 32 bits wide

  assign res_high = {32{1'b0}};
endmodule

module ORR (
  input  [31:0] a,
  input  [31:0] b,
  output [31:0] res_high,
  output [31:0] res_low
);

  assign res_low = a | b;  // OR_Gate or_1, 32 bits wide

  assign res_high = {32{1'b0}};
endmodule

module XORR (
  input  [31:0] a,
  input  [31:0] b,
  output [31:0] res_high,
  output [31:0] res_low
);

  assign res_low = a ^ b;  // XOR_Gate xor_1, 32 bits wide

  assign res_high = {32{1'b0}};
endmodule

module SRAA (
  input  [31:0] a,
  input  [31:0] b,
  output [31:0] res_high,
  output [31:0] res_low
);

  wire [31:0] and_1_out, bit_extender_1_out, sth1_res_low, sth2_res_low, subtractor_1_out;

  assign and_1_out = b & 32'h1f;  // AND_Gate and_1, 32 bits wide
  assign bit_extender_1_out = {{31{a[31]}}, a[31]};  // Bit_Extender bit_extender_1
  Subtractor #(.width(32)) subtractor_1 (.a(32'h20), .b(and_1_out), .out(subtractor_1_out));  // open: bin, bout
  SRLL sth1 (.a(a), .b(b), .res_low(sth1_res_low));  // open: res_high
  SLLL sth2 (.a(bit_extender_1_out), .b(subtractor_1_out), .res_low(sth2_res_low));  // open: res_high
  assign res_low = sth1_res_low | sth2_res_low;  // OR_Gate or_1, 32 bits wide
  assign res_high = {{31{res_low[31]}}, res_low[31]};  // Bit_Extender bit_extender_2
endmodule

module SRL64 (
  input  [63:0] a,
  input  [31:0] b,
  output [31:0] res_high,
  output [63:0] res_low
);

  wire or_1_out;
  wire [31:0] subtractor_1_out;
  wire [63:0] multiplexer_1_out, shifter_1_out, shifter_2_out, shifter_3_out;

  Subtractor #(.width(32)) subtractor_1 (.a(b), .b(32'h1), .out(subtractor_1_out));  // open: bin, bout
  Shifter #(.shift("lr"), .width(64)) shifter_1 (.in(a), .\dist ({1'b0, b[4:0]}), .out(shifter_1_out));
  Shifter #(.shift("lr"), .width(64)) shifter_2 (.in(a), .\dist ({1'b0, subtractor_1_out[4:0]}), .out(shifter_2_out));
  Shifter #(.shift("lr"), .width(64)) shifter_3 (.in(shifter_2_out), .\dist (6'b000001), .out(shifter_3_out));
  Multiplexer #(.width(64)) multiplexer_1 (
    .in0(shifter_3_out), .in1(shifter_1_out), .out(multiplexer_1_out), .sel(b[0]));
  or or_1 (or_1_out, b[0], b[1], b[2], b[3], b[4]);
  Multiplexer #(.width(64)) multiplexer_2 (.in0(a), .in1(multiplexer_1_out), .out(res_low), .sel(or_1_out));

  assign res_high = {32{1'b0}};
endmodule

module ALU (
  input  [3:0] aluop,
  input  [31:0] b,
  input  [31:0] a,
  input  clk,
  output [31:0] res_high,
  output zero,
  output [31:0] res_low,
  output InstDone
);

  wire comparator_1_eq, comparator_2_eq, comparator_3_eq, multiplexer_3_out, x8_done;
  wire [31:0] adder_1_out, slti1_res_low, x1_res_high, x1_res_low, x2_res_high, x2_res_low, x3_res_high,
       x3_res_low, x4_res_high, x4_res_low, x5_res_high, x5_res_low, x6_res_high, x6_res_low, x7_res_high,
       x7_res_low, x8_quotient, x8_remainder;

  Comparator #(.mode("unsigned"), .width(4)) comparator_1 (
    .a(aluop), .b(4'b0001), .eq(comparator_1_eq));  // open: gt, lt
  ADDD x1 (.S(comparator_1_eq), .b(b), .a(a), .res_low(x1_res_low), .res_high(x1_res_high));
  SLTI slti1 (.a(a), .b(b), .res_low(slti1_res_low));
  ANDD x2 (.a(a), .b(b), .res_high(x2_res_high), .res_low(x2_res_low));
  ORR x3 (.a(a), .b(b), .res_high(x3_res_high), .res_low(x3_res_low));
  XORR x4 (.a(a), .b(b), .res_high(x4_res_high), .res_low(x4_res_low));
  SLLL x5 (.a(a), .b(b), .res_low(x5_res_low), .res_high(x5_res_high));
  SRLL x6 (.a(a), .b(b), .res_high(x6_res_high), .res_low(x6_res_low));
  SRAA x7 (.a(a), .b(b), .res_high(x7_res_high), .res_low(x7_res_low));
  Adder #(.width(32)) adder_1 (.a(a), .b(b), .out(adder_1_out));  // open: cin, cout
  DIV x8 (.divisor(b), .dividend(a), .clk(clk), .remainder(x8_remainder), .quotient(x8_quotient), .done(x8_done));
  Multiplexer #(.select(4), .width(32)) multiplexer_1 (
    .in0(x1_res_high), .in1(x1_res_high), .in3(x8_remainder), .in4(x2_res_high), .in5(x3_res_high),
    .in6(x4_res_high), .in9(x5_res_high), .in10(x6_res_high), .in11(x7_res_high), .out(res_high), .sel(aluop));  // open: in2, in7, in8, in12, in13, in14, in15
  Multiplexer #(.select(4), .width(32)) multiplexer_2 (
    .in0(x1_res_low), .in1(x1_res_low), .in2(slti1_res_low), .in3(x8_quotient), .in4(x2_res_low),
    .in5(x3_res_low), .in6(x4_res_low), .in7(a), .in9(x5_res_low), .in10(x6_res_low), .in11(x7_res_low),
    .in12(adder_1_out), .out(res_low), .sel(aluop));  // open: in8, in13, in14, in15
  Comparator #(.mode("unsigned"), .width(4)) comparator_2 (
    .a(aluop), .b(4'b0011), .eq(comparator_2_eq));  // open: gt, lt
  Multiplexer multiplexer_3 (.in0(1'b1), .in1(x8_done), .out(multiplexer_3_out), .sel(comparator_2_eq));
  Comparator #(.mode("unsigned"), .width(4)) comparator_3 (
    .a(aluop), .b(4'b1110), .eq(comparator_3_eq));  // open: gt, lt
  Multiplexer multiplexer_4 (.in0(multiplexer_3_out), .in1(1'b0), .out(InstDone), .sel(comparator_3_eq));
  Comparator #(.width(32)) comparator_4 (.a({32{1'b0}}), .b(res_low), .eq(zero));  // open: gt, lt
endmodule

module regfile (
  input  clk,
  input  rst,
  input  [31:0] Dwrite,
  input  [4:0] Awrite,
  input  [4:0] Aread0,
  input  [4:0] Aread1,
  output [31:0] Dread0,
  output [31:0] Dread1,
  output [31:0] R1,
  output [31:0] R2,
  output [31:0] R3,
  output [31:0] R4,
  output [31:0] R5,
  output [31:0] R6,
  output [31:0] R7,
  output [31:0] R8,
  output [31:0] R9,
  output [31:0] R10,
  output [31:0] R11,
  output [31:0] R12,
  output [31:0] R13,
  output [31:0] R14,
  output [31:0] R15,
  output [31:0] R16,
  output [31:0] R17,
  output [31:0] R18,
  output [31:0] R19,
  output [31:0] R20,
  output [31:0] R21,
  output [31:0] R22,
  output [31:0] R23,
  output [31:0] R24,
  output [31:0] R25,
  output [31:0] R26,
  output [31:0] R27,
  output [31:0] R28,
  output [31:0] R29,
  output [31:0] R30,
  output [31:0] R31
);

  wire and_1_out, and_2_out, and_3_out, and_4_out, and_5_out, and_6_out, and_7_out, and_8_out, and_9_out,
       and_10_out, and_11_out, and_12_out, and_13_out, and_14_out, and_15_out, and_16_out, and_17_out,
       and_18_out, and_19_out, and_20_out, and_21_out, and_22_out, and_23_out, and_24_out, and_25_out,
       and_26_out, and_27_out, and_28_out, and_29_out, and_30_out, and_31_out, and_32_out, decoder_1_out0,
       decoder_1_out1, decoder_1_out2, decoder_1_out3, decoder_1_out4, decoder_1_out5, decoder_1_out6,
       decoder_1_out7, decoder_2_out0, decoder_2_out1, decoder_2_out2, decoder_2_out3, or_1_out, or_2_out,
       or_3_out, or_4_out, or_5_out, or_6_out, or_7_out, or_8_out, or_9_out, or_10_out, or_11_out, or_12_out,
       or_13_out, or_14_out, or_15_out, or_16_out, or_17_out, or_18_out, or_19_out, or_20_out, or_21_out,
       or_22_out, or_23_out, or_24_out, or_25_out, or_26_out, or_27_out, or_28_out, or_29_out, or_30_out,
       or_31_out, or_32_out, undriven_2, undriven_3, undriven_4, undriven_5;
  wire [31:0] multiplexer_1_out, multiplexer_2_out, multiplexer_3_out, multiplexer_4_out, multiplexer_5_out,
       multiplexer_6_out, multiplexer_7_out, multiplexer_8_out, multiplexer_9_out, undriven;

  Register #(.width(32)) register_1 (.D(undriven), .en(or_1_out), .clk(undriven_2));  // open: Q, clr
  or or_1 (or_1_out, undriven_5, and_1_out);
  and and_1 (and_1_out, undriven_4, undriven_3);
  Decoder #(.select(3)) decoder_1 (
    .out0(decoder_1_out0), .out1(decoder_1_out1), .out2(decoder_1_out2), .out3(decoder_1_out3),
    .out4(decoder_1_out4), .out5(decoder_1_out5), .out6(decoder_1_out6), .out7(decoder_1_out7),
    .sel(Awrite[4:2]));  // open: en
  Decoder #(.select(2)) decoder_2 (
    .out0(decoder_2_out0), .out1(decoder_2_out1), .out2(decoder_2_out2), .out3(decoder_2_out3),
    .sel(Awrite[1:0]));  // open: en
  Multiplexer #(.width(32)) multiplexer_1 (.in0(Dwrite), .in1({32{1'b0}}), .out(multiplexer_1_out), .sel(rst));
  and and_2 (and_2_out, decoder_2_out0, decoder_1_out1);
  and and_3 (and_3_out, decoder_2_out0, decoder_1_out2);
  and and_4 (and_4_out, decoder_2_out0, decoder_1_out3);
  and and_5 (and_5_out, decoder_2_out0, decoder_1_out4);
  and and_6 (and_6_out, decoder_2_out0, decoder_1_out5);
  and and_7 (and_7_out, decoder_2_out0, decoder_1_out6);
  and and_8 (and_8_out, decoder_2_out0, decoder_1_out7);
  Register #(.width(32)) register_2 (.D(multiplexer_1_out), .en(or_2_out), .clk(clk), .Q(R4));  // open: clr
  or or_2 (or_2_out, rst, and_2_out);
  Register #(.width(32)) register_3 (.D(multiplexer_1_out), .en(or_3_out), .clk(clk), .Q(R8));  // open: clr
  or or_3 (or_3_out, rst, and_3_out);
  Register #(.width(32)) register_4 (.D(multiplexer_1_out), .en(or_4_out), .clk(clk), .Q(R12));  // open: clr
  or or_4 (or_4_out, rst, and_4_out);
  Register #(.width(32)) register_5 (.D(multiplexer_1_out), .en(or_5_out), .clk(clk), .Q(R16));  // open: clr
  or or_5 (or_5_out, rst, and_5_out);
  Register #(.width(32)) register_6 (.D(multiplexer_1_out), .en(or_6_out), .clk(clk), .Q(R20));  // open: clr
  or or_6 (or_6_out, rst, and_6_out);
  Register #(.width(32)) register_7 (.D(multiplexer_1_out), .en(or_7_out), .clk(clk), .Q(R24));  // open: clr
  or or_7 (or_7_out, rst, and_7_out);
  Register #(.width(32)) register_8 (.D(multiplexer_1_out), .en(or_8_out), .clk(clk), .Q(R28));  // open: clr
  or or_8 (or_8_out, rst, and_8_out);
  Multiplexer #(.select(3), .width(32)) multiplexer_2 (
    .in0({32{1'b0}}), .in1(R4), .in2(R8), .in3(R12), .in4(R16), .in5(R20), .in6(R24), .in7(R28),
    .out(multiplexer_2_out), .sel(Aread0[4:2]));
  Multiplexer #(.select(3), .width(32)) multiplexer_3 (
    .in0({32{1'b0}}), .in1(R4), .in2(R8), .in3(R12), .in4(R16), .in5(R20), .in6(R24), .in7(R28),
    .out(multiplexer_3_out), .sel(Aread1[4:2]));
  and and_9 (and_9_out, decoder_2_out1, decoder_1_out0);
  and and_10 (and_10_out, decoder_2_out1, decoder_1_out1);
  and and_11 (and_11_out, decoder_2_out1, decoder_1_out2);
  and and_12 (and_12_out, decoder_2_out1, decoder_1_out3);
  and and_13 (and_13_out, decoder_2_out1, decoder_1_out4);
  and and_14 (and_14_out, decoder_2_out1, decoder_1_out5);
  and and_15 (and_15_out, decoder_2_out1, decoder_1_out6);
  and and_16 (and_16_out, decoder_2_out1, decoder_1_out7);
  Register #(.width(32)) register_9 (.D(multiplexer_1_out), .en(or_9_out), .clk(clk), .Q(R1));  // open: clr
  or or_9 (or_9_out, rst, and_9_out);
  Register #(.width(32)) register_10 (.D(multiplexer_1_out), .en(or_10_out), .clk(clk), .Q(R5));  // open: clr
  or or_10 (or_10_out, rst, and_10_out);
  Register #(.width(32)) register_11 (.D(multiplexer_1_out), .en(or_11_out), .clk(clk), .Q(R9));  // open: clr
  or or_11 (or_11_out, rst, and_11_out);
  Register #(.width(32)) register_12 (.D(multiplexer_1_out), .en(or_12_out), .clk(clk), .Q(R13));  // open: clr
  or or_12 (or_12_out, rst, and_12_out);
  Register #(.width(32)) register_13 (.D(multiplexer_1_out), .en(or_13_out), .clk(clk), .Q(R17));  // open: clr
  or or_13 (or_13_out, rst, and_13_out);
  Register #(.width(32)) register_14 (.D(multiplexer_1_out), .en(or_14_out), .clk(clk), .Q(R21));  // open: clr
  or or_14 (or_14_out, rst, and_14_out);
  Register #(.width(32)) register_15 (.D(multiplexer_1_out), .en(or_15_out), .clk(clk), .Q(R25));  // open: clr
  or or_15 (or_15_out, rst, and_15_out);
  Register #(.width(32)) register_16 (.D(multiplexer_1_out), .en(or_16_out), .clk(clk), .Q(R29));  // open: clr
  or or_16 (or_16_out, rst, and_16_out);
  Multiplexer #(.select(3), .width(32)) multiplexer_4 (
    .in0(R1), .in1(R5), .in2(R9), .in3(R13), .in4(R17), .in5(R21), .in6(R25), .in7(R29),
    .out(multiplexer_4_out), .sel(Aread0[4:2]));
  Multiplexer #(.select(3), .width(32)) multiplexer_5 (
    .in0(R1), .in1(R5), .in2(R9), .in3(R13), .in4(R17), .in5(R21), .in6(R25), .in7(R29),
    .out(multiplexer_5_out), .sel(Aread1[4:2]));
  Register #(.width(32)) register_17 (.D(multiplexer_1_out), .en(or_17_out), .clk(clk), .Q(R2));  // open: clr
  or or_17 (or_17_out, rst, and_17_out);
  and and_17 (and_17_out, decoder_2_out2, decoder_1_out0);
  Register #(.width(32)) register_18 (.D(multiplexer_1_out), .en(or_18_out), .clk(clk), .Q(R6));  // open: clr
  or or_18 (or_18_out, rst, and_18_out);
  and and_18 (and_18_out, decoder_2_out2, decoder_1_out1);
  Register #(.width(32)) register_19 (.D(multiplexer_1_out), .en(or_19_out), .clk(clk), .Q(R10));  // open: clr
  or or_19 (or_19_out, rst, and_19_out);
  and and_19 (and_19_out, decoder_2_out2, decoder_1_out2);
  Register #(.width(32)) register_20 (.D(multiplexer_1_out), .en(or_20_out), .clk(clk), .Q(R14));  // open: clr
  or or_20 (or_20_out, rst, and_20_out);
  and and_20 (and_20_out, decoder_2_out2, decoder_1_out3);
  Register #(.width(32)) register_21 (.D(multiplexer_1_out), .en(or_21_out), .clk(clk), .Q(R18));  // open: clr
  or or_21 (or_21_out, rst, and_21_out);
  and and_21 (and_21_out, decoder_2_out2, decoder_1_out4);
  Register #(.width(32)) register_22 (.D(multiplexer_1_out), .en(or_22_out), .clk(clk), .Q(R22));  // open: clr
  or or_22 (or_22_out, rst, and_22_out);
  and and_22 (and_22_out, decoder_2_out2, decoder_1_out5);
  Register #(.width(32)) register_23 (.D(multiplexer_1_out), .en(or_23_out), .clk(clk), .Q(R26));  // open: clr
  or or_23 (or_23_out, rst, and_23_out);
  and and_23 (and_23_out, decoder_2_out2, decoder_1_out6);
  Register #(.width(32)) register_24 (.D(multiplexer_1_out), .en(or_24_out), .clk(clk), .Q(R30));  // open: clr
  or or_24 (or_24_out, rst, and_24_out);
  and and_24 (and_24_out, decoder_2_out2, decoder_1_out7);
  Multiplexer #(.select(3), .width(32)) multiplexer_6 (
    .in0(R2), .in1(R6), .in2(R10), .in3(R14), .in4(R18), .in5(R22), .in6(R26), .in7(R30),
    .out(multiplexer_6_out), .sel(Aread0[4:2]));
  Multiplexer #(.select(3), .width(32)) multiplexer_7 (
    .in0(R2), .in1(R6), .in2(R10), .in3(R14), .in4(R18), .in5(R22), .in6(R26), .in7(R30),
    .out(multiplexer_7_out), .sel(Aread1[4:2]));
  Register #(.width(32)) register_25 (.D(multiplexer_1_out), .en(or_25_out), .clk(clk), .Q(R3));  // open: clr
  or or_25 (or_25_out, rst, and_25_out);
  and and_25 (and_25_out, decoder_2_out3, decoder_1_out0);
  Register #(.width(32)) register_26 (.D(multiplexer_1_out), .en(or_26_out), .clk(clk), .Q(R7));  // open: clr
  or or_26 (or_26_out, rst, and_26_out);
  and and_26 (and_26_out, decoder_2_out3, decoder_1_out1);
  Register #(.width(32)) register_27 (.D(multiplexer_1_out), .en(or_27_out), .clk(clk), .Q(R11));  // open: clr
  or or_27 (or_27_out, rst, and_27_out);
  and and_27 (and_27_out, decoder_2_out3, decoder_1_out2);
  Register #(.width(32)) register_28 (.D(multiplexer_1_out), .en(or_28_out), .clk(clk), .Q(R15));  // open: clr
  or or_28 (or_28_out, rst, and_28_out);
  and and_28 (and_28_out, decoder_2_out3, decoder_1_out3);
  Register #(.width(32)) register_29 (.D(multiplexer_1_out), .en(or_29_out), .clk(clk), .Q(R19));  // open: clr
  or or_29 (or_29_out, rst, and_29_out);
  and and_29 (and_29_out, decoder_2_out3, decoder_1_out4);
  Register #(.width(32)) register_30 (.D(multiplexer_1_out), .en(or_30_out), .clk(clk), .Q(R23));  // open: clr
  or or_30 (or_30_out, rst, and_30_out);
  and and_30 (and_30_out, decoder_2_out3, decoder_1_out5);
  Register #(.width(32)) register_31 (.D(multiplexer_1_out), .en(or_31_out), .clk(clk), .Q(R27));  // open: clr
  or or_31 (or_31_out, rst, and_31_out);
  and and_31 (and_31_out, decoder_2_out3, decoder_1_out6);
  Register #(.width(32)) register_32 (.D(multiplexer_1_out), .en(or_32_out), .clk(clk), .Q(R31));  // open: clr
  or or_32 (or_32_out, rst, and_32_out);
  and and_32 (and_32_out, decoder_2_out3, decoder_1_out7);
  Multiplexer #(.select(3), .width(32)) multiplexer_8 (
    .in0(R3), .in1(R7), .in2(R11), .in3(R15), .in4(R19), .in5(R23), .in6(R27), .in7(R31),
    .out(multiplexer_8_out), .sel(Aread0[4:2]));
  Multiplexer #(.select(3), .width(32)) multiplexer_9 (
    .in0(R3), .in1(R7), .in2(R11), .in3(R15), .in4(R19), .in5(R23), .in6(R27), .in7(R31),
    .out(multiplexer_9_out), .sel(Aread1[4:2]));
  Multiplexer #(.select(2), .width(32)) multiplexer_10 (
    .in0(multiplexer_2_out), .in1(multiplexer_4_out), .in2(multiplexer_6_out), .in3(multiplexer_8_out),
    .out(Dread0), .sel(Aread0[1:0]));
  Multiplexer #(.select(2), .width(32)) multiplexer_11 (
    .in0(multiplexer_3_out), .in1(multiplexer_5_out), .in2(multiplexer_7_out), .in3(multiplexer_9_out),
    .out(Dread1), .sel(Aread1[1:0]));

  // Notes on the sheet:
  //   Field Template
endmodule

module InstructionDecode (
  input  [31:0] Instruction,
  output [5:0] opCode,
  output [4:0] rt,
  output [4:0] rs,
  output [31:0] imm,
  output [4:0] rd,
  output [31:0] shmt,
  output [5:0] func
);

  assign imm = {{16{Instruction[15]}}, Instruction[15:0]};  // Bit_Extender bit_extender_1
  assign shmt = {{27{1'b0}}, Instruction[10:6]};  // Bit_Extender bit_extender_2

  assign func = Instruction[5:0];
  assign opCode = Instruction[31:26];
  assign rd = Instruction[15:11];
  assign rs = Instruction[20:16];
  assign rt = Instruction[25:21];
endmodule

module ControlUnit (
  input  [5:0] func,
  input  main_clock,
  input  inst,
  input  inst2,
  input  [5:0] opCode,
  output [3:0] ALUop,
  output nop,
  output regDst,
  output ALUsrc,
  output shmt,
  output j,
  output regWrite,
  output memToReg,
  output memWrite,
  output branch,
  output divv,
  output mohi,
  output FregWrite,
  output TOCOP,
  output FROMCOP,
  output [2:0] FALUop
);

  wire add, addi, and_1_out, and_2_out, and_3_out, and_6_out, andd, FABS, FADD, FMULT, FregWrite_t, FSIN,
       FSLT, FSUB, jr, mfhi, mflo, multiplexer_10_out, multiplexer_17_out, multiplexer_30_out,
       multiplexer_31_out, not_1_out, not_2_out, orr, register_1_q, register_2_q, slll, slti, sraa, srll,
       sub, xorr;
  wire [2:0] multiplexer_1_out, multiplexer_2_out, multiplexer_5_out, multiplexer_6_out, multiplexer_11_out,
       multiplexer_12_out;
  wire [3:0] multiplexer_3_out, multiplexer_4_out, multiplexer_7_out, multiplexer_8_out, multiplexer_9_out,
       multiplexer_14_out, multiplexer_15_out, multiplexer_16_out, multiplexer_18_out, multiplexer_19_out,
       multiplexer_20_out, multiplexer_21_out, multiplexer_22_out, multiplexer_23_out, multiplexer_24_out,
       multiplexer_25_out, multiplexer_26_out, multiplexer_27_out, multiplexer_28_out;

  Comparator #(.mode("unsigned"), .width(6)) comparator_1 (.a(6'b100000), .b(func), .eq(add));  // open: gt, lt
  Comparator #(.mode("unsigned"), .width(6)) comparator_2 (.a(6'b100010), .b(func), .eq(sub));  // open: gt, lt
  Comparator #(.mode("unsigned"), .width(6)) comparator_3 (.a(6'b100100), .b(func), .eq(andd));  // open: gt, lt
  Comparator #(.mode("unsigned"), .width(6)) comparator_4 (.a(6'b100101), .b(func), .eq(orr));  // open: gt, lt
  Comparator #(.mode("unsigned"), .width(6)) comparator_5 (.a(6'b100110), .b(func), .eq(xorr));  // open: gt, lt
  Comparator #(.mode("unsigned"), .width(6)) comparator_6 (.a(6'b000100), .b(func), .eq(slll));  // open: gt, lt
  Comparator #(.mode("unsigned"), .width(6)) comparator_7 (.a(6'b000110), .b(func), .eq(srll));  // open: gt, lt
  Comparator #(.mode("unsigned"), .width(6)) comparator_8 (.a(6'b000111), .b(func), .eq(sraa));  // open: gt, lt
  Comparator #(.mode("unsigned"), .width(6)) comparator_9 (.a(6'b011010), .b(func), .eq(divv));  // open: gt, lt
  Comparator #(.mode("unsigned"), .width(6)) comparator_10 (.a(6'b010000), .b(func), .eq(mfhi));  // open: gt, lt
  Comparator #(.mode("unsigned"), .width(6)) comparator_11 (.a({6{1'b0}}), .b(func), .eq(shmt));  // open: gt, lt
  Comparator #(.mode("unsigned"), .width(6)) comparator_12 (.a(6'b001000), .b(func), .eq(jr));  // open: gt, lt
  Comparator #(.mode("unsigned"), .width(6)) comparator_13 (.a(6'b010010), .b(func), .eq(mflo));  // open: gt, lt
  Comparator #(.mode("unsigned"), .width(6)) comparator_14 (.a(6'b000001), .b(func), .eq(FSIN));  // open: gt, lt
  Comparator #(.mode("unsigned"), .width(6)) comparator_15 (.a(6'b010011), .b(func), .eq(FADD));  // open: gt, lt
  Comparator #(.mode("unsigned"), .width(6)) comparator_16 (.a(6'b010100), .b(func), .eq(FSUB));  // open: gt, lt
  Comparator #(.mode("unsigned"), .width(6)) comparator_17 (.a(6'b010101), .b(func), .eq(FMULT));  // open: gt, lt
  Comparator #(.mode("unsigned"), .width(6)) comparator_18 (.a(6'b010110), .b(func), .eq(FABS));  // open: gt, lt
  Comparator #(.mode("unsigned"), .width(6)) comparator_19 (.a(6'b010111), .b(func), .eq(FSLT));  // open: gt, lt
  Comparator #(.mode("unsigned"), .width(6)) comparator_20 (.a(6'b011000), .b(func), .eq(TOCOP));  // open: gt, lt
  Comparator #(.mode("unsigned"), .width(6)) comparator_21 (.a(6'b011001), .b(func), .eq(FROMCOP));  // open: gt, lt
  Multiplexer #(.width(3)) multiplexer_1 (.in0(3'b111), .in1(3'b101), .out(multiplexer_1_out), .sel(FSIN));
  Multiplexer #(.width(3)) multiplexer_2 (.in0(multiplexer_1_out), .in1(3'b100), .out(multiplexer_2_out), .sel(FSLT));
  Multiplexer #(.width(4)) multiplexer_3 (.in0(4'b1111), .in1(4'b0000), .out(multiplexer_3_out), .sel(add));
  Multiplexer #(.width(4)) multiplexer_4 (.in0(multiplexer_3_out), .in1(4'b0001), .out(multiplexer_4_out), .sel(sub));
  Register #(.width(1)) register_1 (.D(inst), .clk(main_clock), .Q(register_1_q));  // open: en, clr
  or or_1 (FregWrite_t, FSIN, FADD, FSUB, FMULT, FABS, FSLT, TOCOP);
  Multiplexer #(.width(3)) multiplexer_5 (.in0(multiplexer_2_out), .in1(3'b011), .out(multiplexer_5_out), .sel(FABS));
  Multiplexer #(.width(3)) multiplexer_6 (.in0(multiplexer_5_out), .in1(3'b010), .out(multiplexer_6_out), .sel(FMULT));
  Multiplexer #(.width(4)) multiplexer_7 (.in0(multiplexer_4_out), .in1(4'b0100), .out(multiplexer_7_out), .sel(andd));
  Multiplexer #(.width(4)) multiplexer_8 (.in0(multiplexer_7_out), .in1(4'b0101), .out(multiplexer_8_out), .sel(orr));
  Multiplexer #(.width(4)) multiplexer_9 (.in0(multiplexer_8_out), .in1(4'b0110), .out(multiplexer_9_out), .sel(xorr));
  and and_1 (and_1_out, inst, ~register_1_q);  // AND_Gate
  not not_1 (not_1_out, inst);
  Multiplexer multiplexer_10 (.in0(not_1_out), .in1(1'b1), .out(multiplexer_10_out), .sel(and_1_out));
  and and_2 (and_2_out, ~FregWrite_t, regDst);  // AND_Gate
  and and_3 (and_3_out, FROMCOP, regDst);
  and and_4 (mohi, regDst, mfhi);
  and and_5 (FregWrite, FregWrite_t, regDst);
  Multiplexer #(.width(3)) multiplexer_11 (.in0(multiplexer_6_out), .in1(3'b001), .out(multiplexer_11_out), .sel(FSUB));
  Multiplexer #(.width(3)) multiplexer_12 (
    .in0(multiplexer_11_out), .in1(3'b000), .out(multiplexer_12_out), .sel(FADD));
  Multiplexer #(.width(3)) multiplexer_13 (.in0(3'b111), .in1(multiplexer_12_out), .out(FALUop), .sel(regDst));
  Multiplexer #(.width(4)) multiplexer_14 (
    .in0(multiplexer_9_out), .in1(4'b1001), .out(multiplexer_14_out), .sel(slll));
  Multiplexer #(.width(4)) multiplexer_15 (
    .in0(multiplexer_14_out), .in1(4'b1010), .out(multiplexer_15_out), .sel(srll));
  Multiplexer #(.width(4)) multiplexer_16 (
    .in0(multiplexer_15_out), .in1(4'b1011), .out(multiplexer_16_out), .sel(sraa));
  Multiplexer multiplexer_17 (.in0(1'b0), .in1(multiplexer_10_out), .out(multiplexer_17_out), .sel(divv));
  or or_2 (regWrite, and_2_out, and_3_out, addi, slti, memToReg);
  Multiplexer #(.width(4)) multiplexer_18 (
    .in0(multiplexer_16_out), .in1(4'b0011), .out(multiplexer_18_out), .sel(divv));
  Multiplexer #(.width(4)) multiplexer_19 (
    .in0(multiplexer_18_out), .in1(4'b1111), .out(multiplexer_19_out), .sel(mfhi));
  Comparator #(.mode("unsigned"), .width(6)) comparator_22 (.a({6{1'b0}}), .b(opCode), .eq(regDst));  // open: gt, lt
  Comparator #(.mode("unsigned"), .width(6)) comparator_23 (.a(6'b001000), .b(opCode), .eq(addi));  // open: gt, lt
  Comparator #(.mode("unsigned"), .width(6)) comparator_24 (.a(6'b101011), .b(opCode), .eq(memWrite));  // open: gt, lt
  Comparator #(.mode("unsigned"), .width(6)) comparator_25 (.a(6'b100011), .b(opCode), .eq(memToReg));  // open: gt, lt
  Comparator #(.mode("unsigned"), .width(6)) comparator_26 (.a(6'b000101), .b(opCode), .eq(branch));  // open: gt, lt
  Comparator #(.mode("unsigned"), .width(6)) comparator_27 (.a(6'b001010), .b(opCode), .eq(slti));  // open: gt, lt
  Comparator #(.mode("unsigned"), .width(6)) comparator_28 (.a(6'b000010), .b(opCode), .eq(j));  // open: gt, lt
  Multiplexer #(.width(4)) multiplexer_20 (
    .in0(multiplexer_19_out), .in1(4'b1001), .out(multiplexer_20_out), .sel(shmt));
  Multiplexer #(.width(4)) multiplexer_21 (.in0(multiplexer_20_out), .in1(4'b1111), .out(multiplexer_21_out), .sel(jr));
  Multiplexer #(.width(4)) multiplexer_22 (
    .in0(multiplexer_21_out), .in1(4'b1111), .out(multiplexer_22_out), .sel(mflo));
  Multiplexer #(.width(4)) multiplexer_23 (
    .in0(multiplexer_22_out), .in1(4'b1100), .out(multiplexer_23_out), .sel(addi));
  Multiplexer #(.width(4)) multiplexer_24 (
    .in0(multiplexer_23_out), .in1(4'b0000), .out(multiplexer_24_out), .sel(memWrite));
  Multiplexer #(.width(4)) multiplexer_25 (
    .in0(multiplexer_24_out), .in1(4'b0000), .out(multiplexer_25_out), .sel(memToReg));
  Multiplexer #(.width(4)) multiplexer_26 (
    .in0(multiplexer_25_out), .in1(4'b0111), .out(multiplexer_26_out), .sel(branch));
  Multiplexer #(.width(4)) multiplexer_27 (
    .in0(multiplexer_26_out), .in1(4'b0010), .out(multiplexer_27_out), .sel(slti));
  or or_3 (ALUsrc, addi, memWrite, memToReg, branch, slti);
  Multiplexer #(.width(4)) multiplexer_28 (.in0(multiplexer_27_out), .in1(4'b1111), .out(multiplexer_28_out), .sel(j));
  Multiplexer #(.width(4)) multiplexer_29 (.in0(multiplexer_28_out), .in1(4'b1110), .out(ALUop), .sel(FSIN));
  Register #(.width(1)) register_2 (.D(inst2), .clk(main_clock), .Q(register_2_q));  // open: en, clr
  and and_6 (and_6_out, inst2, ~register_2_q);  // AND_Gate
  not not_2 (not_2_out, inst2);
  Multiplexer multiplexer_30 (.in0(not_2_out), .in1(1'b1), .out(multiplexer_30_out), .sel(and_6_out));
  Multiplexer multiplexer_31 (.in0(1'b0), .in1(multiplexer_30_out), .out(multiplexer_31_out), .sel(FSIN));
  or or_4 (nop, multiplexer_31_out, multiplexer_17_out);

  // Other names for the same wires on the sheet: bne = branch; div = divv; lw = memToReg; Rtype = regDst; sll2 = shmt;
  //   sw = memWrite
endmodule

module DIV (
  input  [31:0] divisor,
  input  [31:0] dividend,
  input  clk,
  output [31:0] remainder,
  output [31:0] quotient,
  output done
);

  wire and_1_out, comparator_1_eq, comparator_2_eq, comparator_3_eq, comparator_3_gt, comparator_4_eq,
       nand_1_out, not_1_out, not_2_out, or_1_out, or_3_out, or_4_out, or_5_out;
  wire [6:0] counter_1_q;
  wire [31:0] b_q, multiplexer_1_out, multiplexer_2_out, multiplexer_3_out, multiplexer_4_out,
       multiplexer_5_out, multiplexer_6_out, or_2_out, register_1_q, register_2_q, subtractor_1_out;

  Register #(.width(32)) register_1 (.D(divisor), .en(1'b1), .clk(clk), .Q(register_1_q));  // open: clr
  Register #(.width(32)) register_2 (.D(dividend), .en(1'b1), .clk(clk), .Q(register_2_q));  // open: clr
  Comparator #(.width(32)) comparator_1 (.a(register_1_q), .b(divisor), .eq(comparator_1_eq));  // open: gt, lt
  nand nand_1 (nand_1_out, comparator_2_eq, comparator_1_eq);
  Comparator #(.width(32)) comparator_2 (.a(register_2_q), .b(dividend), .eq(comparator_2_eq));  // open: gt, lt
  Register #(.width(32)) b (.D(divisor), .en(nand_1_out), .clk(clk), .Q(b_q));  // open: clr
  not not_1 (not_1_out, or_1_out);
  or or_1 (or_1_out, counter_1_q[0], counter_1_q[1], counter_1_q[2], counter_1_q[3], counter_1_q[4], counter_1_q[5], counter_1_q[6]);
  assign or_2_out = quotient | 32'h1;  // OR_Gate or_2, 32 bits wide
  Counter #(.max('h7f), .width(7)) counter_1 (
    .clr(nand_1_out), .load(not_1_out), .up(1'b0), .clk(clk), .D(7'b1000000), .Q(counter_1_q));  // open: count, carry
  Multiplexer #(.width(32)) multiplexer_1 (
    .in0(remainder), .in1(subtractor_1_out), .out(multiplexer_1_out), .sel(or_3_out));
  Subtractor #(.width(32)) subtractor_1 (.a(remainder), .b(b_q), .out(subtractor_1_out));  // open: bin, bout
  Comparator #(.mode("unsigned"), .width(32)) comparator_3 (
    .a(remainder), .b(b_q), .gt(comparator_3_gt), .eq(comparator_3_eq));  // open: lt
  or or_3 (or_3_out, comparator_3_gt, comparator_3_eq);
  Multiplexer #(.width(32)) multiplexer_2 (.in0(quotient), .in1(or_2_out), .out(multiplexer_2_out), .sel(or_3_out));
  Multiplexer #(.width(32)) multiplexer_3 (
    .in0(multiplexer_2_out), .in1(dividend), .out(multiplexer_3_out), .sel(not_1_out));
  or or_4 (or_4_out, not_1_out, counter_1_q[0]);
  Multiplexer #(.width(32)) multiplexer_4 (
    .in0({remainder[30:0], quotient[31]}), .in1(multiplexer_5_out), .out(multiplexer_4_out), .sel(or_4_out));
  Multiplexer #(.width(32)) multiplexer_5 (
    .in0(multiplexer_1_out), .in1({32{1'b0}}), .out(multiplexer_5_out), .sel(not_1_out));
  Multiplexer #(.width(32)) multiplexer_6 (
    .in0({quotient[30:0], 1'b0}), .in1(multiplexer_3_out), .out(multiplexer_6_out), .sel(or_4_out));
  and and_1 (and_1_out, clk, not_2_out);
  Register #(.width(32)) a (.D(multiplexer_4_out), .en(1'b1), .clk(and_1_out), .Q(remainder));  // open: clr
  Register #(.width(32)) q (.D(multiplexer_6_out), .en(1'b1), .clk(and_1_out), .Q(quotient));  // open: clr
  not not_2 (not_2_out, done);
  Comparator #(.width(7)) comparator_4 (.a(counter_1_q), .b(7'b0000001), .eq(comparator_4_eq));  // open: gt, lt
  D_Flip_Flop d_ff_1 (.D(or_5_out), .clk(clk), .Q(done), .reset(nand_1_out));  // open: Qn, preset
  or or_5 (or_5_out, done, comparator_4_eq);
endmodule

module SLTI (
  input  [31:0] a,
  input  [31:0] b,
  output [31:0] res_low
);

  wire comparator_1_lt;

  Comparator #(.width(32)) comparator_1 (.a(a), .b(b), .lt(comparator_1_lt));  // open: gt, eq
  assign res_low = {{31{1'b0}}, comparator_1_lt};  // Bit_Extender bit_extender_1
endmodule

module FP_ALU (
  input  [31:0] a,
  input  [31:0] b,
  input  [2:0] aluop,
  input  clk,
  output [31:0] res,
  output Done
);

  wire fsinH_done;
  wire [31:0] fabsH_res, faddH_res, fmultH_res, fsinH_res, fsltH_res, fsubH_res;

  fadd faddH (.a(a), .b(b), .res(faddH_res));  // open: INFINITY_PIN, NAN_PIN
  fsub fsubH (.a(a), .b(b), .res(fsubH_res));  // open: INFINITY_PIN, NAN_PIN
  fmult fmultH (.b(a), .a(b), .res(fmultH_res));
  fabs fabsH (.a(a), .res(fabsH_res));
  fslt fsltH (.a(a), .b(b), .res(fsltH_res));  // open: INFINITY_PIN, NAN_PIN
  fsin fsinH (.count(a), .clk(clk), .x(b), .res(fsinH_res), .Done(fsinH_done));
  Multiplexer #(.select(3), .width(32)) multiplexer_1 (
    .in0(faddH_res), .in1(fsubH_res), .in2(fmultH_res), .in3(fabsH_res), .in4(fsltH_res), .in5(fsinH_res),
    .out(res), .sel(aluop));  // open: in6, in7
  Multiplexer #(.select(3)) multiplexer_2 (
    .in0(1'b1), .in1(1'b1), .in2(1'b1), .in3(1'b1), .in4(1'b1), .in5(fsinH_done), .in6(1'b1), .in7(1'b1),
    .out(Done), .sel(aluop));
endmodule

module fadd (
  input  [31:0] a,
  input  [31:0] b,
  output INFINITY_PIN,
  output NAN_PIN,
  output [31:0] res
);

  wire adder_3_cout, adder_5_cout, and_1_out, and_2_out, and_3_out, and_4_out, and_5_out, and_6_out,
       and_7_out, and_8_out, and_9_out, c_out, comparator_1_eq, comparator_2_eq, comparator_3_eq,
       comparator_4_eq, comparator_5_eq, comparator_6_eq, comparator_7_eq, comparator_8_eq, comparator_9_eq,
       comparator_10_eq, comparator_11_eq, comparator_12_eq, comparator_12_gt, comparator_13_eq,
       comparator_13_gt, comparator_13_lt, comparator_14_lt, comparator_15_lt, g1, g2, INFINITY_sign,
       NAN_sign, not_1_out, not_2_out, not_3_out, or_3_out, plus_one_exponent_1, plus_one_exponent_2,
       plus_one_exponent_3, s1, s2, subnormal_a, subnormal_b, v26_s, v29_s;
  wire [1:0] adder_2_out, bit_extender_3_out;
  wire [7:0] adder_7_out, exponent_result, multiplexer_9_out, subtractor_1_out, subtractor_2_out;
  wire [8:0] subtractor_7_out, subtractor_8_out;
  wire [22:0] adder_8_out, adder_9_out, fraction_result, fraction_result_1, fraction_result_2,
       fraction_result_3, fraction_without_normalize_1, fraction_without_normalize_2,
       fraction_without_normalize_3, multiplexer_8_out, multiplexer_10_out, multiplexer_19_out,
       multiplexer_20_out, shifter_1_out, shifter_2_out;
  wire [31:0] bit_extender_1_out, bit_extender_2_out, bit_extender_4_out, bit_extender_5_out, minus_result,
       multiplexer_7_out, multiplexer_12_out, sh1, sh2, shifted1, shifted2, subtractor_3_out,
       subtractor_4_out, subtractor_5_out, subtractor_6_out, v25_res_low, v28_res_low;
  wire [63:0] bit_extender_6_out, bit_extender_7_out;

  Subtractor subtractor_1 (.a(b[30:23]), .b(a[30:23]), .out(subtractor_1_out));  // open: bin, bout
  Subtractor subtractor_2 (.a(a[30:23]), .b(b[30:23]), .out(subtractor_2_out));  // open: bin, bout
  assign bit_extender_1_out = {{24{1'b0}}, subtractor_1_out};  // Bit_Extender bit_extender_1
  Subtractor #(.width(32)) subtractor_3 (.a(bit_extender_1_out), .b(32'h1), .out(subtractor_3_out));  // open: bin, bout
  assign bit_extender_2_out = {{24{1'b0}}, subtractor_2_out};  // Bit_Extender bit_extender_2
  Subtractor #(.width(32)) subtractor_4 (.a(bit_extender_2_out), .b(32'h1), .out(subtractor_4_out));  // open: bin, bout
  Adder #(.width(23)) adder_1 (
    .a(b[22:0]), .b(a[22:0]), .out(fraction_without_normalize_3), .cout(c_out));  // open: cin
  assign bit_extender_3_out = {{1{1'b0}}, c_out};  // Bit_Extender bit_extender_3
  Comparator #(.width(23)) comparator_1 (.a(b[22:0]), .b({23{1'b0}}), .eq(comparator_1_eq));  // open: gt, lt
  Comparator #(.width(23)) comparator_2 (.a(b[22:0]), .b({23{1'b0}}), .eq(comparator_2_eq));  // open: gt, lt
  assign bit_extender_4_out = {{8{1'b0}}, {subnormal_a, a[22:0]}};  // Bit_Extender bit_extender_4
  Multiplexer #(.width(32)) multiplexer_1 (
    .in0(subtractor_3_out), .in1(bit_extender_1_out), .out(sh1), .sel(subnormal_a));
  assign bit_extender_5_out = {{8{1'b0}}, {subnormal_b, b[22:0]}};  // Bit_Extender bit_extender_5
  Multiplexer #(.width(32)) multiplexer_2 (
    .in0(subtractor_4_out), .in1(bit_extender_2_out), .out(sh2), .sel(subnormal_b));
  Adder #(.width(2)) adder_2 (.a(bit_extender_3_out), .b(2'b10), .out(adder_2_out));  // open: cin, cout
  Comparator comparator_3 (.a(a[30:23]), .b({8{1'b1}}), .eq(comparator_3_eq));  // open: gt, lt
  not not_1 (not_1_out, comparator_4_eq);
  Comparator #(.width(23)) comparator_4 (.a(a[22:0]), .b({23{1'b0}}), .eq(comparator_4_eq));  // open: gt, lt
  Comparator comparator_5 (.a(b[30:23]), .b({8{1'b1}}), .eq(comparator_5_eq));  // open: gt, lt
  not not_2 (not_2_out, comparator_1_eq);
  Comparator comparator_6 (.a(a[30:23]), .b({8{1'b1}}), .eq(comparator_6_eq));  // open: gt, lt
  Comparator #(.width(23)) comparator_7 (.a(a[22:0]), .b({23{1'b0}}), .eq(comparator_7_eq));  // open: gt, lt
  Comparator comparator_8 (.a(b[30:23]), .b({8{1'b1}}), .eq(comparator_8_eq));  // open: gt, lt
  Comparator comparator_9 (.a(a[30:23]), .b({8{1'b0}}), .eq(comparator_9_eq));  // open: gt, lt
  Comparator comparator_10 (.a(b[30:23]), .b({8{1'b0}}), .eq(comparator_10_eq));  // open: gt, lt
  and and_1 (and_1_out, comparator_5_eq, not_2_out);
  and and_2 (and_2_out, comparator_8_eq, comparator_2_eq);
  Multiplexer multiplexer_3 (.in0(1'b1), .in1(1'b0), .out(subnormal_b), .sel(comparator_10_eq));
  and and_3 (and_3_out, comparator_3_eq, not_1_out);
  and and_4 (and_4_out, comparator_6_eq, comparator_7_eq);
  Multiplexer multiplexer_4 (.in0(1'b1), .in1(1'b0), .out(subnormal_a), .sel(comparator_9_eq));
  SRL_fadd v24 (.a(bit_extender_4_out), .b(sh1), .res_low(shifted1));  // open: one_signal
  SLLL v25 (.a(shifted1), .b(sh1), .res_low(v25_res_low));  // open: res_high
  SRL_fadd v27 (.a(bit_extender_5_out), .b(sh2), .res_low(shifted2));  // open: one_signal
  Multiplexer multiplexer_5 (.in0(b[31]), .in1(a[31]), .out(NAN_sign), .sel(and_3_out));
  or or_1 (NAN_PIN, and_3_out, and_1_out);
  Multiplexer multiplexer_6 (.in0(b[31]), .in1(a[31]), .out(INFINITY_sign), .sel(and_4_out));
  or or_2 (INFINITY_PIN, and_4_out, and_2_out);
  Comparator #(.width(1)) comparator_11 (.a(a[31]), .b(b[31]), .eq(comparator_11_eq));  // open: gt, lt
  SLLL v28 (.a(shifted2), .b(sh2), .res_low(v28_res_low));  // open: res_high
  Comparator #(.width(9)) comparator_12 (
    .a({1'b0, a[30:23]}), .b({1'b0, b[30:23]}), .gt(comparator_12_gt), .eq(comparator_12_eq));  // open: lt
  Multiplexer #(.width(32)) multiplexer_7 (
    .in0({a[31], exponent_result, fraction_result}), .in1(minus_result), .out(multiplexer_7_out),
    .sel(not_3_out));
  not not_3 (not_3_out, comparator_11_eq);
  assign bit_extender_6_out = {{32{1'b0}}, subtractor_5_out};  // Bit_Extender bit_extender_6
  Subtractor #(.width(32)) subtractor_5 (
    .a(bit_extender_4_out), .b(v25_res_low), .out(subtractor_5_out));  // open: bin, bout
  Subtractor #(.width(32)) subtractor_6 (
    .a(bit_extender_5_out), .b(v28_res_low), .out(subtractor_6_out));  // open: bin, bout
  Comparator #(.width(9)) comparator_13 (
    .a({1'b0, a[30:23]}), .b({1'b0, b[30:23]}), .gt(comparator_13_gt), .eq(comparator_13_eq),
    .lt(comparator_13_lt));
  Adder #(.width(23)) adder_3 (
    .a(shifted1[22:0]), .b(b[22:0]), .out(fraction_without_normalize_1), .cout(adder_3_cout));  // open: cin
  Adder #(.width(1)) adder_4 (.a(adder_3_cout), .b(subnormal_b), .cout(plus_one_exponent_1));  // open: out, cin
  Adder #(.width(23)) adder_5 (
    .a(shifted2[22:0]), .b(a[22:0]), .out(fraction_without_normalize_2), .cout(adder_5_cout));  // open: cin
  Adder #(.width(1)) adder_6 (.a(adder_5_cout), .b(subnormal_a), .cout(plus_one_exponent_2));  // open: out, cin
  Multiplexer #(.width(23)) multiplexer_8 (
    .in0(fraction_result_1), .in1(fraction_result_2), .out(multiplexer_8_out), .sel(comparator_12_gt));
  Multiplexer #(.width(8)) multiplexer_9 (
    .in0(b[30:23]), .in1(a[30:23]), .out(multiplexer_9_out), .sel(comparator_13_gt));
  add_find_bit_1 v26 (.number(bit_extender_6_out), .shift(sh1[5:0]), .sticky(g1), .s(v26_s));
  assign bit_extender_7_out = {{32{1'b0}}, subtractor_6_out};  // Bit_Extender bit_extender_7
  Multiplexer #(.width(23)) multiplexer_10 (
    .in0(fraction_without_normalize_3), .in1({adder_2_out[0], fraction_without_normalize_3[22:1]}),
    .out(multiplexer_10_out), .sel(subnormal_b));
  Multiplexer #(.width(23)) multiplexer_11 (
    .in0(multiplexer_8_out), .in1(fraction_result_3), .out(fraction_result), .sel(comparator_12_eq));
  Multiplexer #(.width(32)) multiplexer_12 (
    .in0(multiplexer_7_out), .in1({INFINITY_sign, 31'h7f800000}), .out(multiplexer_12_out), .sel(INFINITY_PIN));
  add_find_bit_1 v29 (.number(bit_extender_7_out), .shift(sh2[5:0]), .sticky(g2), .s(v29_s));
  Adder adder_7 (.a(multiplexer_9_out), .b(8'h1), .out(adder_7_out));  // open: cin, cout
  fMinnus v23 (.a(a), .b(b), .res(minus_result));
  and and_5 (and_5_out, comparator_13_gt, plus_one_exponent_1);
  and and_6 (and_6_out, comparator_13_lt, plus_one_exponent_2);
  and and_7 (and_7_out, comparator_13_eq, plus_one_exponent_3);
  Multiplexer #(.width(32)) multiplexer_13 (
    .in0(multiplexer_12_out), .in1({NAN_sign, 31'h7fc00000}), .out(res), .sel(NAN_PIN));
  Multiplexer multiplexer_14 (.in0(c_out), .in1(adder_2_out[1]), .out(plus_one_exponent_3), .sel(subnormal_b));
  Multiplexer #(.width(8)) multiplexer_15 (
    .in0(multiplexer_9_out), .in1(adder_7_out), .out(exponent_result), .sel(or_3_out));
  or or_3 (or_3_out, and_5_out, and_6_out, and_7_out);
  Shifter #(.shift("lr"), .width(23)) shifter_1 (
    .in(fraction_without_normalize_1), .\dist (5'b00001), .out(shifter_1_out));
  Comparator #(.width(32)) comparator_14 (.a(sh1), .b(32'h19), .lt(comparator_14_lt));  // open: gt, eq
  Multiplexer multiplexer_16 (.in0(1'b0), .in1(v26_s), .out(s1), .sel(comparator_14_lt));
  Shifter #(.shift("lr"), .width(23)) shifter_2 (
    .in(fraction_without_normalize_2), .\dist (5'b00001), .out(shifter_2_out));
  Comparator #(.width(32)) comparator_15 (.a(sh2), .b(32'h19), .lt(comparator_15_lt));  // open: gt, eq
  Multiplexer #(.width(23)) multiplexer_17 (
    .in0(fraction_without_normalize_3), .in1(multiplexer_10_out), .out(fraction_result_3),
    .sel(plus_one_exponent_3));
  Subtractor #(.width(9)) subtractor_7 (
    .a({1'b0, a[30:23]}), .b({1'b0, b[30:23]}), .out(subtractor_7_out));  // open: bin, bout
  Subtractor #(.width(9)) subtractor_8 (
    .a({1'b0, b[30:23]}), .b({1'b0, a[30:23]}), .out(subtractor_8_out));  // open: bin, bout
  Multiplexer multiplexer_18 (.in0(1'b0), .in1(v29_s), .out(s2), .sel(comparator_15_lt));
  Comparator #(.width(9)) comparator_16 (.a(subtractor_7_out), .b(9'hc0));  // open: gt, eq, lt
  Comparator #(.width(9)) comparator_17 (.a(subtractor_8_out), .b(9'hc0));  // open: gt, eq, lt
  Multiplexer #(.width(23)) multiplexer_19 (
    .in0(fraction_without_normalize_1), .in1(shifter_1_out), .out(multiplexer_19_out),
    .sel(plus_one_exponent_1));
  Multiplexer #(.width(23)) multiplexer_20 (
    .in0(fraction_without_normalize_2), .in1(shifter_2_out), .out(multiplexer_20_out),
    .sel(plus_one_exponent_2));
  Adder #(.width(23)) adder_8 (.a(multiplexer_19_out), .b(23'h1), .out(adder_8_out));  // open: cin, cout
  and and_8 (and_8_out, s1, g1);
  Multiplexer #(.width(23)) multiplexer_21 (
    .in0(multiplexer_19_out), .in1(adder_8_out), .out(fraction_result_1), .sel(and_8_out));
  Adder #(.width(23)) adder_9 (.a(multiplexer_20_out), .b(23'h1), .out(adder_9_out));  // open: cin, cout
  and and_9 (and_9_out, s2, g2);
  Multiplexer #(.width(23)) multiplexer_22 (
    .in0(multiplexer_20_out), .in1(adder_9_out), .out(fraction_result_2), .sel(and_9_out));

  // Other names for the same wires on the sheet: fraction_a[22:0] = a[22:0]; fraction_b[22:0] = b[22:0];
  //   sign_a = a[31]; exponent_b[7:0] = b[30:23]; exponent_a[7:0] = a[30:23]; sign_b = b[31]
endmodule

module fsub (
  input  [31:0] a,
  input  [31:0] b,
  output INFINITY_PIN,
  output NAN_PIN,
  output [31:0] res
);

  wire [31:31] not_1_out;

  not not_1 (not_1_out[31], b[31]);
  fadd v21 (.a(a), .b({not_1_out[31], b[30:0]}), .INFINITY_PIN(INFINITY_PIN), .NAN_PIN(NAN_PIN), .res(res));
endmodule

module fmult (
  input  [31:0] b,
  input  [31:0] a,
  output [31:0] res
);

  wire a_infinity, a_neg_exp, and_1_out, and_2_out, and_3_out, and_4_out, and_11_out, b_infinity, b_neg_exp,
       bitselector_1_out, bitselector_2_out, comparator_1_eq, comparator_2_eq, comparator_3_eq,
       comparator_4_eq, comparator_5_eq, comparator_6_eq, comparator_7_eq, comparator_8_eq, comparator_9_eq,
       comparator_10_eq, comparator_11_eq, comparator_12_eq, comparator_13_eq, comparator_14_eq,
       comparator_15_eq, comparator_16_eq, comparator_17_eq, comparator_17_gt, comparator_18_eq,
       comparator_18_gt, comparator_19_lt, comparator_20_gt, comparator_21_gt, INFINITY_pin,
       multiplexer_6_out, NAN_pin, nor_1_out, nor_2_out, normal_to_denormal, not_1_out, not_2_out, not_3_out,
       not_4_out, or_1_out, or_2_out, res_zero, result_denormalized, result_MSB, subnormal_a2, subnormal_b2,
       sum_inf, zero_a2, zero_b2;
  wire [5:0] normal_exp, shift_amount, subtractor_1_out, subtractor_2_out;
  wire [6:6] subtractor_1_out_2, subtractor_2_out_2;
  wire [7:0] a_subtracted_exp, adder_2_out, adder_3_out, b_subtracted_exp, exponent_result2, msb_location,
       multiplexer_2_out, multiplexer_10_out, multiplexer_11_out, multiplexer_16_out, multiplexer_17_out,
       multiplexer_19_out, multiplexer_21_out, not_5_out, result_shamt, subtractor_3_out, subtractor_4_out,
       subtractor_6_out;
  wire [7:6] multiplexer_1_out;
  wire [8:0] adder_1_out, subtractor_5_out;
  wire [22:0] multiplexer_14_out, multiplexer_15_out, multiplexer_20_out;
  wire [22:1] multiplexer_9_out_2;
  wire [22:22] multiplexer_9_out_3;
  wire [23:0] multiplexer_3_out, multiplexer_4_out, multiplexer_9_out;
  wire [63:0] bit_extender_1_out, bit_extender_2_out, multiplexer_5_out, multiplexer_7_out,
       multiplexer_8_out, multiplier_1_out, shifter_1_out, shifter_2_out, shifter_3_out;
  wire [63:48] multiplexer_9_out_4;

  Multiplexer #(.width(8)) multiplexer_1 (
    .in0(b_subtracted_exp), .in1(a_subtracted_exp), .out({multiplexer_1_out, normal_exp}), .sel(subnormal_b2));
  and and_1 (and_1_out, zero_a2, b_infinity);
  and and_2 (and_2_out, zero_b2, a_infinity);
  Comparator comparator_1 (.a(a[30:23]), .b({8{1'b1}}), .eq(comparator_1_eq));  // open: gt, lt
  Comparator #(.width(23)) comparator_2 (.a(a[22:0]), .b({23{1'b0}}), .eq(comparator_2_eq));  // open: gt, lt
  Comparator comparator_3 (.a(b[30:23]), .b({8{1'b1}}), .eq(comparator_3_eq));  // open: gt, lt
  Comparator #(.width(23)) comparator_4 (.a(b[22:0]), .b({23{1'b0}}), .eq(comparator_4_eq));  // open: gt, lt
  Comparator comparator_5 (.a(a[30:23]), .b({8{1'b1}}), .eq(comparator_5_eq));  // open: gt, lt
  Comparator #(.width(23)) comparator_6 (.a(a[22:0]), .b({23{1'b0}}), .eq(comparator_6_eq));  // open: gt, lt
  Comparator comparator_7 (.a(b[30:23]), .b({8{1'b1}}), .eq(comparator_7_eq));  // open: gt, lt
  Comparator #(.width(23)) comparator_8 (.a(b[22:0]), .b({23{1'b0}}), .eq(comparator_8_eq));  // open: gt, lt
  Comparator comparator_9 (.a(a[30:23]), .b({8{1'b0}}), .eq(comparator_9_eq));  // open: gt, lt
  Comparator #(.width(23)) comparator_10 (.a(a[22:0]), .b({23{1'b0}}), .eq(comparator_10_eq));  // open: gt, lt
  Comparator comparator_11 (.a(b[30:23]), .b({8{1'b0}}), .eq(comparator_11_eq));  // open: gt, lt
  Comparator #(.width(23)) comparator_12 (.a(b[22:0]), .b({23{1'b0}}), .eq(comparator_12_eq));  // open: gt, lt
  Comparator comparator_13 (.a(b[30:23]), .b({8{1'b0}}), .eq(comparator_13_eq));  // open: gt, lt
  Comparator #(.width(23)) comparator_14 (.a(b[22:0]), .b({23{1'b0}}), .eq(comparator_14_eq));  // open: gt, lt
  Comparator comparator_15 (.a(a[30:23]), .b({8{1'b0}}), .eq(comparator_15_eq));  // open: gt, lt
  Comparator #(.width(23)) comparator_16 (.a(a[22:0]), .b({23{1'b0}}), .eq(comparator_16_eq));  // open: gt, lt
  Comparator comparator_17 (
    .a(msb_location), .b({multiplexer_1_out, normal_exp}), .gt(comparator_17_gt), .eq(comparator_17_eq));  // open: lt
  Comparator #(.mode("unsigned")) comparator_18 (
    .a({multiplexer_1_out, normal_exp}), .b(8'h40), .gt(comparator_18_gt), .eq(comparator_18_eq));  // open: lt
  not not_1 (not_1_out, comparator_2_eq);
  not not_2 (not_2_out, comparator_4_eq);
  not not_3 (not_3_out, comparator_10_eq);
  not not_4 (not_4_out, comparator_12_eq);
  or or_1 (or_1_out, comparator_17_gt, comparator_17_eq);
  Multiplexer #(.width(8)) multiplexer_2 (
    .in0(msb_location), .in1({multiplexer_1_out, normal_exp}), .out(multiplexer_2_out), .sel(or_1_out));
  or or_2 (or_2_out, comparator_18_gt, comparator_18_eq);
  Multiplexer #(.width(24)) multiplexer_3 (
    .in0({1'b1, b[22:0]}), .in1({1'b0, b[22:0]}), .out(multiplexer_3_out), .sel(subnormal_b2));
  and and_3 (and_3_out, comparator_1_eq, not_1_out);
  and and_4 (and_4_out, comparator_3_eq, not_2_out);
  and and_5 (a_infinity, comparator_5_eq, comparator_6_eq);
  and and_6 (b_infinity, comparator_7_eq, comparator_8_eq);
  and and_7 (subnormal_a2, comparator_9_eq, not_3_out);
  and and_8 (subnormal_b2, comparator_11_eq, not_4_out);
  and and_9 (zero_b2, comparator_13_eq, comparator_14_eq);
  and and_10 (zero_a2, comparator_15_eq, comparator_16_eq);
  and and_11 (and_11_out, subnormal_a2, subnormal_b2);
  Shifter #(.width(64)) shifter_1 (.in(multiplier_1_out), .\dist (multiplexer_2_out[5:0]), .out(shifter_1_out));
  Multiplexer #(.width(24)) multiplexer_4 (
    .in0({1'b1, a[22:0]}), .in1({1'b0, a[22:0]}), .out(multiplexer_4_out), .sel(subnormal_a2));
  or or_3 (NAN_pin, and_1_out, and_2_out, and_3_out, and_4_out);
  or or_4 (INFINITY_pin, a_infinity, sum_inf, b_infinity);
  or or_5 (res_zero, zero_b2, and_11_out, zero_a2);
  assign bit_extender_1_out = {{40{1'b0}}, multiplexer_3_out};  // Bit_Extender bit_extender_1
  xor xor_1 (res[31], a[31], b[31]);
  assign bit_extender_2_out = {{40{1'b0}}, multiplexer_4_out};  // Bit_Extender bit_extender_2
  find_msb findMSBh (.input1(multiplier_1_out), .result_msb(msb_location));
  Shifter #(.shift("lr"), .width(64)) shifter_2 (.in(multiplier_1_out), .\dist (normal_exp), .out(shifter_2_out));
  Multiplexer #(.width(64)) multiplexer_5 (
    .in0(shifter_2_out), .in1({64{1'b0}}), .out(multiplexer_5_out), .sel(or_2_out));
  Multiplier #(.width(64)) multiplier_1 (
    .a(bit_extender_2_out), .b(bit_extender_1_out), .out(multiplier_1_out));  // open: cin, cout
  Multiplexer multiplexer_6 (.in0(b_neg_exp), .in1(a_neg_exp), .out(multiplexer_6_out), .sel(subnormal_b2));
  Multiplexer #(.width(64)) multiplexer_7 (
    .in0(shifter_1_out), .in1(multiplexer_5_out), .out(multiplexer_7_out), .sel(multiplexer_6_out));
  Shifter #(.shift("lr"), .width(64)) shifter_3 (.in(multiplier_1_out), .\dist (shift_amount), .out(shifter_3_out));
  Multiplexer #(.width(64)) multiplexer_8 (
    .in0(multiplexer_7_out), .in1(multiplier_1_out), .out(multiplexer_8_out), .sel(result_denormalized));
  Multiplexer #(.width(64)) multiplexer_9 (
    .in0(multiplexer_8_out), .in1(shifter_3_out),
    .out({multiplexer_9_out_4, result_MSB, multiplexer_9_out_3[22], multiplexer_9_out_2, multiplexer_9_out}),
    .sel(normal_to_denormal));
  Multiplexer #(.width(8)) multiplexer_10 (.in0(8'h7f), .in1(8'h7e), .out(multiplexer_10_out), .sel(subnormal_a2));
  Multiplexer #(.width(8)) multiplexer_11 (.in0(8'h7f), .in1(8'h7e), .out(multiplexer_11_out), .sel(subnormal_b2));
  BitSelector #(.width(64)) bitselector_1 (
    .in({multiplexer_9_out_4, result_MSB, multiplexer_9_out_3[22], multiplexer_9_out_2, multiplexer_9_out}),
    .out(bitselector_1_out), .sel(6'b101111));
  BitSelector #(.width(64)) bitselector_2 (
    .in({multiplexer_9_out_4, result_MSB, multiplexer_9_out_3[22], multiplexer_9_out_2, multiplexer_9_out}),
    .out(bitselector_2_out), .sel(6'b101110));
  Subtractor subtractor_1 (
    .a(a[30:23]), .b(multiplexer_10_out), .out({a_neg_exp, subtractor_1_out_2[6], subtractor_1_out}));  // open: bin, bout
  Subtractor subtractor_2 (
    .a(b[30:23]), .b(multiplexer_11_out), .out({b_neg_exp, subtractor_2_out_2[6], subtractor_2_out}));  // open: bin, bout
  nor nor_1 (nor_1_out, bitselector_2_out, bitselector_1_out);
  Subtractor subtractor_3 (
    .a({8{1'b0}}), .b({b_neg_exp, subtractor_2_out_2[6], subtractor_2_out}), .out(subtractor_3_out));  // open: bin, bout
  Subtractor subtractor_4 (
    .a({8{1'b0}}), .b({a_neg_exp, subtractor_1_out_2[6], subtractor_1_out}), .out(subtractor_4_out));  // open: bin, bout
  xnor xnor_1 (result_denormalized, subnormal_a2, subnormal_b2);
  Multiplexer #(.width(8)) multiplexer_12 (
    .in0({b_neg_exp, subtractor_2_out_2[6], subtractor_2_out}), .in1(subtractor_3_out),
    .out(b_subtracted_exp), .sel(b_neg_exp));
  Multiplexer #(.width(8)) multiplexer_13 (
    .in0({a_neg_exp, subtractor_1_out_2[6], subtractor_1_out}), .in1(subtractor_4_out),
    .out(a_subtracted_exp), .sel(a_neg_exp));
  Multiplexer #(.width(23)) multiplexer_14 (
    .in0({multiplexer_9_out_2, multiplexer_9_out[23]}), .in1({multiplexer_9_out_3[22], multiplexer_9_out_2}),
    .out(multiplexer_14_out), .sel(result_MSB));
  Multiplexer #(.width(23)) multiplexer_15 (
    .in0(multiplexer_14_out), .in1({23{1'b0}}), .out(multiplexer_15_out), .sel(res_zero));
  Multiplexer #(.width(8)) multiplexer_16 (
    .in0(exponent_result2), .in1({8{1'b0}}), .out(multiplexer_16_out), .sel(res_zero));
  Comparator #(.width(9)) comparator_19 (.a(adder_1_out), .b(9'h182), .lt(comparator_19_lt));  // open: gt, eq
  Adder #(.width(9)) adder_1 (
    .a({1'b0, a_neg_exp, subtractor_1_out_2[6], subtractor_1_out}),
    .b({1'b0, b_neg_exp, subtractor_2_out_2[6], subtractor_2_out}), .out(adder_1_out));  // open: cin, cout
  Adder adder_2 (
    .a({a_neg_exp, subtractor_1_out_2[6], subtractor_1_out}),
    .b({b_neg_exp, subtractor_2_out_2[6], subtractor_2_out}), .out(adder_2_out));  // open: cin, cout
  Comparator #(.mode("unsigned")) comparator_20 (.a(adder_2_out), .b(8'h7f), .gt(comparator_20_gt));  // open: eq, lt
  and and_12 (normal_to_denormal, b_neg_exp, comparator_19_lt, a_neg_exp);
  Adder adder_3 (.a(adder_2_out), .b(8'h7f), .out(adder_3_out));  // open: cin, cout
  and and_13 (sum_inf, comparator_20_gt, nor_2_out);
  nor nor_2 (nor_2_out, a_neg_exp, b_neg_exp);
  Multiplexer #(.width(8)) multiplexer_17 (
    .in0(multiplexer_16_out), .in1({8{1'b0}}), .out(multiplexer_17_out), .sel(nor_1_out));
  Subtractor #(.width(9)) subtractor_5 (.a(9'h182), .b(adder_1_out), .out(subtractor_5_out));  // open: bin, bout
  Subtractor subtractor_6 (.a(adder_3_out), .b(msb_location), .out(subtractor_6_out));  // open: bin, bout
  Adder adder_4 (.a(adder_3_out), .b(8'h1), .out(result_shamt));  // open: cin, cout
  Comparator #(.width(9)) comparator_21 (.a(subtractor_5_out), .b(9'h3f), .gt(comparator_21_gt));  // open: eq, lt
  Multiplexer #(.width(6)) multiplexer_18 (
    .in0(subtractor_5_out[5:0]), .in1({6{1'b1}}), .out(shift_amount), .sel(comparator_21_gt));
  Multiplexer #(.width(8)) multiplexer_19 (
    .in0(adder_3_out), .in1(result_shamt), .out(multiplexer_19_out), .sel(result_MSB));
  Multiplexer #(.width(23)) multiplexer_20 (
    .in0(multiplexer_15_out), .in1({23{1'b0}}), .out(multiplexer_20_out), .sel(INFINITY_pin));
  Multiplexer #(.width(8)) multiplexer_21 (
    .in0(multiplexer_17_out), .in1({8{1'b1}}), .out(multiplexer_21_out), .sel(INFINITY_pin));
  assign not_5_out = ~multiplexer_19_out;  // NOT_Gate not_5, 8 bits wide
  Adder adder_5 (.a(not_5_out), .b(8'h1));  // open: out, cin, cout
  Multiplexer #(.width(8)) multiplexer_22 (
    .in0(subtractor_6_out), .in1(multiplexer_19_out), .out(exponent_result2), .sel(result_denormalized));
  Multiplexer #(.width(23)) multiplexer_23 (.in0(multiplexer_20_out), .in1({23{1'b1}}), .out(res[22:0]), .sel(NAN_pin));
  Multiplexer #(.width(8)) multiplexer_24 (.in0(multiplexer_21_out), .in1({8{1'b1}}), .out(res[30:23]), .sel(NAN_pin));

  // Other names for the same wires on the sheet: b2[31:0] = b; fraction_b2[22:0] = b[22:0]; a2[31:0] = a;
  //   fraction_a2[22:0] = a[22:0]; exponent_a2[7:0] = a[30:23]; sign_a2 = a[31]; exponent_b2[7:0] = b[30:23];
  //   sign_b2 = b[31]; sign_result = res[31]
endmodule

module fabs (
  input  [31:0] a,
  output [31:0] res
);


  assign res = {1'b0, a[30:0]};

  // Other names for the same wires on the sheet: a2[31:0] = a
endmodule

module fslt (
  input  [31:0] a,
  input  [31:0] b,
  output INFINITY_PIN,
  output NAN_PIN,
  output [31:0] res
);

  wire [31:0] v30_res;

  fsub v30 (.a(a), .b(b), .INFINITY_PIN(INFINITY_PIN), .NAN_PIN(NAN_PIN), .res(v30_res));
  Multiplexer #(.width(32)) multiplexer_1 (.in0({32{1'b0}}), .in1(32'h1), .out(res), .sel(v30_res[31]));
endmodule

module fsin (
  input  [31:0] count,
  input  clk,
  input  [31:0] x,
  output [31:0] res,
  output Done
);

  wire comparator_1_eq, multiplexer_4_out, multiplexer_7_out, SineDone, start_sin;
  wire [3:0] multiplexer_3_out, multiplexer_6_out, sine_step, sine_steps_start, subtractor_1_out;
  wire [31:0] addh_res, calcH_term, multh_res, multiplexer_1_out, multiplexer_2_out, multiplexer_5_out;

  D_Flip_Flop d_ff_1 (.clk(clk), .Qn(start_sin), .preset(clk), .reset(SineDone));  // open: D, Q
  Multiplexer #(.select(4), .width(32)) multiplexer_1 (
    .in0(32'h3f800000), .in1(32'hbe2aaaab), .in2(32'h3c088889), .in3(32'hb9500d01), .in4(32'h3638ef1d),
    .in5(32'hb2d7322b), .in6(32'h2f309231), .in7(32'hab573f9f), .in8(32'h274a963c), .in9(32'ha317a4da),
    .in10(32'h1eb8dc78), .in11(32'h9a3b0da1), .in12(32'h159f9e67), .in13(32'h90e8d58e), .in14(32'hc12cfcc),
    .in15(32'h8721a697), .out(multiplexer_1_out), .sel(sine_step));
  floatTOdec floatToDecH (.float(count), .dec(sine_steps_start));
  Calculate_Term_sin calcH (.x(x), .a(sine_step), .term(calcH_term));
  fmult multh (.b(multiplexer_1_out), .a(calcH_term), .res(multh_res));
  fadd addh (.a(res), .b(multh_res), .res(addh_res));  // open: INFINITY_PIN, NAN_PIN
  Multiplexer #(.width(32)) multiplexer_2 (.in0(addh_res), .in1(res), .out(multiplexer_2_out), .sel(SineDone));
  Subtractor #(.width(4)) subtractor_1 (.a(sine_step), .b(4'b0001), .out(subtractor_1_out));  // open: bin, bout
  Comparator #(.width(4)) comparator_1 (.a(sine_step), .b(4'b0000), .eq(comparator_1_eq));  // open: gt, lt
  Multiplexer #(.width(4)) multiplexer_3 (
    .in0(subtractor_1_out), .in1(sine_step), .out(multiplexer_3_out), .sel(SineDone));
  Multiplexer multiplexer_4 (.in0(comparator_1_eq), .in1(SineDone), .out(multiplexer_4_out), .sel(SineDone));
  Multiplexer #(.width(32)) multiplexer_5 (
    .in0(multiplexer_2_out), .in1({32{1'b0}}), .out(multiplexer_5_out), .sel(start_sin));
  Multiplexer #(.width(4)) multiplexer_6 (
    .in0(multiplexer_3_out), .in1(sine_steps_start), .out(multiplexer_6_out), .sel(start_sin));
  Multiplexer multiplexer_7 (.in0(multiplexer_4_out), .in1(1'b0), .out(multiplexer_7_out), .sel(start_sin));
  Register #(.width(32)) register_1 (.D(multiplexer_5_out), .clk(clk), .Q(res));  // open: en, clr
  Register #(.width(4)) register_2 (.D(multiplexer_6_out), .clk(clk), .Q(sine_step));  // open: en, clr
  Register #(.width(1)) register_3 (.D(multiplexer_7_out), .clk(clk), .Q(SineDone));  // open: en, clr
  D_Flip_Flop d_ff_2 (.D(SineDone), .clk(clk), .Q(Done));  // open: Qn, preset, reset

  // Other names for the same wires on the sheet: sineTrans[31:0] = res
endmodule

module SRL_fadd (
  input  [31:0] a,
  input  [31:0] b,
  output one_signal,
  output [31:0] res_low
);

  wire comparator_1_eq, comparator_2_eq, comparator_3_gt, not_1_out, or_1_out;
  wire [31:0] multiplexer_1_out, multiplexer_2_out, shifter_1_out, shifter_2_out, shifter_3_out,
       subtractor_1_out;

  Subtractor #(.width(32)) subtractor_1 (.a(b), .b(32'h1), .out(subtractor_1_out));  // open: bin, bout
  Comparator #(.width(32)) comparator_1 (.a(a), .b({32{1'b0}}), .eq(comparator_1_eq));  // open: gt, lt
  Comparator #(.width(32)) comparator_2 (.a(res_low), .b({32{1'b0}}), .eq(comparator_2_eq));  // open: gt, lt
  Comparator #(.width(32)) comparator_3 (.a(b), .b(32'h1f), .gt(comparator_3_gt));  // open: eq, lt
  not not_1 (not_1_out, comparator_1_eq);
  Shifter #(.shift("lr"), .width(32)) shifter_1 (.in(a), .\dist (b[4:0]), .out(shifter_1_out));
  Shifter #(.shift("lr"), .width(32)) shifter_2 (.in(a), .\dist (subtractor_1_out[4:0]), .out(shifter_2_out));
  and and_1 (one_signal, not_1_out, comparator_2_eq);
  Shifter #(.shift("lr"), .width(32)) shifter_3 (.in(shifter_2_out), .\dist (5'b00001), .out(shifter_3_out));
  Multiplexer #(.width(32)) multiplexer_1 (
    .in0(shifter_3_out), .in1(shifter_1_out), .out(multiplexer_1_out), .sel(b[0]));
  or or_1 (or_1_out, b[0], b[1], b[2], b[3], b[4]);
  Multiplexer #(.width(32)) multiplexer_2 (.in0(a), .in1(multiplexer_1_out), .out(multiplexer_2_out), .sel(or_1_out));
  Multiplexer #(.width(32)) multiplexer_3 (
    .in0(multiplexer_2_out), .in1({32{1'b0}}), .out(res_low), .sel(comparator_3_gt));
endmodule

module fMinnus (
  input  [31:0] a,
  input  [31:0] b,
  output [31:0] res
);

  wire and_1_out, and_2_out, and_3_out, and_4_out, comparator_1_lt, comparator_2_eq, comparator_3_eq,
       comparator_4_eq, comparator_5_eq, comparator_6_eq, comparator_7_eq, comparator_8_eq, comparator_9_eq,
       comparator_10_eq, comparator_11_lt, comparator_12_eq, comparator_13_eq, comparator_14_eq,
       comparator_14_gt, comparator_15_eq, comparator_15_gt, comparator_16_lt, comparator_17_gt,
       comparator_18_eq, comparator_18_gt, comparator_19_eq, exponents_bigger, exponents_difference_alot,
       INFINITY_pin, multiplexer_10_out, multiplexer_12_out, multiplexer_13_out, multiplexer_15_out, NAN_pin,
       not_1_out, not_2_out, not_3_out, sign_result, subnormal_a, subnormal_b;
  wire [4:0] v18_res;
  wire [5:0] adder_1_out, shift_for_normalize_3;
  wire [7:0] bit_extender_1_out, exponent_result, exponent_result_1, exponent_result_2, exponent_result_3,
       multiplexer_11_out, multiplexer_14_out, multiplexer_16_out, multiplexer_17_out, multiplexer_18_out,
       multiplexer_19_out, subtractor_6_out;
  wire [8:0] bit_extender_2_out, exponent_manfi;
  wire [22:0] fraction_result, fraction_result_1, fraction_result_2, fraction_result_3, multiplexer_5_out,
       multiplexer_6_out, multiplexer_7_out, multiplexer_8_out;
  wire [23:0] fraction_sub_result_3, subtractor_1_out, subtractor_2_out;
  wire [31:0] bit_extender_3_out, bit_extender_4_out, v19_res_low;

  Subtractor #(.width(24)) subtractor_1 (
    .a({subnormal_a, a[22:0]}), .b({subnormal_b, b[22:0]}), .out(subtractor_1_out));  // open: bin, bout
  Subtractor #(.width(24)) subtractor_2 (
    .a({subnormal_b, b[22:0]}), .b({subnormal_a, a[22:0]}), .out(subtractor_2_out));  // open: bin, bout
  Comparator #(.width(24)) comparator_1 (
    .a({1'b0, a[22:0]}), .b({1'b0, b[22:0]}), .lt(comparator_1_lt));  // open: gt, eq
  Multiplexer #(.width(24)) multiplexer_1 (
    .in0(subtractor_1_out), .in1(subtractor_2_out), .out(fraction_sub_result_3), .sel(comparator_1_lt));
  Comparator comparator_2 (.a(a[30:23]), .b({8{1'b1}}), .eq(comparator_2_eq));  // open: gt, lt
  not not_1 (not_1_out, comparator_3_eq);
  Comparator #(.width(23)) comparator_3 (.a(a[22:0]), .b({23{1'b0}}), .eq(comparator_3_eq));  // open: gt, lt
  Comparator comparator_4 (.a(b[30:23]), .b({8{1'b1}}), .eq(comparator_4_eq));  // open: gt, lt
  not not_2 (not_2_out, comparator_5_eq);
  Comparator #(.width(23)) comparator_5 (.a(b[22:0]), .b({23{1'b0}}), .eq(comparator_5_eq));  // open: gt, lt
  Comparator comparator_6 (.a(a[30:23]), .b({8{1'b1}}), .eq(comparator_6_eq));  // open: gt, lt
  Comparator #(.width(23)) comparator_7 (.a(a[22:0]), .b({23{1'b0}}), .eq(comparator_7_eq));  // open: gt, lt
  Comparator comparator_8 (.a(b[30:23]), .b({8{1'b1}}), .eq(comparator_8_eq));  // open: gt, lt
  Comparator #(.width(23)) comparator_9 (.a(b[22:0]), .b({23{1'b0}}), .eq(comparator_9_eq));  // open: gt, lt
  Comparator comparator_10 (.a(b[30:23]), .b({8{1'b0}}), .eq(comparator_10_eq));  // open: gt, lt
  Comparator #(.width(9)) comparator_11 (.a(exponent_manfi), .b({9{1'b0}}), .lt(comparator_11_lt));  // open: gt, eq
  Comparator comparator_12 (.a(a[30:23]), .b({8{1'b0}}), .eq(comparator_12_eq));  // open: gt, lt
  Comparator #(.width(31)) comparator_13 (.a(a[30:0]), .b(b[30:0]), .eq(comparator_13_eq));  // open: gt, lt
  and and_1 (and_1_out, comparator_2_eq, not_1_out);
  and and_2 (and_2_out, comparator_4_eq, not_2_out);
  and and_3 (and_3_out, comparator_6_eq, comparator_7_eq);
  and and_4 (and_4_out, comparator_8_eq, comparator_9_eq);
  Multiplexer multiplexer_2 (.in0(1'b1), .in1(1'b0), .out(subnormal_a), .sel(comparator_12_eq));
  Multiplexer multiplexer_3 (.in0(1'b1), .in1(1'b0), .out(subnormal_b), .sel(comparator_10_eq));
  Multiplexer #(.width(32)) multiplexer_4 (
    .in0({sign_result, exponent_result, fraction_result}), .in1({32{1'b0}}), .out(res), .sel(comparator_13_eq));
  Multiplexer #(.width(23)) multiplexer_5 (
    .in0(fraction_result_3), .in1(fraction_sub_result_3[22:0]), .out(multiplexer_5_out),
    .sel(comparator_11_lt));
  Comparator #(.width(9)) comparator_14 (
    .a({1'b0, a[30:23]}), .b({1'b0, b[30:23]}), .gt(comparator_14_gt), .eq(comparator_14_eq));  // open: lt
  or or_1 (NAN_pin, and_1_out, and_2_out);
  or or_2 (INFINITY_pin, and_3_out, and_4_out);
  Multiplexer #(.width(23)) multiplexer_6 (
    .in0(fraction_result_1), .in1(fraction_result_2), .out(multiplexer_6_out), .sel(comparator_14_gt));
  Multiplexer #(.width(23)) multiplexer_7 (
    .in0(multiplexer_6_out), .in1(multiplexer_5_out), .out(multiplexer_7_out), .sel(comparator_14_eq));
  Multiplexer #(.width(23)) multiplexer_8 (
    .in0(a[22:0]), .in1(b[22:0]), .out(multiplexer_8_out), .sel(exponents_bigger));
  Multiplexer #(.width(23)) multiplexer_9 (
    .in0(multiplexer_7_out), .in1(multiplexer_8_out), .out(fraction_result), .sel(exponents_difference_alot));
  assign bit_extender_1_out = {{2{1'b0}}, shift_for_normalize_3};  // Bit_Extender bit_extender_1
  assign bit_extender_2_out = {{2{1'b0}}, {1'b0, shift_for_normalize_3}};  // Bit_Extender bit_extender_2
  Comparator #(.width(9)) comparator_15 (
    .a({1'b0, a[30:23]}), .b({1'b0, b[30:23]}), .gt(comparator_15_gt), .eq(comparator_15_eq));  // open: lt
  Multiplexer multiplexer_10 (.in0(b[31]), .in1(a[31]), .out(multiplexer_10_out), .sel(comparator_15_gt));
  Subtractor subtractor_3 (.a(b[30:23]), .b(bit_extender_1_out), .out(exponent_result_3));  // open: bin, bout
  Subtractor #(.width(9)) subtractor_4 (
    .a({1'b0, b[30:23]}), .b(bit_extender_2_out), .out(exponent_manfi));  // open: bin, bout
  Comparator #(.width(9)) comparator_16 (.a(exponent_manfi), .b({9{1'b0}}), .lt(comparator_16_lt));  // open: gt, eq
  Adder #(.width(6)) adder_1 (.a(shift_for_normalize_3), .b(6'b000001), .out(adder_1_out));  // open: cin, cout
  Comparator #(.width(24)) comparator_17 (
    .a({1'b0, a[22:0]}), .b({1'b0, b[22:0]}), .gt(comparator_17_gt));  // open: eq, lt
  assign bit_extender_3_out = {{8{1'b0}}, fraction_sub_result_3};  // Bit_Extender bit_extender_3
  assign bit_extender_4_out = {{26{1'b0}}, adder_1_out};  // Bit_Extender bit_extender_4
  Multiplexer #(.width(8)) multiplexer_11 (
    .in0(exponent_result_3), .in1(b[30:23]), .out(multiplexer_11_out), .sel(comparator_16_lt));
  Multiplexer multiplexer_12 (.in0(b[31]), .in1(a[31]), .out(multiplexer_12_out), .sel(comparator_17_gt));
  Multiplexer multiplexer_13 (
    .in0(multiplexer_10_out), .in1(multiplexer_12_out), .out(multiplexer_13_out), .sel(comparator_15_eq));
  substract v16 (
    .fraction_b(b[22:0]), .sub_normal_b(subnormal_b), .fraction_a(a[22:0]), .exponent_a(a[30:23]),
    .exponent_b(b[30:23]), .fraction_result(fraction_result_2), .exponent_result(exponent_result_2));
  Comparator #(.width(9)) comparator_18 (
    .a({1'b0, a[30:23]}), .b({1'b0, b[30:23]}), .gt(comparator_18_gt), .eq(comparator_18_eq),
    .lt(exponents_bigger));
  SLLL v19 (.a(bit_extender_3_out), .b(bit_extender_4_out), .res_low(v19_res_low));  // open: res_high
  bitOne v18 (.a(fraction_sub_result_3), .res(v18_res));
  Multiplexer #(.width(8)) multiplexer_14 (
    .in0(exponent_result_1), .in1(exponent_result_2), .out(multiplexer_14_out), .sel(comparator_18_gt));
  Multiplexer multiplexer_15 (.in0(a[31]), .in1(b[31]), .out(multiplexer_15_out), .sel(exponents_bigger));
  Multiplexer #(.width(8)) multiplexer_16 (
    .in0(multiplexer_14_out), .in1(multiplexer_11_out), .out(multiplexer_16_out), .sel(comparator_18_eq));
  Subtractor #(.width(6)) subtractor_5 (
    .a(6'b011000), .b({1'b0, v18_res}), .out(shift_for_normalize_3));  // open: bin, bout
  Multiplexer #(.width(8)) multiplexer_17 (
    .in0(b[30:23]), .in1(a[30:23]), .out(multiplexer_17_out), .sel(comparator_18_gt));
  Multiplexer #(.width(8)) multiplexer_18 (
    .in0(a[30:23]), .in1(b[30:23]), .out(multiplexer_18_out), .sel(comparator_18_gt));
  not not_3 (not_3_out, comparator_19_eq);
  Comparator #(.width(6)) comparator_19 (
    .a(shift_for_normalize_3), .b({6{1'b0}}), .eq(comparator_19_eq));  // open: gt, lt
  Multiplexer #(.width(8)) multiplexer_19 (
    .in0(a[30:23]), .in1(b[30:23]), .out(multiplexer_19_out), .sel(exponents_bigger));
  Multiplexer multiplexer_20 (
    .in0(multiplexer_13_out), .in1(multiplexer_15_out), .out(sign_result), .sel(exponents_difference_alot));
  Subtractor subtractor_6 (.a(multiplexer_17_out), .b(multiplexer_18_out), .out(subtractor_6_out));  // open: bin, bout
  Comparator #(.mode("unsigned")) comparator_20 (
    .a(subtractor_6_out), .b(8'h3f), .gt(exponents_difference_alot));  // open: eq, lt
  substract v17 (
    .fraction_b(a[22:0]), .sub_normal_b(subnormal_a), .fraction_a(b[22:0]), .exponent_a(b[30:23]),
    .exponent_b(a[30:23]), .fraction_result(fraction_result_1), .exponent_result(exponent_result_1));
  Multiplexer #(.width(8)) multiplexer_21 (
    .in0(multiplexer_16_out), .in1(multiplexer_19_out), .out(exponent_result), .sel(exponents_difference_alot));
  Multiplexer #(.width(23)) multiplexer_22 (
    .in0(fraction_sub_result_3[22:0]), .in1(v19_res_low[23:1]), .out(fraction_result_3), .sel(not_3_out));

  // Other names for the same wires on the sheet: fraction_a[22:0] = a[22:0]; fraction_b[22:0] = b[22:0];
  //   exponent_a[7:0] = a[30:23]; exponent_b[7:0] = b[30:23]; sign_a = a[31]; sign_b = b[31];
  //   fraction_without_normalize_3[23:0] = fraction_sub_result_3
endmodule
module bitOne (
  input  [23:0] a,
  output [4:0] res
);

  wire and_1_out, and_2_out, and_3_out, and_4_out, and_5_out, and_6_out, and_7_out, and_8_out, and_9_out,
       and_10_out, and_11_out, and_12_out, and_13_out, and_14_out, and_15_out, and_16_out, and_17_out,
       and_18_out, and_19_out, and_20_out, and_21_out, and_22_out, comparator_1_eq, comparator_1_gt,
       comparator_2_lt, comparator_3_gt, comparator_4_lt, comparator_5_gt, comparator_6_lt, comparator_7_gt,
       comparator_8_lt, comparator_9_gt, comparator_10_lt, comparator_11_gt, comparator_12_lt,
       comparator_13_gt, comparator_14_lt, comparator_15_gt, comparator_16_lt, comparator_17_gt,
       comparator_18_lt, comparator_19_gt, comparator_20_lt, comparator_21_gt, comparator_22_lt,
       comparator_23_gt, comparator_24_lt, comparator_25_gt, comparator_26_lt, comparator_27_gt,
       comparator_28_lt, comparator_29_gt, comparator_30_lt, comparator_31_gt, comparator_32_lt,
       comparator_33_gt, comparator_34_lt, comparator_35_gt, comparator_36_lt, comparator_37_gt,
       comparator_38_lt, comparator_39_gt, comparator_40_lt, comparator_41_gt, comparator_42_lt,
       comparator_43_gt, comparator_44_lt, comparator_45_eq, comparator_46_lt, comparator_47_eq, or_1_out;
  wire [4:0] multiplexer_1_out, multiplexer_2_out, multiplexer_3_out, multiplexer_4_out, multiplexer_5_out,
       multiplexer_6_out, multiplexer_7_out, multiplexer_8_out, multiplexer_9_out, multiplexer_10_out,
       multiplexer_11_out, multiplexer_12_out, multiplexer_13_out, multiplexer_14_out, multiplexer_15_out,
       multiplexer_16_out, multiplexer_17_out, multiplexer_18_out, multiplexer_19_out, multiplexer_20_out,
       multiplexer_21_out, multiplexer_22_out, multiplexer_23_out, multiplexer_24_out;

  Comparator #(.width(24)) comparator_1 (.a(a), .b(24'h1), .gt(comparator_1_gt), .eq(comparator_1_eq));  // open: lt
  Comparator #(.width(24)) comparator_2 (.a(a), .b(24'h4), .lt(comparator_2_lt));  // open: gt, eq
  Comparator #(.width(24)) comparator_3 (.a(a), .b(24'h3), .gt(comparator_3_gt));  // open: eq, lt
  Comparator #(.width(24)) comparator_4 (.a(a), .b(24'h8), .lt(comparator_4_lt));  // open: gt, eq
  Comparator #(.width(24)) comparator_5 (.a(a), .b(24'h7), .gt(comparator_5_gt));  // open: eq, lt
  Comparator #(.width(24)) comparator_6 (.a(a), .b(24'h10), .lt(comparator_6_lt));  // open: gt, eq
  Comparator #(.width(24)) comparator_7 (.a(a), .b(24'hf), .gt(comparator_7_gt));  // open: eq, lt
  Comparator #(.width(24)) comparator_8 (.a(a), .b(24'h20), .lt(comparator_8_lt));  // open: gt, eq
  Comparator #(.width(24)) comparator_9 (.a(a), .b(24'h1f), .gt(comparator_9_gt));  // open: eq, lt
  Comparator #(.width(24)) comparator_10 (.a(a), .b(24'h40), .lt(comparator_10_lt));  // open: gt, eq
  Comparator #(.width(24)) comparator_11 (.a(a), .b(24'h3f), .gt(comparator_11_gt));  // open: eq, lt
  Comparator #(.width(24)) comparator_12 (.a(a), .b(24'h80), .lt(comparator_12_lt));  // open: gt, eq
  Comparator #(.width(24)) comparator_13 (.a(a), .b(24'h7f), .gt(comparator_13_gt));  // open: eq, lt
  Comparator #(.width(24)) comparator_14 (.a(a), .b(24'h100), .lt(comparator_14_lt));  // open: gt, eq
  Comparator #(.width(24)) comparator_15 (.a(a), .b(24'hff), .gt(comparator_15_gt));  // open: eq, lt
  Comparator #(.width(24)) comparator_16 (.a(a), .b(24'h200), .lt(comparator_16_lt));  // open: gt, eq
  Comparator #(.width(24)) comparator_17 (.a(a), .b(24'h1ff), .gt(comparator_17_gt));  // open: eq, lt
  Comparator #(.width(24)) comparator_18 (.a(a), .b(24'h400), .lt(comparator_18_lt));  // open: gt, eq
  Comparator #(.width(24)) comparator_19 (.a(a), .b(24'h3ff), .gt(comparator_19_gt));  // open: eq, lt
  Comparator #(.width(24)) comparator_20 (.a(a), .b(24'h800), .lt(comparator_20_lt));  // open: gt, eq
  Comparator #(.width(24)) comparator_21 (.a(a), .b(24'h7ff), .gt(comparator_21_gt));  // open: eq, lt
  Comparator #(.width(24)) comparator_22 (.a(a), .b(24'h1000), .lt(comparator_22_lt));  // open: gt, eq
  Comparator #(.width(24)) comparator_23 (.a(a), .b(24'hfff), .gt(comparator_23_gt));  // open: eq, lt
  Comparator #(.width(24)) comparator_24 (.a(a), .b(24'h2000), .lt(comparator_24_lt));  // open: gt, eq
  Comparator #(.width(24)) comparator_25 (.a(a), .b(24'h1fff), .gt(comparator_25_gt));  // open: eq, lt
  Comparator #(.width(24)) comparator_26 (.a(a), .b(24'h4000), .lt(comparator_26_lt));  // open: gt, eq
  Comparator #(.width(24)) comparator_27 (.a(a), .b(24'h3fff), .gt(comparator_27_gt));  // open: eq, lt
  Comparator #(.width(24)) comparator_28 (.a(a), .b(24'h8000), .lt(comparator_28_lt));  // open: gt, eq
  Comparator #(.width(24)) comparator_29 (.a(a), .b(24'h7fff), .gt(comparator_29_gt));  // open: eq, lt
  Comparator #(.width(24)) comparator_30 (.a(a), .b(24'h10000), .lt(comparator_30_lt));  // open: gt, eq
  Comparator #(.width(24)) comparator_31 (.a(a), .b(24'hffff), .gt(comparator_31_gt));  // open: eq, lt
  Comparator #(.width(24)) comparator_32 (.a(a), .b(24'h20000), .lt(comparator_32_lt));  // open: gt, eq
  Comparator #(.width(24)) comparator_33 (.a(a), .b(24'h1ffff), .gt(comparator_33_gt));  // open: eq, lt
  Comparator #(.width(24)) comparator_34 (.a(a), .b(24'h40000), .lt(comparator_34_lt));  // open: gt, eq
  Comparator #(.width(24)) comparator_35 (.a(a), .b(24'h3ffff), .gt(comparator_35_gt));  // open: eq, lt
  Comparator #(.width(24)) comparator_36 (.a(a), .b(24'h80000), .lt(comparator_36_lt));  // open: gt, eq
  Comparator #(.width(24)) comparator_37 (.a(a), .b(24'h7ffff), .gt(comparator_37_gt));  // open: eq, lt
  Comparator #(.width(24)) comparator_38 (.a(a), .b(24'h100000), .lt(comparator_38_lt));  // open: gt, eq
  Comparator #(.width(24)) comparator_39 (.a(a), .b(24'hfffff), .gt(comparator_39_gt));  // open: eq, lt
  Comparator #(.width(24)) comparator_40 (.a(a), .b(24'h200000), .lt(comparator_40_lt));  // open: gt, eq
  Comparator #(.width(24)) comparator_41 (.a(a), .b(24'h1fffff), .gt(comparator_41_gt));  // open: eq, lt
  Comparator #(.width(24)) comparator_42 (.a(a), .b(24'h400000), .lt(comparator_42_lt));  // open: gt, eq
  Comparator #(.width(24)) comparator_43 (.a(a), .b(24'h3fffff), .gt(comparator_43_gt));  // open: eq, lt
  Comparator #(.width(24)) comparator_44 (.a(a), .b(24'h7fffff), .lt(comparator_44_lt));  // open: gt, eq
  Comparator #(.width(24)) comparator_45 (.a(a), .b(24'h7fffff), .eq(comparator_45_eq));  // open: gt, lt
  Comparator #(.width(24)) comparator_46 (.a(a), .b({24{1'b0}}), .lt(comparator_46_lt));  // open: gt, eq
  Comparator #(.width(24)) comparator_47 (.a(a), .b({24{1'b0}}), .eq(comparator_47_eq));  // open: gt, lt
  Multiplexer #(.width(5)) multiplexer_1 (
    .in0(multiplexer_2_out), .in1(5'b00001), .out(multiplexer_1_out), .sel(comparator_1_eq));
  and and_1 (and_1_out, comparator_1_gt, comparator_2_lt);
  and and_2 (and_2_out, comparator_3_gt, comparator_4_lt);
  and and_3 (and_3_out, comparator_5_gt, comparator_6_lt);
  and and_4 (and_4_out, comparator_7_gt, comparator_8_lt);
  and and_5 (and_5_out, comparator_9_gt, comparator_10_lt);
  and and_6 (and_6_out, comparator_11_gt, comparator_12_lt);
  and and_7 (and_7_out, comparator_13_gt, comparator_14_lt);
  and and_8 (and_8_out, comparator_15_gt, comparator_16_lt);
  and and_9 (and_9_out, comparator_17_gt, comparator_18_lt);
  and and_10 (and_10_out, comparator_19_gt, comparator_20_lt);
  and and_11 (and_11_out, comparator_21_gt, comparator_22_lt);
  and and_12 (and_12_out, comparator_23_gt, comparator_24_lt);
  and and_13 (and_13_out, comparator_25_gt, comparator_26_lt);
  and and_14 (and_14_out, comparator_27_gt, comparator_28_lt);
  and and_15 (and_15_out, comparator_29_gt, comparator_30_lt);
  and and_16 (and_16_out, comparator_31_gt, comparator_32_lt);
  and and_17 (and_17_out, comparator_33_gt, comparator_34_lt);
  and and_18 (and_18_out, comparator_35_gt, comparator_36_lt);
  and and_19 (and_19_out, comparator_37_gt, comparator_38_lt);
  and and_20 (and_20_out, comparator_39_gt, comparator_40_lt);
  and and_21 (and_21_out, comparator_41_gt, comparator_42_lt);
  and and_22 (and_22_out, comparator_43_gt, or_1_out);
  or or_1 (or_1_out, comparator_44_lt, comparator_45_eq);
  Multiplexer #(.width(5)) multiplexer_2 (
    .in0({5{1'b0}}), .in1({5{1'b0}}), .out(multiplexer_2_out), .sel(comparator_47_eq));
  Multiplexer #(.width(5)) multiplexer_3 (
    .in0(multiplexer_1_out), .in1(5'b00010), .out(multiplexer_3_out), .sel(and_1_out));
  Multiplexer #(.width(5)) multiplexer_4 (
    .in0(multiplexer_3_out), .in1(5'b00011), .out(multiplexer_4_out), .sel(and_2_out));
  Multiplexer #(.width(5)) multiplexer_5 (
    .in0(multiplexer_4_out), .in1(5'b00100), .out(multiplexer_5_out), .sel(and_3_out));
  Multiplexer #(.width(5)) multiplexer_6 (
    .in0(multiplexer_5_out), .in1(5'b00101), .out(multiplexer_6_out), .sel(and_4_out));
  Multiplexer #(.width(5)) multiplexer_7 (
    .in0(multiplexer_6_out), .in1(5'b00110), .out(multiplexer_7_out), .sel(and_5_out));
  Multiplexer #(.width(5)) multiplexer_8 (
    .in0(multiplexer_7_out), .in1(5'b00111), .out(multiplexer_8_out), .sel(and_6_out));
  Multiplexer #(.width(5)) multiplexer_9 (
    .in0(multiplexer_8_out), .in1(5'b01000), .out(multiplexer_9_out), .sel(and_7_out));
  Multiplexer #(.width(5)) multiplexer_10 (
    .in0(multiplexer_9_out), .in1(5'b01001), .out(multiplexer_10_out), .sel(and_8_out));
  Multiplexer #(.width(5)) multiplexer_11 (
    .in0(multiplexer_10_out), .in1(5'b01010), .out(multiplexer_11_out), .sel(and_9_out));
  Multiplexer #(.width(5)) multiplexer_12 (
    .in0(multiplexer_11_out), .in1(5'b01011), .out(multiplexer_12_out), .sel(and_10_out));
  Multiplexer #(.width(5)) multiplexer_13 (
    .in0(multiplexer_12_out), .in1(5'b01100), .out(multiplexer_13_out), .sel(and_11_out));
  Multiplexer #(.width(5)) multiplexer_14 (
    .in0(multiplexer_13_out), .in1(5'b01101), .out(multiplexer_14_out), .sel(and_12_out));
  Multiplexer #(.width(5)) multiplexer_15 (
    .in0(multiplexer_14_out), .in1(5'b01110), .out(multiplexer_15_out), .sel(and_13_out));
  Multiplexer #(.width(5)) multiplexer_16 (
    .in0(multiplexer_15_out), .in1(5'b01111), .out(multiplexer_16_out), .sel(and_14_out));
  Multiplexer #(.width(5)) multiplexer_17 (
    .in0(multiplexer_16_out), .in1(5'b10000), .out(multiplexer_17_out), .sel(and_15_out));
  Multiplexer #(.width(5)) multiplexer_18 (
    .in0(multiplexer_17_out), .in1(5'b10001), .out(multiplexer_18_out), .sel(and_16_out));
  Multiplexer #(.width(5)) multiplexer_19 (
    .in0(multiplexer_18_out), .in1(5'b10010), .out(multiplexer_19_out), .sel(and_17_out));
  Multiplexer #(.width(5)) multiplexer_20 (
    .in0(multiplexer_19_out), .in1(5'b10011), .out(multiplexer_20_out), .sel(and_18_out));
  Multiplexer #(.width(5)) multiplexer_21 (
    .in0(multiplexer_20_out), .in1(5'b10100), .out(multiplexer_21_out), .sel(and_19_out));
  Multiplexer #(.width(5)) multiplexer_22 (
    .in0(multiplexer_21_out), .in1(5'b10101), .out(multiplexer_22_out), .sel(and_20_out));
  Multiplexer #(.width(5)) multiplexer_23 (
    .in0(multiplexer_22_out), .in1(5'b10110), .out(multiplexer_23_out), .sel(and_21_out));
  Multiplexer #(.width(5)) multiplexer_24 (
    .in0(multiplexer_23_out), .in1(5'b10111), .out(multiplexer_24_out), .sel(and_22_out));
  Multiplexer #(.width(5)) multiplexer_25 (.in0(multiplexer_24_out), .in1(5'b11000), .out(res), .sel(comparator_46_lt));
endmodule

module add_find_bit_1 (
  input  [63:0] number,
  input  [5:0] shift,
  output sticky,
  output s
);

  wire bitselector_2_out, bitselector_3_out, bitselector_4_out, bitselector_5_out, bitselector_6_out,
       bitselector_7_out, bitselector_8_out, bitselector_9_out, bitselector_10_out, bitselector_11_out,
       bitselector_12_out, bitselector_13_out, bitselector_14_out, bitselector_15_out, bitselector_16_out,
       bitselector_17_out, bitselector_18_out, bitselector_19_out, bitselector_20_out, bitselector_21_out,
       bitselector_22_out, bitselector_23_out, bitselector_24_out, bitselector_25_out, bitselector_26_out;
  wire [5:0] subtractor_1_out, subtractor_2_out, subtractor_3_out, subtractor_4_out, subtractor_5_out,
       subtractor_6_out, subtractor_7_out, subtractor_8_out, subtractor_9_out, subtractor_10_out,
       subtractor_11_out, subtractor_12_out, subtractor_13_out, subtractor_14_out, subtractor_15_out,
       subtractor_16_out, subtractor_17_out, subtractor_18_out, subtractor_19_out, subtractor_20_out,
       subtractor_21_out, subtractor_22_out, subtractor_23_out, subtractor_24_out, subtractor_25_out,
       subtractor_26_out;

  Subtractor #(.width(6)) subtractor_1 (.a(shift), .b(6'b000001), .out(subtractor_1_out));  // open: bin, bout
  BitSelector #(.width(64)) bitselector_1 (.in(number), .out(sticky), .sel(subtractor_1_out));
  Subtractor #(.width(6)) subtractor_2 (
    .a(subtractor_1_out), .b(6'b000001), .out(subtractor_2_out));  // open: bin, bout
  Subtractor #(.width(6)) subtractor_3 (
    .a(subtractor_1_out), .b(6'b000010), .out(subtractor_3_out));  // open: bin, bout
  Subtractor #(.width(6)) subtractor_4 (
    .a(subtractor_1_out), .b(6'b000011), .out(subtractor_4_out));  // open: bin, bout
  Subtractor #(.width(6)) subtractor_5 (
    .a(subtractor_1_out), .b(6'b000100), .out(subtractor_5_out));  // open: bin, bout
  Subtractor #(.width(6)) subtractor_6 (
    .a(subtractor_1_out), .b(6'b000101), .out(subtractor_6_out));  // open: bin, bout
  Subtractor #(.width(6)) subtractor_7 (
    .a(subtractor_1_out), .b(6'b000110), .out(subtractor_7_out));  // open: bin, bout
  Subtractor #(.width(6)) subtractor_8 (
    .a(subtractor_1_out), .b(6'b000111), .out(subtractor_8_out));  // open: bin, bout
  Subtractor #(.width(6)) subtractor_9 (
    .a(subtractor_1_out), .b(6'b001000), .out(subtractor_9_out));  // open: bin, bout
  Subtractor #(.width(6)) subtractor_10 (
    .a(subtractor_1_out), .b(6'b001001), .out(subtractor_10_out));  // open: bin, bout
  Subtractor #(.width(6)) subtractor_11 (
    .a(subtractor_1_out), .b(6'b001010), .out(subtractor_11_out));  // open: bin, bout
  Subtractor #(.width(6)) subtractor_12 (
    .a(subtractor_1_out), .b(6'b001011), .out(subtractor_12_out));  // open: bin, bout
  Subtractor #(.width(6)) subtractor_13 (
    .a(subtractor_1_out), .b(6'b001100), .out(subtractor_13_out));  // open: bin, bout
  Subtractor #(.width(6)) subtractor_14 (
    .a(subtractor_1_out), .b(6'b001101), .out(subtractor_14_out));  // open: bin, bout
  Subtractor #(.width(6)) subtractor_15 (
    .a(subtractor_1_out), .b(6'b001110), .out(subtractor_15_out));  // open: bin, bout
  Subtractor #(.width(6)) subtractor_16 (
    .a(subtractor_1_out), .b(6'b001111), .out(subtractor_16_out));  // open: bin, bout
  Subtractor #(.width(6)) subtractor_17 (
    .a(subtractor_1_out), .b(6'b010000), .out(subtractor_17_out));  // open: bin, bout
  Subtractor #(.width(6)) subtractor_18 (
    .a(subtractor_1_out), .b(6'b010001), .out(subtractor_18_out));  // open: bin, bout
  Subtractor #(.width(6)) subtractor_19 (
    .a(subtractor_1_out), .b(6'b010010), .out(subtractor_19_out));  // open: bin, bout
  Subtractor #(.width(6)) subtractor_20 (
    .a(subtractor_1_out), .b(6'b010011), .out(subtractor_20_out));  // open: bin, bout
  Subtractor #(.width(6)) subtractor_21 (
    .a(subtractor_1_out), .b(6'b010100), .out(subtractor_21_out));  // open: bin, bout
  Subtractor #(.width(6)) subtractor_22 (
    .a(subtractor_1_out), .b(6'b010101), .out(subtractor_22_out));  // open: bin, bout
  Subtractor #(.width(6)) subtractor_23 (
    .a(subtractor_1_out), .b(6'b010110), .out(subtractor_23_out));  // open: bin, bout
  Subtractor #(.width(6)) subtractor_24 (
    .a(subtractor_1_out), .b(6'b010111), .out(subtractor_24_out));  // open: bin, bout
  Subtractor #(.width(6)) subtractor_25 (
    .a(subtractor_1_out), .b(6'b011000), .out(subtractor_25_out));  // open: bin, bout
  Subtractor #(.width(6)) subtractor_26 (
    .a(subtractor_1_out), .b(6'b011001), .out(subtractor_26_out));  // open: bin, bout
  BitSelector #(.width(64)) bitselector_2 (.in(number), .out(bitselector_2_out), .sel(subtractor_2_out));
  BitSelector #(.width(64)) bitselector_3 (.in(number), .out(bitselector_3_out), .sel(subtractor_3_out));
  BitSelector #(.width(64)) bitselector_4 (.in(number), .out(bitselector_4_out), .sel(subtractor_4_out));
  BitSelector #(.width(64)) bitselector_5 (.in(number), .out(bitselector_5_out), .sel(subtractor_5_out));
  BitSelector #(.width(64)) bitselector_6 (.in(number), .out(bitselector_6_out), .sel(subtractor_6_out));
  BitSelector #(.width(64)) bitselector_7 (.in(number), .out(bitselector_7_out), .sel(subtractor_7_out));
  BitSelector #(.width(64)) bitselector_8 (.in(number), .out(bitselector_8_out), .sel(subtractor_8_out));
  BitSelector #(.width(64)) bitselector_9 (.in(number), .out(bitselector_9_out), .sel(subtractor_9_out));
  BitSelector #(.width(64)) bitselector_10 (.in(number), .out(bitselector_10_out), .sel(subtractor_10_out));
  BitSelector #(.width(64)) bitselector_11 (.in(number), .out(bitselector_11_out), .sel(subtractor_11_out));
  BitSelector #(.width(64)) bitselector_12 (.in(number), .out(bitselector_12_out), .sel(subtractor_12_out));
  BitSelector #(.width(64)) bitselector_13 (.in(number), .out(bitselector_13_out), .sel(subtractor_13_out));
  BitSelector #(.width(64)) bitselector_14 (.in(number), .out(bitselector_14_out), .sel(subtractor_14_out));
  BitSelector #(.width(64)) bitselector_15 (.in(number), .out(bitselector_15_out), .sel(subtractor_15_out));
  BitSelector #(.width(64)) bitselector_16 (.in(number), .out(bitselector_16_out), .sel(subtractor_16_out));
  BitSelector #(.width(64)) bitselector_17 (.in(number), .out(bitselector_17_out), .sel(subtractor_17_out));
  BitSelector #(.width(64)) bitselector_18 (.in(number), .out(bitselector_18_out), .sel(subtractor_18_out));
  BitSelector #(.width(64)) bitselector_19 (.in(number), .out(bitselector_19_out), .sel(subtractor_19_out));
  BitSelector #(.width(64)) bitselector_20 (.in(number), .out(bitselector_20_out), .sel(subtractor_20_out));
  BitSelector #(.width(64)) bitselector_21 (.in(number), .out(bitselector_21_out), .sel(subtractor_21_out));
  BitSelector #(.width(64)) bitselector_22 (.in(number), .out(bitselector_22_out), .sel(subtractor_22_out));
  BitSelector #(.width(64)) bitselector_23 (.in(number), .out(bitselector_23_out), .sel(subtractor_23_out));
  BitSelector #(.width(64)) bitselector_24 (.in(number), .out(bitselector_24_out), .sel(subtractor_24_out));
  BitSelector #(.width(64)) bitselector_25 (.in(number), .out(bitselector_25_out), .sel(subtractor_25_out));
  BitSelector #(.width(64)) bitselector_26 (.in(number), .out(bitselector_26_out), .sel(subtractor_26_out));
  or or_1 (s, bitselector_2_out, bitselector_3_out, bitselector_4_out, bitselector_5_out, bitselector_6_out, bitselector_7_out, bitselector_8_out, bitselector_9_out, bitselector_10_out, bitselector_11_out, bitselector_12_out, bitselector_13_out, bitselector_14_out, bitselector_15_out, bitselector_16_out, bitselector_17_out, bitselector_18_out, bitselector_19_out, bitselector_20_out, bitselector_21_out, bitselector_22_out, bitselector_23_out, bitselector_24_out, bitselector_25_out, bitselector_26_out);

  // Other names for the same wires on the sheet: for_round[63:0] = number; shift_for_normalize_2[5:0] = shift
endmodule

module substract (
  input  [22:0] fraction_b,
  input  sub_normal_b,
  input  [22:0] fraction_a,
  input  [7:0] exponent_a,
  input  [7:0] exponent_b,
  output [22:0] fraction_result,
  output [7:0] exponent_result
);

  wire adder_4_cout, and_3_out, and_4_out, and_5_out, and_6_out, bit1, bitselector_1_out, bitselector_3_out,
       bitselector_4_out, bitselector_5_out, bitselector_6_out, bitselector_7_out, bitselector_8_out,
       bitselector_9_out, bitselector_10_out, bitselector_11_out, bitselector_12_out, bitselector_13_out,
       bitselector_14_out, bitselector_15_out, bitselector_16_out, bitselector_17_out, bitselector_18_out,
       bitselector_19_out, bitselector_20_out, bitselector_21_out, bitselector_22_out, bitselector_23_out,
       bitselector_24_out, bitselector_25_out, bitselector_26_out, bitselector_27_out, bitselector_28_out,
       bitselector_29_out, bitselector_30_out, bitselector_31_out, comparator_1_gt, comparator_2_eq,
       comparator_3_eq, comparator_4_eq, comparator_5_eq, not_2_out, not_3_out, or_2_out, sticky, t2;
  wire [4:0] v13_res;
  wire [5:0] adder_1_out, adder_2_out, adder_3_out, and_1_out, and_2_out, shift_for_normalize_2,
       subtractor_6_out, subtractor_9_out, subtractor_10_out, subtractor_11_out, subtractor_12_out,
       subtractor_13_out, subtractor_14_out, subtractor_15_out, subtractor_16_out, subtractor_17_out,
       subtractor_18_out, subtractor_19_out, subtractor_20_out, subtractor_21_out, subtractor_22_out,
       subtractor_23_out, subtractor_24_out, subtractor_25_out, subtractor_26_out, subtractor_27_out,
       subtractor_28_out, subtractor_29_out, subtractor_30_out, subtractor_31_out, subtractor_32_out,
       subtractor_33_out, subtractor_34_out;
  wire [7:0] adder_5_out, bit_extender_6_out, exponent_not_end, k1, subtractor_1_out, subtractor_3_out,
       subtractor_5_out;
  wire [22:0] adder_4_out, fraction_after_shift, fraction_result_2, multiplexer_6_out;
  wire [23:0] fraction_sub_result_2;
  wire [25:0] k13;
  wire [31:0] bit_extender_1_out, bit_extender_3_out, bit_extender_4_out, bit_extender_5_out, f21, f22,
       multiplexer_2_out, shift_num_2, subtractor_2_out, subtractor_4_out, subtractor_7_out;
  wire [31:26] v14_res_low;
  wire [40:0] multiplexer_9_out;
  wire [63:0] f_b_new, for_round, multiplexer_4_out, multiplexer_7_out, multiplexer_8_out, shifter_1_out,
       shifter_2_out, shifter_3_out, shifter_4_out, shifter_5_out, shifter_6_out;

  Subtractor subtractor_1 (.a(exponent_a), .b(exponent_b), .out(subtractor_1_out));  // open: bin, bout
  assign bit_extender_1_out = {{24{1'b0}}, subtractor_1_out};  // Bit_Extender bit_extender_1
  Subtractor #(.width(32)) subtractor_2 (.a(bit_extender_1_out), .b(32'h1), .out(subtractor_2_out));  // open: bin, bout
  Subtractor subtractor_3 (.a(exponent_a), .b(exponent_b), .out(subtractor_3_out));  // open: bin, bout
  assign f21 = {{8{1'b0}}, {sub_normal_b, fraction_b}};  // Bit_Extender bit_extender_2
  Multiplexer #(.width(32)) multiplexer_1 (
    .in0(subtractor_2_out), .in1(bit_extender_1_out), .out(shift_num_2), .sel(sub_normal_b));
  assign bit_extender_3_out = {{24{1'b0}}, subtractor_3_out};  // Bit_Extender bit_extender_3
  Subtractor #(.width(32)) subtractor_4 (.a(bit_extender_3_out), .b(32'h1), .out(subtractor_4_out));  // open: bin, bout
  Subtractor subtractor_5 (.a(exponent_a), .b(exponent_b), .out(subtractor_5_out));  // open: bin, bout
  Multiplexer #(.width(32)) multiplexer_2 (
    .in0(subtractor_4_out), .in1(bit_extender_3_out), .out(multiplexer_2_out), .sel(sub_normal_b));
  Comparator comparator_1 (.a(subtractor_5_out), .b(8'h28), .gt(comparator_1_gt));  // open: eq, lt
  SRL_fadd v12 (.a(f21), .b(shift_num_2), .res_low(f22));  // open: one_signal
  Subtractor #(.width(6)) subtractor_6 (
    .a(multiplexer_2_out[5:0]), .b(6'b000001), .out(subtractor_6_out));  // open: bin, bout
  assign and_1_out = multiplexer_2_out[5:0] & 6'b000001;  // AND_Gate and_1, 6 bits wide
  Shifter #(.shift("lr"), .width(64)) shifter_1 (
    .in({sub_normal_b, fraction_b, {40{1'b0}}}), .\dist (subtractor_6_out), .out(shifter_1_out));
  Shifter #(.shift("lr"), .width(64)) shifter_2 (
    .in({sub_normal_b, fraction_b, {40{1'b0}}}), .\dist (multiplexer_2_out[5:0]), .out(shifter_2_out));
  BitSelector #(.width(6)) bitselector_1 (.in(and_1_out), .out(bitselector_1_out), .sel(3'b000));
  Adder #(.width(6)) adder_1 (.a(shift_for_normalize_2), .b(6'b000001), .out(adder_1_out));  // open: cin, cout
  Shifter #(.shift("lr"), .width(64)) shifter_3 (.in(shifter_1_out), .\dist (6'b000001), .out(shifter_3_out));
  Comparator #(.width(6)) comparator_2 (
    .a(multiplexer_2_out[5:0]), .b({6{1'b0}}), .eq(comparator_2_eq));  // open: gt, lt
  assign bit_extender_4_out = {{26{1'b0}}, adder_1_out};  // Bit_Extender bit_extender_4
  Multiplexer #(.width(64)) multiplexer_3 (
    .in0(multiplexer_4_out), .in1(shifter_2_out), .out(f_b_new), .sel(bitselector_1_out));
  Multiplexer #(.width(64)) multiplexer_4 (
    .in0(shifter_3_out), .in1({sub_normal_b, fraction_b, {40{1'b0}}}), .out(multiplexer_4_out),
    .sel(comparator_2_eq));
  Multiplexer #(.width(23)) multiplexer_5 (
    .in0(fraction_result_2), .in1(fraction_a), .out(fraction_result), .sel(comparator_1_gt));
  SLLL v14 (.a({fraction_sub_result_2, k1}), .b(bit_extender_4_out), .res_low({v14_res_low, k13}));  // open: res_high
  bitOne v13 (.a(fraction_sub_result_2), .res(v13_res));
  Subtractor #(.width(64)) subtractor_7 (
    .a({1'b1, fraction_a, {40{1'b0}}}), .b(f_b_new), .out({fraction_sub_result_2, k1, subtractor_7_out}));  // open: bin, bout
  Adder #(.width(6)) adder_2 (.a(shift_for_normalize_2), .b(6'b000001), .out(adder_2_out));  // open: cin, cout
  Subtractor #(.width(6)) subtractor_8 (
    .a(6'b011000), .b({1'b0, v13_res}), .out(shift_for_normalize_2));  // open: bin, bout
  assign bit_extender_5_out = {{26{1'b0}}, adder_2_out};  // Bit_Extender bit_extender_5
  Adder #(.width(6)) adder_3 (.a(shift_for_normalize_2), .b(6'b100111), .out(adder_3_out));  // open: cin, cout
  not not_1 (t2, comparator_3_eq);
  Comparator #(.width(6)) comparator_3 (
    .a(shift_for_normalize_2), .b({6{1'b0}}), .eq(comparator_3_eq));  // open: gt, lt
  BitSelector #(.width(64)) bitselector_2 (.in(for_round), .out(sticky), .sel(adder_3_out));
  Subtractor #(.width(6)) subtractor_9 (.a(adder_3_out), .b(6'b000001), .out(subtractor_9_out));  // open: bin, bout
  Subtractor #(.width(6)) subtractor_10 (.a(adder_3_out), .b(6'b000010), .out(subtractor_10_out));  // open: bin, bout
  Subtractor #(.width(6)) subtractor_11 (.a(adder_3_out), .b(6'b000011), .out(subtractor_11_out));  // open: bin, bout
  Subtractor #(.width(6)) subtractor_12 (.a(adder_3_out), .b(6'b000100), .out(subtractor_12_out));  // open: bin, bout
  Subtractor #(.width(6)) subtractor_13 (.a(adder_3_out), .b(6'b000101), .out(subtractor_13_out));  // open: bin, bout
  Subtractor #(.width(6)) subtractor_14 (.a(adder_3_out), .b(6'b000110), .out(subtractor_14_out));  // open: bin, bout
  Subtractor #(.width(6)) subtractor_15 (.a(adder_3_out), .b(6'b000111), .out(subtractor_15_out));  // open: bin, bout
  Subtractor #(.width(6)) subtractor_16 (.a(adder_3_out), .b(6'b001000), .out(subtractor_16_out));  // open: bin, bout
  Subtractor #(.width(6)) subtractor_17 (.a(adder_3_out), .b(6'b001001), .out(subtractor_17_out));  // open: bin, bout
  Subtractor #(.width(6)) subtractor_18 (.a(adder_3_out), .b(6'b001010), .out(subtractor_18_out));  // open: bin, bout
  Subtractor #(.width(6)) subtractor_19 (.a(adder_3_out), .b(6'b001011), .out(subtractor_19_out));  // open: bin, bout
  Subtractor #(.width(6)) subtractor_20 (.a(adder_3_out), .b(6'b001100), .out(subtractor_20_out));  // open: bin, bout
  Subtractor #(.width(6)) subtractor_21 (.a(adder_3_out), .b(6'b001101), .out(subtractor_21_out));  // open: bin, bout
  Subtractor #(.width(6)) subtractor_22 (.a(adder_3_out), .b(6'b001110), .out(subtractor_22_out));  // open: bin, bout
  Subtractor #(.width(6)) subtractor_23 (.a(adder_3_out), .b(6'b001111), .out(subtractor_23_out));  // open: bin, bout
  Subtractor #(.width(6)) subtractor_24 (.a(adder_3_out), .b(6'b010000), .out(subtractor_24_out));  // open: bin, bout
  Subtractor #(.width(6)) subtractor_25 (.a(adder_3_out), .b(6'b010001), .out(subtractor_25_out));  // open: bin, bout
  Subtractor #(.width(6)) subtractor_26 (.a(adder_3_out), .b(6'b010010), .out(subtractor_26_out));  // open: bin, bout
  Subtractor #(.width(6)) subtractor_27 (.a(adder_3_out), .b(6'b010011), .out(subtractor_27_out));  // open: bin, bout
  Subtractor #(.width(6)) subtractor_28 (.a(adder_3_out), .b(6'b010100), .out(subtractor_28_out));  // open: bin, bout
  Subtractor #(.width(6)) subtractor_29 (.a(adder_3_out), .b(6'b010101), .out(subtractor_29_out));  // open: bin, bout
  Subtractor #(.width(6)) subtractor_30 (.a(adder_3_out), .b(6'b010110), .out(subtractor_30_out));  // open: bin, bout
  Subtractor #(.width(6)) subtractor_31 (.a(adder_3_out), .b(6'b010111), .out(subtractor_31_out));  // open: bin, bout
  Subtractor #(.width(6)) subtractor_32 (.a(adder_3_out), .b(6'b011000), .out(subtractor_32_out));  // open: bin, bout
  Subtractor #(.width(6)) subtractor_33 (.a(adder_3_out), .b(6'b011001), .out(subtractor_33_out));  // open: bin, bout
  assign and_2_out = bit_extender_5_out[5:0] & 6'b000001;  // AND_Gate and_2, 6 bits wide
  BitSelector #(.width(64)) bitselector_3 (.in(for_round), .out(bitselector_3_out), .sel(subtractor_9_out));
  BitSelector #(.width(64)) bitselector_4 (.in(for_round), .out(bitselector_4_out), .sel(subtractor_10_out));
  BitSelector #(.width(64)) bitselector_5 (.in(for_round), .out(bitselector_5_out), .sel(subtractor_11_out));
  BitSelector #(.width(64)) bitselector_6 (.in(for_round), .out(bitselector_6_out), .sel(subtractor_12_out));
  BitSelector #(.width(64)) bitselector_7 (.in(for_round), .out(bitselector_7_out), .sel(subtractor_13_out));
  BitSelector #(.width(64)) bitselector_8 (.in(for_round), .out(bitselector_8_out), .sel(subtractor_14_out));
  BitSelector #(.width(64)) bitselector_9 (.in(for_round), .out(bitselector_9_out), .sel(subtractor_15_out));
  BitSelector #(.width(64)) bitselector_10 (.in(for_round), .out(bitselector_10_out), .sel(subtractor_16_out));
  BitSelector #(.width(64)) bitselector_11 (.in(for_round), .out(bitselector_11_out), .sel(subtractor_17_out));
  BitSelector #(.width(64)) bitselector_12 (.in(for_round), .out(bitselector_12_out), .sel(subtractor_18_out));
  BitSelector #(.width(64)) bitselector_13 (.in(for_round), .out(bitselector_13_out), .sel(subtractor_19_out));
  BitSelector #(.width(64)) bitselector_14 (.in(for_round), .out(bitselector_14_out), .sel(subtractor_20_out));
  BitSelector #(.width(64)) bitselector_15 (.in(for_round), .out(bitselector_15_out), .sel(subtractor_21_out));
  BitSelector #(.width(64)) bitselector_16 (.in(for_round), .out(bitselector_16_out), .sel(subtractor_22_out));
  BitSelector #(.width(64)) bitselector_17 (.in(for_round), .out(bitselector_17_out), .sel(subtractor_23_out));
  BitSelector #(.width(64)) bitselector_18 (.in(for_round), .out(bitselector_18_out), .sel(subtractor_24_out));
  BitSelector #(.width(64)) bitselector_19 (.in(for_round), .out(bitselector_19_out), .sel(subtractor_25_out));
  BitSelector #(.width(64)) bitselector_20 (.in(for_round), .out(bitselector_20_out), .sel(subtractor_26_out));
  BitSelector #(.width(64)) bitselector_21 (.in(for_round), .out(bitselector_21_out), .sel(subtractor_27_out));
  BitSelector #(.width(64)) bitselector_22 (.in(for_round), .out(bitselector_22_out), .sel(subtractor_28_out));
  BitSelector #(.width(64)) bitselector_23 (.in(for_round), .out(bitselector_23_out), .sel(subtractor_29_out));
  BitSelector #(.width(64)) bitselector_24 (.in(for_round), .out(bitselector_24_out), .sel(subtractor_30_out));
  BitSelector #(.width(64)) bitselector_25 (.in(for_round), .out(bitselector_25_out), .sel(subtractor_31_out));
  BitSelector #(.width(64)) bitselector_26 (.in(for_round), .out(bitselector_26_out), .sel(subtractor_32_out));
  BitSelector #(.width(64)) bitselector_27 (.in(for_round), .out(bitselector_27_out), .sel(subtractor_33_out));
  Subtractor #(.width(6)) subtractor_34 (
    .a(bit_extender_5_out[5:0]), .b(6'b000001), .out(subtractor_34_out));  // open: bin, bout
  Shifter #(.width(64)) shifter_4 (
    .in({fraction_sub_result_2, k1, subtractor_7_out}), .\dist (bit_extender_5_out[5:0]), .out(shifter_4_out));
  BitSelector #(.width(6)) bitselector_28 (.in(and_2_out), .out(bitselector_28_out), .sel(3'b000));
  Shifter #(.width(64)) shifter_5 (
    .in({fraction_sub_result_2, k1, subtractor_7_out}), .\dist (subtractor_34_out), .out(shifter_5_out));
  Multiplexer #(.width(23)) multiplexer_6 (
    .in0(fraction_sub_result_2[22:0]), .in1(fraction_after_shift), .out(multiplexer_6_out), .sel(t2));
  Shifter #(.width(64)) shifter_6 (.in(shifter_5_out), .\dist (6'b000001), .out(shifter_6_out));
  Multiplexer #(.width(64)) multiplexer_7 (
    .in0(shifter_6_out), .in1({fraction_sub_result_2, k1, subtractor_7_out}), .out(multiplexer_7_out),
    .sel(comparator_4_eq));
  Comparator #(.width(6)) comparator_4 (
    .a(bit_extender_5_out[5:0]), .b({6{1'b0}}), .eq(comparator_4_eq));  // open: gt, lt
  Multiplexer #(.width(64)) multiplexer_8 (
    .in0(multiplexer_7_out), .in1(shifter_4_out), .out(multiplexer_8_out), .sel(bitselector_28_out));
  Comparator #(.width(6)) comparator_5 (
    .a(shift_for_normalize_2), .b({6{1'b0}}), .eq(comparator_5_eq));  // open: gt, lt
  or or_1 (bit1, bitselector_3_out, bitselector_4_out, bitselector_5_out, bitselector_6_out, bitselector_7_out, bitselector_8_out, bitselector_9_out, bitselector_10_out, bitselector_11_out, bitselector_12_out, bitselector_13_out, bitselector_14_out, bitselector_15_out, bitselector_16_out, bitselector_17_out, bitselector_18_out, bitselector_19_out, bitselector_20_out, bitselector_21_out, bitselector_22_out, bitselector_23_out, bitselector_24_out, bitselector_25_out, bitselector_26_out, bitselector_27_out);
  BitSelector #(.width(23)) bitselector_29 (.in(multiplexer_6_out), .out(bitselector_29_out), .sel({5{1'b0}}));
  BitSelector #(.width(23)) bitselector_30 (.in(multiplexer_6_out), .out(bitselector_30_out), .sel({5{1'b0}}));
  BitSelector #(.width(23)) bitselector_31 (.in(multiplexer_6_out), .out(bitselector_31_out), .sel({5{1'b0}}));
  Multiplexer #(.width(64)) multiplexer_9 (
    .in0(multiplexer_8_out), .in1({fraction_sub_result_2, k1, subtractor_7_out}),
    .out({fraction_after_shift, multiplexer_9_out}), .sel(comparator_5_eq));
  Adder #(.width(23)) adder_4 (.a(multiplexer_6_out), .b(23'h1), .out(adder_4_out), .cout(adder_4_cout));  // open: cin
  not not_2 (not_2_out, bit1);
  not not_3 (not_3_out, bitselector_30_out);
  Multiplexer #(.width(23)) multiplexer_10 (
    .in0(multiplexer_6_out), .in1(adder_4_out), .out(fraction_result_2), .sel(or_2_out));
  and and_3 (and_3_out, sticky, bitselector_29_out, not_2_out);
  and and_4 (and_4_out, sticky, not_3_out, bit1);
  and and_5 (and_5_out, sticky, bitselector_31_out, bit1);
  or or_2 (or_2_out, and_3_out, and_5_out, and_4_out);
  and and_6 (and_6_out, or_2_out, adder_4_cout);
  Subtractor #(.width(64)) subtractor_35 (
    .a({fraction_after_shift, multiplexer_9_out}), .b({fraction_after_shift, {41{1'b0}}}), .out(for_round));  // open: bin, bout
  Adder adder_5 (.a(exponent_not_end), .b(8'h1), .out(adder_5_out));  // open: cin, cout
  assign bit_extender_6_out = {{2{1'b0}}, shift_for_normalize_2};  // Bit_Extender bit_extender_6
  Multiplexer #(.width(8)) multiplexer_11 (
    .in0(exponent_not_end), .in1(adder_5_out), .out(exponent_result), .sel(and_6_out));
  Subtractor subtractor_36 (.a(exponent_a), .b(bit_extender_6_out), .out(exponent_not_end));  // open: bin, bout

  // Other names for the same wires on the sheet: z1[23:0] = {sub_normal_b, fraction_b}; subnormal_b = sub_normal_b;
  //   fraction_without_normalize_2[23:0] = fraction_sub_result_2; k1[31:8] = fraction_sub_result_2;
  //   exponent_result_2[7:0] = exponent_result; fraction_b_2[23:0] = f22[23:0]
endmodule

module find_msb (
  input  [63:0] input1,
  output [7:0] result_msb
);

  wire bitselector_1_out, bitselector_2_out, bitselector_3_out, bitselector_4_out, bitselector_5_out,
       bitselector_6_out, bitselector_7_out, bitselector_8_out, bitselector_9_out, bitselector_10_out,
       bitselector_11_out, bitselector_12_out, bitselector_13_out, bitselector_14_out, bitselector_15_out,
       bitselector_16_out, bitselector_17_out, bitselector_18_out, bitselector_19_out, bitselector_20_out,
       bitselector_21_out, bitselector_22_out, bitselector_23_out, bitselector_24_out, bitselector_25_out,
       bitselector_26_out, bitselector_27_out, bitselector_28_out, bitselector_29_out, bitselector_30_out,
       bitselector_31_out, bitselector_32_out, bitselector_33_out, bitselector_34_out, bitselector_35_out,
       bitselector_36_out, bitselector_37_out, bitselector_38_out, bitselector_39_out, bitselector_40_out,
       bitselector_41_out, bitselector_42_out, bitselector_43_out, bitselector_44_out, bitselector_45_out,
       bitselector_46_out, bitselector_47_out, bitselector_48_out;
  wire [5:0] multiplexer_1_out, multiplexer_2_out, multiplexer_3_out, multiplexer_4_out, multiplexer_5_out,
       multiplexer_6_out, multiplexer_7_out, multiplexer_8_out, multiplexer_9_out, multiplexer_10_out,
       multiplexer_11_out, multiplexer_12_out, multiplexer_13_out, multiplexer_14_out, multiplexer_15_out,
       multiplexer_16_out, multiplexer_17_out, multiplexer_18_out, multiplexer_19_out, multiplexer_20_out,
       multiplexer_21_out, multiplexer_22_out, multiplexer_23_out, multiplexer_24_out, multiplexer_25_out,
       multiplexer_26_out, multiplexer_27_out, multiplexer_28_out, multiplexer_29_out, multiplexer_30_out,
       multiplexer_31_out, multiplexer_32_out, multiplexer_33_out, multiplexer_34_out, multiplexer_35_out,
       multiplexer_36_out, multiplexer_37_out, multiplexer_38_out, multiplexer_39_out, multiplexer_40_out,
       multiplexer_41_out, multiplexer_42_out, multiplexer_43_out, multiplexer_44_out, multiplexer_45_out,
       multiplexer_46_out, multiplexer_47_out;

  Multiplexer #(.width(6)) multiplexer_1 (
    .in0(6'b111110), .in1(6'b101110), .out(multiplexer_1_out), .sel(bitselector_1_out));
  BitSelector #(.width(64)) bitselector_1 (.in(input1), .out(bitselector_1_out), .sel({6{1'b0}}));
  BitSelector #(.width(64)) bitselector_2 (.in(input1), .out(bitselector_2_out), .sel(6'b000001));
  Multiplexer #(.width(6)) multiplexer_2 (
    .in0(multiplexer_1_out), .in1(6'b101101), .out(multiplexer_2_out), .sel(bitselector_2_out));
  Multiplexer #(.width(6)) multiplexer_3 (
    .in0(multiplexer_2_out), .in1(6'b101100), .out(multiplexer_3_out), .sel(bitselector_3_out));
  BitSelector #(.width(64)) bitselector_3 (.in(input1), .out(bitselector_3_out), .sel(6'b000010));
  Multiplexer #(.width(6)) multiplexer_4 (
    .in0(multiplexer_3_out), .in1(6'b101011), .out(multiplexer_4_out), .sel(bitselector_4_out));
  BitSelector #(.width(64)) bitselector_4 (.in(input1), .out(bitselector_4_out), .sel(6'b000011));
  BitSelector #(.width(64)) bitselector_5 (.in(input1), .out(bitselector_5_out), .sel(6'b000100));
  Multiplexer #(.width(6)) multiplexer_5 (
    .in0(multiplexer_4_out), .in1(6'b101010), .out(multiplexer_5_out), .sel(bitselector_5_out));
  Multiplexer #(.width(6)) multiplexer_6 (
    .in0(multiplexer_5_out), .in1(6'b101001), .out(multiplexer_6_out), .sel(bitselector_6_out));
  BitSelector #(.width(64)) bitselector_6 (.in(input1), .out(bitselector_6_out), .sel(6'b000101));
  Multiplexer #(.width(6)) multiplexer_7 (
    .in0(multiplexer_6_out), .in1(6'b101000), .out(multiplexer_7_out), .sel(bitselector_7_out));
  BitSelector #(.width(64)) bitselector_7 (.in(input1), .out(bitselector_7_out), .sel(6'b000110));
  Multiplexer #(.width(6)) multiplexer_8 (
    .in0(multiplexer_7_out), .in1(6'b100111), .out(multiplexer_8_out), .sel(bitselector_8_out));
  BitSelector #(.width(64)) bitselector_8 (.in(input1), .out(bitselector_8_out), .sel(6'b000111));
  BitSelector #(.width(64)) bitselector_9 (.in(input1), .out(bitselector_9_out), .sel(6'b001000));
  Multiplexer #(.width(6)) multiplexer_9 (
    .in0(multiplexer_8_out), .in1(6'b100110), .out(multiplexer_9_out), .sel(bitselector_9_out));
  Multiplexer #(.width(6)) multiplexer_10 (
    .in0(multiplexer_9_out), .in1(6'b100101), .out(multiplexer_10_out), .sel(bitselector_10_out));
  BitSelector #(.width(64)) bitselector_10 (.in(input1), .out(bitselector_10_out), .sel(6'b001001));
  Multiplexer #(.width(6)) multiplexer_11 (
    .in0(multiplexer_10_out), .in1(6'b100100), .out(multiplexer_11_out), .sel(bitselector_11_out));
  BitSelector #(.width(64)) bitselector_11 (.in(input1), .out(bitselector_11_out), .sel(6'b001010));
  Multiplexer #(.width(6)) multiplexer_12 (
    .in0(multiplexer_11_out), .in1(6'b100011), .out(multiplexer_12_out), .sel(bitselector_12_out));
  BitSelector #(.width(64)) bitselector_12 (.in(input1), .out(bitselector_12_out), .sel(6'b001011));
  Multiplexer #(.width(6)) multiplexer_13 (
    .in0(multiplexer_12_out), .in1(6'b100010), .out(multiplexer_13_out), .sel(bitselector_13_out));
  BitSelector #(.width(64)) bitselector_13 (.in(input1), .out(bitselector_13_out), .sel(6'b001100));
  BitSelector #(.width(64)) bitselector_14 (.in(input1), .out(bitselector_14_out), .sel(6'b001101));
  Multiplexer #(.width(6)) multiplexer_14 (
    .in0(multiplexer_13_out), .in1(6'b100001), .out(multiplexer_14_out), .sel(bitselector_14_out));
  BitSelector #(.width(64)) bitselector_15 (.in(input1), .out(bitselector_15_out), .sel(6'b001110));
  Multiplexer #(.width(6)) multiplexer_15 (
    .in0(multiplexer_14_out), .in1(6'b100000), .out(multiplexer_15_out), .sel(bitselector_15_out));
  Multiplexer #(.width(6)) multiplexer_16 (
    .in0(multiplexer_15_out), .in1(6'b011111), .out(multiplexer_16_out), .sel(bitselector_16_out));
  BitSelector #(.width(64)) bitselector_16 (.in(input1), .out(bitselector_16_out), .sel(6'b001111));
  Multiplexer #(.width(6)) multiplexer_17 (
    .in0(multiplexer_16_out), .in1(6'b011110), .out(multiplexer_17_out), .sel(bitselector_17_out));
  BitSelector #(.width(64)) bitselector_17 (.in(input1), .out(bitselector_17_out), .sel(6'b010000));
  BitSelector #(.width(64)) bitselector_18 (.in(input1), .out(bitselector_18_out), .sel(6'b010001));
  Multiplexer #(.width(6)) multiplexer_18 (
    .in0(multiplexer_17_out), .in1(6'b011101), .out(multiplexer_18_out), .sel(bitselector_18_out));
  Multiplexer #(.width(6)) multiplexer_19 (
    .in0(multiplexer_18_out), .in1(6'b011100), .out(multiplexer_19_out), .sel(bitselector_19_out));
  BitSelector #(.width(64)) bitselector_19 (.in(input1), .out(bitselector_19_out), .sel(6'b010010));
  Multiplexer #(.width(6)) multiplexer_20 (
    .in0(multiplexer_19_out), .in1(6'b011011), .out(multiplexer_20_out), .sel(bitselector_20_out));
  BitSelector #(.width(64)) bitselector_20 (.in(input1), .out(bitselector_20_out), .sel(6'b010011));
  Multiplexer #(.width(6)) multiplexer_21 (
    .in0(multiplexer_20_out), .in1(6'b011010), .out(multiplexer_21_out), .sel(bitselector_21_out));
  BitSelector #(.width(64)) bitselector_21 (.in(input1), .out(bitselector_21_out), .sel(6'b010100));
  Multiplexer #(.width(6)) multiplexer_22 (
    .in0(multiplexer_21_out), .in1(6'b011001), .out(multiplexer_22_out), .sel(bitselector_22_out));
  BitSelector #(.width(64)) bitselector_22 (.in(input1), .out(bitselector_22_out), .sel(6'b010101));
  Multiplexer #(.width(6)) multiplexer_23 (
    .in0(multiplexer_22_out), .in1(6'b011000), .out(multiplexer_23_out), .sel(bitselector_23_out));
  BitSelector #(.width(64)) bitselector_23 (.in(input1), .out(bitselector_23_out), .sel(6'b010110));
  BitSelector #(.width(64)) bitselector_24 (.in(input1), .out(bitselector_24_out), .sel(6'b010111));
  Multiplexer #(.width(6)) multiplexer_24 (
    .in0(multiplexer_23_out), .in1(6'b010111), .out(multiplexer_24_out), .sel(bitselector_24_out));
  Multiplexer #(.width(6)) multiplexer_25 (
    .in0(multiplexer_24_out), .in1(6'b010110), .out(multiplexer_25_out), .sel(bitselector_25_out));
  BitSelector #(.width(64)) bitselector_25 (.in(input1), .out(bitselector_25_out), .sel(6'b011000));
  Multiplexer #(.width(6)) multiplexer_26 (
    .in0(multiplexer_25_out), .in1(6'b010101), .out(multiplexer_26_out), .sel(bitselector_26_out));
  BitSelector #(.width(64)) bitselector_26 (.in(input1), .out(bitselector_26_out), .sel(6'b011001));
  BitSelector #(.width(64)) bitselector_27 (.in(input1), .out(bitselector_27_out), .sel(6'b011010));
  Multiplexer #(.width(6)) multiplexer_27 (
    .in0(multiplexer_26_out), .in1(6'b010100), .out(multiplexer_27_out), .sel(bitselector_27_out));
  Multiplexer #(.width(6)) multiplexer_28 (
    .in0(multiplexer_27_out), .in1(6'b010011), .out(multiplexer_28_out), .sel(bitselector_28_out));
  BitSelector #(.width(64)) bitselector_28 (.in(input1), .out(bitselector_28_out), .sel(6'b011011));
  Multiplexer #(.width(6)) multiplexer_29 (
    .in0(multiplexer_28_out), .in1(6'b010010), .out(multiplexer_29_out), .sel(bitselector_29_out));
  BitSelector #(.width(64)) bitselector_29 (.in(input1), .out(bitselector_29_out), .sel(6'b011100));
  Multiplexer #(.width(6)) multiplexer_30 (
    .in0(multiplexer_29_out), .in1(6'b010001), .out(multiplexer_30_out), .sel(bitselector_30_out));
  BitSelector #(.width(64)) bitselector_30 (.in(input1), .out(bitselector_30_out), .sel(6'b011101));
  Multiplexer #(.width(6)) multiplexer_31 (
    .in0(multiplexer_30_out), .in1(6'b010000), .out(multiplexer_31_out), .sel(bitselector_31_out));
  BitSelector #(.width(64)) bitselector_31 (.in(input1), .out(bitselector_31_out), .sel(6'b011110));
  Multiplexer #(.width(6)) multiplexer_32 (
    .in0(multiplexer_31_out), .in1(6'b001111), .out(multiplexer_32_out), .sel(bitselector_32_out));
  BitSelector #(.width(64)) bitselector_32 (.in(input1), .out(bitselector_32_out), .sel(6'b011111));
  Multiplexer #(.width(6)) multiplexer_33 (
    .in0(multiplexer_32_out), .in1(6'b001110), .out(multiplexer_33_out), .sel(bitselector_33_out));
  BitSelector #(.width(64)) bitselector_33 (.in(input1), .out(bitselector_33_out), .sel(6'b100000));
  Multiplexer #(.width(6)) multiplexer_34 (
    .in0(multiplexer_33_out), .in1(6'b001101), .out(multiplexer_34_out), .sel(bitselector_34_out));
  BitSelector #(.width(64)) bitselector_34 (.in(input1), .out(bitselector_34_out), .sel(6'b100001));
  BitSelector #(.width(64)) bitselector_35 (.in(input1), .out(bitselector_35_out), .sel(6'b100010));
  Multiplexer #(.width(6)) multiplexer_35 (
    .in0(multiplexer_34_out), .in1(6'b001100), .out(multiplexer_35_out), .sel(bitselector_35_out));
  Multiplexer #(.width(6)) multiplexer_36 (
    .in0(multiplexer_35_out), .in1(6'b001011), .out(multiplexer_36_out), .sel(bitselector_36_out));
  BitSelector #(.width(64)) bitselector_36 (.in(input1), .out(bitselector_36_out), .sel(6'b100011));
  Multiplexer #(.width(6)) multiplexer_37 (
    .in0(multiplexer_36_out), .in1(6'b001010), .out(multiplexer_37_out), .sel(bitselector_37_out));
  BitSelector #(.width(64)) bitselector_37 (.in(input1), .out(bitselector_37_out), .sel(6'b100100));
  BitSelector #(.width(64)) bitselector_38 (.in(input1), .out(bitselector_38_out), .sel(6'b100101));
  Multiplexer #(.width(6)) multiplexer_38 (
    .in0(multiplexer_37_out), .in1(6'b001001), .out(multiplexer_38_out), .sel(bitselector_38_out));
  Multiplexer #(.width(6)) multiplexer_39 (
    .in0(multiplexer_38_out), .in1(6'b001000), .out(multiplexer_39_out), .sel(bitselector_39_out));
  BitSelector #(.width(64)) bitselector_39 (.in(input1), .out(bitselector_39_out), .sel(6'b100110));
  BitSelector #(.width(64)) bitselector_40 (.in(input1), .out(bitselector_40_out), .sel(6'b100111));
  Multiplexer #(.width(6)) multiplexer_40 (
    .in0(multiplexer_39_out), .in1(6'b000111), .out(multiplexer_40_out), .sel(bitselector_40_out));
  Multiplexer #(.width(6)) multiplexer_41 (
    .in0(multiplexer_40_out), .in1(6'b000110), .out(multiplexer_41_out), .sel(bitselector_41_out));
  BitSelector #(.width(64)) bitselector_41 (.in(input1), .out(bitselector_41_out), .sel(6'b101000));
  Multiplexer #(.width(6)) multiplexer_42 (
    .in0(multiplexer_41_out), .in1(6'b000101), .out(multiplexer_42_out), .sel(bitselector_42_out));
  BitSelector #(.width(64)) bitselector_42 (.in(input1), .out(bitselector_42_out), .sel(6'b101001));
  BitSelector #(.width(64)) bitselector_43 (.in(input1), .out(bitselector_43_out), .sel(6'b101010));
  Multiplexer #(.width(6)) multiplexer_43 (
    .in0(multiplexer_42_out), .in1(6'b000100), .out(multiplexer_43_out), .sel(bitselector_43_out));
  Multiplexer #(.width(6)) multiplexer_44 (
    .in0(multiplexer_43_out), .in1(6'b000011), .out(multiplexer_44_out), .sel(bitselector_44_out));
  BitSelector #(.width(64)) bitselector_44 (.in(input1), .out(bitselector_44_out), .sel(6'b101011));
  Multiplexer #(.width(6)) multiplexer_45 (
    .in0(multiplexer_44_out), .in1(6'b000010), .out(multiplexer_45_out), .sel(bitselector_45_out));
  BitSelector #(.width(64)) bitselector_45 (.in(input1), .out(bitselector_45_out), .sel(6'b101100));
  Multiplexer #(.width(6)) multiplexer_46 (
    .in0(multiplexer_45_out), .in1(6'b000001), .out(multiplexer_46_out), .sel(bitselector_46_out));
  BitSelector #(.width(64)) bitselector_46 (.in(input1), .out(bitselector_46_out), .sel(6'b101101));
  Multiplexer #(.width(6)) multiplexer_47 (
    .in0(multiplexer_46_out), .in1({6{1'b0}}), .out(multiplexer_47_out), .sel(bitselector_47_out));
  BitSelector #(.width(64)) bitselector_47 (.in(input1), .out(bitselector_47_out), .sel(6'b101110));
  Multiplexer #(.width(8)) multiplexer_48 (
    .in0({2'b00, multiplexer_47_out}), .in1({8{1'b1}}), .out(result_msb), .sel(bitselector_48_out));
  BitSelector #(.width(64)) bitselector_48 (.in(input1), .out(bitselector_48_out), .sel(6'b101111));

  // Other names for the same wires on the sheet: in1[63:0] = input1
endmodule

module Calculate_Term_sin (
  input  [31:0] x,
  input  [3:0] a,
  output [31:0] term
);

  wire [31:0] mul2_res, mul4_res, mul8_res, mul13_res, mul16_res, mul57_res, mul915_res, mul1731_res,
       multiplexer_1_out, multiplexer_2_out, multiplexer_3_out;

  fmult mul2 (.b(x), .a(x), .res(mul2_res));
  Multiplexer #(.width(32)) multiplexer_1 (.in0(x), .in1(mul13_res), .out(multiplexer_1_out), .sel(a[0]));
  fmult mul13 (.b(mul2_res), .a(x), .res(mul13_res));
  fmult mul4 (.b(mul2_res), .a(mul2_res), .res(mul4_res));
  fmult mul57 (.b(mul4_res), .a(multiplexer_1_out), .res(mul57_res));
  Multiplexer #(.width(32)) multiplexer_2 (
    .in0(multiplexer_1_out), .in1(mul57_res), .out(multiplexer_2_out), .sel(a[1]));
  fmult mul8 (.b(mul4_res), .a(mul4_res), .res(mul8_res));
  fmult mul16 (.b(mul8_res), .a(mul8_res), .res(mul16_res));
  fmult mul915 (.b(mul8_res), .a(multiplexer_2_out), .res(mul915_res));
  Multiplexer #(.width(32)) multiplexer_3 (
    .in0(multiplexer_2_out), .in1(mul915_res), .out(multiplexer_3_out), .sel(a[2]));
  Multiplexer #(.width(32)) multiplexer_4 (.in0(multiplexer_3_out), .in1(mul1731_res), .out(term), .sel(a[3]));
  fmult mul1731 (.b(mul16_res), .a(multiplexer_3_out), .res(mul1731_res));
endmodule

module floatTOdec (
  input  [31:0] float,
  output [3:0] dec
);

  wire comparator_1_eq, comparator_2_eq, comparator_3_eq, comparator_4_eq, comparator_5_eq, comparator_6_eq,
       comparator_7_eq, comparator_8_eq, comparator_9_eq, comparator_10_eq, comparator_11_eq,
       comparator_12_eq, comparator_13_eq, comparator_14_eq, comparator_15_eq;
  wire [3:0] multiplexer_1_out, multiplexer_2_out, multiplexer_3_out, multiplexer_4_out, multiplexer_5_out,
       multiplexer_6_out, multiplexer_7_out, multiplexer_8_out, multiplexer_9_out, multiplexer_10_out,
       multiplexer_11_out, multiplexer_12_out, multiplexer_13_out, multiplexer_14_out;

  Comparator #(.width(32)) comparator_1 (.a(float), .b(32'h3f800000), .eq(comparator_1_eq));  // open: gt, lt
  Comparator #(.width(32)) comparator_2 (.a(float), .b(32'h40000000), .eq(comparator_2_eq));  // open: gt, lt
  Comparator #(.width(32)) comparator_3 (.a(float), .b(32'h40400000), .eq(comparator_3_eq));  // open: gt, lt
  Comparator #(.width(32)) comparator_4 (.a(float), .b(32'h40800000), .eq(comparator_4_eq));  // open: gt, lt
  Comparator #(.width(32)) comparator_5 (.a(float), .b(32'h40a00000), .eq(comparator_5_eq));  // open: gt, lt
  Comparator #(.width(32)) comparator_6 (.a(float), .b(32'h40c00000), .eq(comparator_6_eq));  // open: gt, lt
  Comparator #(.width(32)) comparator_7 (.a(float), .b(32'h40e00000), .eq(comparator_7_eq));  // open: gt, lt
  Comparator #(.width(32)) comparator_8 (.a(float), .b(32'h41000000), .eq(comparator_8_eq));  // open: gt, lt
  Comparator #(.width(32)) comparator_9 (.a(float), .b(32'h41100000), .eq(comparator_9_eq));  // open: gt, lt
  Comparator #(.width(32)) comparator_10 (.a(float), .b(32'h41200000), .eq(comparator_10_eq));  // open: gt, lt
  Comparator #(.width(32)) comparator_11 (.a(float), .b(32'h41300000), .eq(comparator_11_eq));  // open: gt, lt
  Comparator #(.width(32)) comparator_12 (.a(float), .b(32'h41400000), .eq(comparator_12_eq));  // open: gt, lt
  Comparator #(.width(32)) comparator_13 (.a(float), .b(32'h41500000), .eq(comparator_13_eq));  // open: gt, lt
  Comparator #(.width(32)) comparator_14 (.a(float), .b(32'h41600000), .eq(comparator_14_eq));  // open: gt, lt
  Comparator #(.width(32)) comparator_15 (.a(float), .b(32'h41700000), .eq(comparator_15_eq));  // open: gt, lt
  Multiplexer #(.width(4)) multiplexer_1 (.in0(4'b1111), .in1(4'b0000), .out(multiplexer_1_out), .sel(comparator_1_eq));
  Multiplexer #(.width(4)) multiplexer_2 (
    .in0(multiplexer_1_out), .in1(4'b0001), .out(multiplexer_2_out), .sel(comparator_2_eq));
  Multiplexer #(.width(4)) multiplexer_3 (
    .in0(multiplexer_2_out), .in1(4'b0010), .out(multiplexer_3_out), .sel(comparator_3_eq));
  Multiplexer #(.width(4)) multiplexer_4 (
    .in0(multiplexer_3_out), .in1(4'b0011), .out(multiplexer_4_out), .sel(comparator_4_eq));
  Multiplexer #(.width(4)) multiplexer_5 (
    .in0(multiplexer_4_out), .in1(4'b0100), .out(multiplexer_5_out), .sel(comparator_5_eq));
  Multiplexer #(.width(4)) multiplexer_6 (
    .in0(multiplexer_5_out), .in1(4'b0101), .out(multiplexer_6_out), .sel(comparator_6_eq));
  Multiplexer #(.width(4)) multiplexer_7 (
    .in0(multiplexer_6_out), .in1(4'b0110), .out(multiplexer_7_out), .sel(comparator_7_eq));
  Multiplexer #(.width(4)) multiplexer_8 (
    .in0(multiplexer_7_out), .in1(4'b0111), .out(multiplexer_8_out), .sel(comparator_8_eq));
  Multiplexer #(.width(4)) multiplexer_9 (
    .in0(multiplexer_8_out), .in1(4'b1000), .out(multiplexer_9_out), .sel(comparator_9_eq));
  Multiplexer #(.width(4)) multiplexer_10 (
    .in0(multiplexer_9_out), .in1(4'b1001), .out(multiplexer_10_out), .sel(comparator_10_eq));
  Multiplexer #(.width(4)) multiplexer_11 (
    .in0(multiplexer_10_out), .in1(4'b1010), .out(multiplexer_11_out), .sel(comparator_11_eq));
  Multiplexer #(.width(4)) multiplexer_12 (
    .in0(multiplexer_11_out), .in1(4'b1011), .out(multiplexer_12_out), .sel(comparator_12_eq));
  Multiplexer #(.width(4)) multiplexer_13 (
    .in0(multiplexer_12_out), .in1(4'b1100), .out(multiplexer_13_out), .sel(comparator_13_eq));
  Multiplexer #(.width(4)) multiplexer_14 (
    .in0(multiplexer_13_out), .in1(4'b1101), .out(multiplexer_14_out), .sel(comparator_14_eq));
  Multiplexer #(.width(4)) multiplexer_15 (.in0(multiplexer_14_out), .in1(4'b1110), .out(dec), .sel(comparator_15_eq));

  // Other names for the same wires on the sheet: b[31:0] = float
endmodule
